// Logisim project tetris-16-bit.circ as structural Verilog: 17 circuits, main circuit Computer
module Computer (
);

  wire and_1_out, C_out, CLK, clock_1_out, cpu_1_break, cpu_1_write, not_1_out, RESET;
  wire [15:0] cpu_1_addressm, cpu_1_counter, cpu_1_outm, display_control_1_out_7, display_control_1_out_8,
       display_control_1_out_9, display_control_1_out_10, display_control_1_out_11, display_control_1_out_12,
       display_control_1_out_13, display_control_1_out_14, display_control_1_out_15,
       display_control_1_out_16, display_control_1_out_17, display_control_1_out_18,
       display_control_1_out_19, display_control_1_out_20, display_control_1_out_21,
       display_control_1_out_22, display_control_1_out_23, display_control_1_out_24,
       display_control_1_out_25, display_control_1_out_26, display_control_1_out_27,
       display_control_1_out_28, display_control_1_out_29, display_control_1_out_30,
       display_control_1_out_31, display_control_1_out_32, display_control_1_out_33,
       display_control_1_out_34, display_control_1_out_35, display_control_1_out_36,
       display_control_1_out_37, display_control_1_out_38, display_control_1_out_39,
       display_control_1_out_40, display_control_1_out_41, display_control_1_out_42,
       display_control_1_out_43, display_control_1_out_44, display_control_1_out_45,
       display_control_1_out_46, display_control_1_out_47, display_control_1_out_48,
       display_control_1_out_49, display_control_1_out_50, display_control_1_out_51,
       display_control_1_out_52, display_control_1_out_53, display_control_1_out_54,
       display_control_1_out_55, display_control_1_out_56, display_control_1_out_57,
       display_control_1_out_58, display_control_1_out_59, display_control_1_out_60,
       display_control_1_out_61, display_control_1_out_62, display_control_1_out_63,
       display_control_1_out_64, display_control_1_out_65, display_control_1_out_66,
       display_control_1_out_67, display_control_1_out_68, display_control_1_out_69,
       display_control_1_out_70, display_control_1_out_71, display_control_1_out_72,
       display_control_1_out_73, display_control_1_out_74, display_control_1_out_75,
       display_control_1_out_76, display_control_1_out_77, display_control_1_out_78,
       display_control_1_out_79, display_control_1_out_80, display_control_1_out_81,
       display_control_1_out_82, display_control_1_out_83, display_control_1_out_84,
       display_control_1_out_85, display_control_1_out_86, display_control_1_out_87,
       display_control_1_out_88, display_control_1_out_89, display_control_1_out_90,
       display_control_1_out_91, display_control_1_out_92, display_control_1_out_93,
       display_control_1_out_94, display_control_1_out_95, display_control_1_out_96,
       display_control_1_out_97, display_control_1_out_98, display_control_1_out_99,
       display_control_1_out_100, display_control_1_out_101, display_control_1_out_102,
       display_control_1_out_103, display_control_1_out_104, display_control_1_out_105,
       display_control_1_out_106, display_control_1_out_107, display_control_1_out_108,
       display_control_1_out_109, display_control_1_out_110, display_control_1_out_111,
       display_control_1_out_112, display_control_1_out_113, display_control_1_out_114,
       display_control_1_out_115, display_control_1_out_116, display_control_1_out_117,
       display_control_1_out_118, display_control_1_out_119, display_control_1_out_120,
       display_control_1_out_121, display_control_1_out_122, display_control_1_out_123,
       display_control_1_out_124, display_control_1_out_125, display_control_1_out_126,
       display_control_1_out_127, display_control_1_out_128, display_control_1_out_129,
       display_control_1_out_130, display_control_1_out_131, display_control_1_out_132,
       display_control_1_out_133, display_control_1_out_134, display_control_1_out_135,
       display_control_1_out_136, display_control_1_out_137, display_control_1_out_138,
       display_control_1_out_139, display_control_1_out_140, display_control_1_out_141,
       display_control_1_out_142, display_control_1_out_143, display_control_1_out_144,
       display_control_1_out_145, display_control_1_out_146, display_control_1_out_147,
       display_control_1_out_148, display_control_1_out_149, display_control_1_out_150,
       display_control_1_out_151, display_control_1_out_152, display_control_1_out_153,
       display_control_1_out_154, display_control_1_out_155, display_control_1_out_156,
       display_control_1_out_157, display_control_1_out_158, display_control_1_out_159,
       display_control_1_out_160, display_control_1_out_161, display_control_1_out_162,
       display_control_1_out_163, display_control_1_out_164, display_control_1_out_165,
       display_control_1_out_166, display_control_1_out_167, display_control_1_out_168,
       display_control_1_out_169, display_control_1_out_170, display_control_1_out_171,
       display_control_1_out_172, display_control_1_out_173, display_control_1_out_174,
       display_control_1_out_175, display_control_1_out_176, display_control_1_out_177,
       display_control_1_out_178, display_control_1_out_179, display_control_1_out_180,
       display_control_1_out_181, display_control_1_out_182, display_control_1_out_183,
       display_control_1_out_184, display_control_1_out_185, display_control_1_out_186,
       display_control_1_out_187, display_control_1_out_188, display_control_1_out_189,
       display_control_1_out_190, display_control_1_out_191, display_control_1_out_192,
       display_control_1_out_193, display_control_1_out_194, display_control_1_out_195,
       display_control_1_out_196, display_control_1_out_197, display_control_1_out_198,
       display_control_1_out_199, display_control_1_out_200, display_control_1_out_201,
       display_control_1_out_202, display_control_1_out_203, display_control_1_out_204,
       display_control_1_out_205, display_control_1_out_206, display_control_1_out_207,
       display_control_1_out_208, display_control_1_out_209, display_control_1_out_210,
       display_control_1_out_211, display_control_1_out_212, display_control_1_out_213,
       display_control_1_out_214, display_control_1_out_215, display_control_1_out_216,
       display_control_1_out_217, display_control_1_out_218, display_control_1_out_219,
       display_control_1_out_220, display_control_1_out_221, display_control_1_out_222,
       display_control_1_out_223, display_control_1_out_224, display_control_1_out_225,
       display_control_1_out_226, display_control_1_out_227, display_control_1_out_228,
       display_control_1_out_229, display_control_1_out_230, display_control_1_out_231,
       display_control_1_out_232, display_control_1_out_233, display_control_1_out_234,
       display_control_1_out_235, display_control_1_out_236, display_control_1_out_237,
       display_control_1_out_238, display_control_1_out_239, display_control_1_out_240,
       display_control_1_out_241, display_control_1_out_242, display_control_1_out_243,
       display_control_1_out_244, display_control_1_out_245, display_control_1_out_246,
       display_control_1_out_247, display_control_1_out_248, display_control_1_out_249,
       display_control_1_out_250, display_control_1_out_251, display_control_1_out_252,
       display_control_1_out_253, display_control_1_out_254, display_control_1_out_255,
       display_control_1_out_256, display_control_1_out_257, display_control_1_out_258,
       display_control_1_out_259, display_control_1_out_260, display_control_1_out_261,
       display_control_1_out_262, display_control_1_out_263, display_control_1_out_264,
       display_control_1_out_265, display_control_1_out_266, display_control_1_out_267,
       display_control_1_out_268, display_control_1_out_269, display_control_1_out_270,
       display_control_1_out_271, display_control_1_out_272, display_control_1_out_273,
       display_control_1_out_274, display_control_1_out_275, display_control_1_out_276,
       display_control_1_out_277, display_control_1_out_278, display_control_1_out_279,
       display_control_1_out_280, display_control_1_out_281, display_control_1_out_282,
       display_control_1_out_283, display_control_1_out_284, display_control_1_out_285,
       display_control_1_out_286, display_control_1_out_287, display_control_1_out_288,
       display_control_1_out_289, display_control_1_out_290, display_control_1_out_291,
       display_control_1_out_292, display_control_1_out_293, display_control_1_out_294,
       display_control_1_out_295, display_control_1_out_296, display_control_1_out_297,
       display_control_1_out_298, display_control_1_out_299, display_control_1_out_300,
       display_control_1_out_301, display_control_1_out_302, display_control_1_out_303,
       display_control_1_out_304, display_control_1_out_305, display_control_1_out_306,
       display_control_1_out_307, display_control_1_out_308, display_control_1_out_309,
       display_control_1_out_310, display_control_1_out_311, display_control_1_out_312,
       display_control_1_out_313, display_control_1_out_314, display_control_1_out_315,
       display_control_1_out_316, display_control_1_out_317, display_control_1_out_318,
       display_control_1_out_319, display_control_1_out_320, display_control_1_out_321,
       display_control_1_out_322, display_control_1_out_323, display_control_1_out_324,
       display_control_1_out_325, display_control_1_out_326, display_control_1_out_327,
       display_control_1_out_328, display_control_1_out_329, display_control_1_out_330,
       display_control_1_out_331, display_control_1_out_332, display_control_1_out_333,
       display_control_1_out_334, display_control_1_out_335, display_control_1_out_336,
       display_control_1_out_337, display_control_1_out_338, display_control_1_out_339,
       display_control_1_out_340, display_control_1_out_341, display_control_1_out_342,
       display_control_1_out_343, display_control_1_out_344, display_control_1_out_345,
       display_control_1_out_346, display_control_1_out_347, display_control_1_out_348,
       display_control_1_out_349, display_control_1_out_350, display_control_1_out_351,
       display_control_1_out_352, display_control_1_out_353, display_control_1_out_354,
       display_control_1_out_355, display_control_1_out_356, display_control_1_out_357,
       display_control_1_out_358, display_control_1_out_359, display_control_1_out_360,
       display_control_1_out_361, display_control_1_out_362, display_control_1_out_363,
       display_control_1_out_364, display_control_1_out_365, display_control_1_out_366,
       display_control_1_out_367, display_control_1_out_368, display_control_1_out_369,
       display_control_1_out_370, display_control_1_out_371, display_control_1_out_372,
       display_control_1_out_373, display_control_1_out_374, display_control_1_out_375,
       display_control_1_out_376, display_control_1_out_377, display_control_1_out_378,
       display_control_1_out_379, display_control_1_out_380, display_control_1_out_381,
       display_control_1_out_382, display_control_1_out_383, display_control_1_out_384,
       display_control_1_out_385, display_control_1_out_386, display_control_1_out_387,
       display_control_1_out_388, display_control_1_out_389, display_control_1_out_390,
       display_control_1_out_391, display_control_1_out_392, display_control_1_out_393,
       display_control_1_out_394, display_control_1_out_395, display_control_1_out_396,
       display_control_1_out_397, display_control_1_out_398, display_control_1_out_399,
       display_control_1_out_400, display_control_1_out_401, display_control_1_out_402,
       display_control_1_out_403, display_control_1_out_404, display_control_1_out_405,
       display_control_1_out_406, display_control_1_out_407, display_control_1_out_408,
       display_control_1_out_409, display_control_1_out_410, display_control_1_out_411,
       display_control_1_out_412, display_control_1_out_413, display_control_1_out_414,
       display_control_1_out_415, display_control_1_out_416, display_control_1_out_417,
       display_control_1_out_418, display_control_1_out_419, display_control_1_out_420,
       display_control_1_out_421, display_control_1_out_422, display_control_1_out_423,
       display_control_1_out_424, display_control_1_out_425, display_control_1_out_426,
       display_control_1_out_427, display_control_1_out_428, display_control_1_out_429,
       display_control_1_out_430, display_control_1_out_431, display_control_1_out_432,
       display_control_1_out_433, display_control_1_out_434, display_control_1_out_435,
       display_control_1_out_436, display_control_1_out_437, display_control_1_out_438,
       display_control_1_out_439, display_control_1_out_440, display_control_1_out_441,
       display_control_1_out_442, display_control_1_out_443, display_control_1_out_444,
       display_control_1_out_445, display_control_1_out_446, display_control_1_out_447,
       display_control_1_out_448, display_control_1_out_449, display_control_1_out_450,
       display_control_1_out_451, display_control_1_out_452, display_control_1_out_453,
       display_control_1_out_454, display_control_1_out_455, display_control_1_out_456,
       display_control_1_out_457, display_control_1_out_458, display_control_1_out_459,
       display_control_1_out_460, display_control_1_out_461, display_control_1_out_462,
       display_control_1_out_463, display_control_1_out_464, display_control_1_out_465,
       display_control_1_out_466, display_control_1_out_467, display_control_1_out_468,
       display_control_1_out_469, display_control_1_out_470, display_control_1_out_471,
       display_control_1_out_472, display_control_1_out_473, display_control_1_out_474,
       display_control_1_out_475, display_control_1_out_476, display_control_1_out_477,
       display_control_1_out_478, display_control_1_out_479, display_control_1_out_480,
       display_control_1_out_481, display_control_1_out_482, display_control_1_out_483,
       display_control_1_out_484, display_control_1_out_485, display_control_1_out_486,
       display_control_1_out_487, display_control_1_out_488, display_control_1_out_489,
       display_control_1_out_490, display_control_1_out_491, display_control_1_out_492,
       display_control_1_out_493, display_control_1_out_494, display_control_1_out_495,
       display_control_1_out_496, display_control_1_out_497, display_control_1_out_498,
       display_control_1_out_499, display_control_1_out_500, display_control_1_out_501,
       display_control_1_out_502, display_control_1_out_503, display_control_1_out_504,
       display_control_1_out_505, display_control_1_out_506, display_control_1_out_507,
       display_control_1_out_508, display_control_1_out_509, display_control_1_out_510,
       display_control_1_out_511, display_control_1_out_512, display_control_1_out_513,
       display_control_1_out_514, display_control_1_out_515, display_control_1_out_516,
       display_control_1_out_517, display_control_1_out_518, ram_1_data, rom_1_data;
  wire [31:0] counter_1_q;

  Clock clock_1 (.out(clock_1_out));
  Button R (.out(RESET));
  Display_Control display_control_1 (
    .Address(cpu_1_addressm), .Data(cpu_1_outm), .Write(cpu_1_write), .CLK(CLK), .RESET(RESET),
    .out_7(display_control_1_out_7), .out_15(display_control_1_out_15), .out_23(display_control_1_out_23),
    .out_31(display_control_1_out_31), .out_39(display_control_1_out_39), .out_47(display_control_1_out_47),
    .out_55(display_control_1_out_55), .out_63(display_control_1_out_63), .out_71(display_control_1_out_71),
    .out_79(display_control_1_out_79), .out_87(display_control_1_out_87), .out_95(display_control_1_out_95),
    .out_103(display_control_1_out_103), .out_111(display_control_1_out_111),
    .out_119(display_control_1_out_119), .out_127(display_control_1_out_127),
    .out_135(display_control_1_out_135), .out_143(display_control_1_out_143),
    .out_151(display_control_1_out_151), .out_159(display_control_1_out_159),
    .out_167(display_control_1_out_167), .out_175(display_control_1_out_175),
    .out_183(display_control_1_out_183), .out_191(display_control_1_out_191),
    .out_199(display_control_1_out_199), .out_207(display_control_1_out_207),
    .out_215(display_control_1_out_215), .out_223(display_control_1_out_223),
    .out_231(display_control_1_out_231), .out_239(display_control_1_out_239),
    .out_247(display_control_1_out_247), .out_255(display_control_1_out_255),
    .out_263(display_control_1_out_263), .out_271(display_control_1_out_271),
    .out_279(display_control_1_out_279), .out_287(display_control_1_out_287),
    .out_295(display_control_1_out_295), .out_303(display_control_1_out_303),
    .out_311(display_control_1_out_311), .out_319(display_control_1_out_319),
    .out_327(display_control_1_out_327), .out_335(display_control_1_out_335),
    .out_343(display_control_1_out_343), .out_351(display_control_1_out_351),
    .out_359(display_control_1_out_359), .out_367(display_control_1_out_367),
    .out_375(display_control_1_out_375), .out_383(display_control_1_out_383),
    .out_391(display_control_1_out_391), .out_399(display_control_1_out_399),
    .out_407(display_control_1_out_407), .out_415(display_control_1_out_415),
    .out_423(display_control_1_out_423), .out_431(display_control_1_out_431),
    .out_439(display_control_1_out_439), .out_447(display_control_1_out_447),
    .out_455(display_control_1_out_455), .out_463(display_control_1_out_463),
    .out_471(display_control_1_out_471), .out_479(display_control_1_out_479),
    .out_487(display_control_1_out_487), .out_495(display_control_1_out_495),
    .out_503(display_control_1_out_503), .out_511(display_control_1_out_511),
    .out_8(display_control_1_out_8), .out_16(display_control_1_out_16), .out_24(display_control_1_out_24),
    .out_32(display_control_1_out_32), .out_40(display_control_1_out_40), .out_48(display_control_1_out_48),
    .out_56(display_control_1_out_56), .out_64(display_control_1_out_64), .out_72(display_control_1_out_72),
    .out_80(display_control_1_out_80), .out_88(display_control_1_out_88), .out_96(display_control_1_out_96),
    .out_104(display_control_1_out_104), .out_112(display_control_1_out_112),
    .out_120(display_control_1_out_120), .out_128(display_control_1_out_128),
    .out_136(display_control_1_out_136), .out_144(display_control_1_out_144),
    .out_152(display_control_1_out_152), .out_160(display_control_1_out_160),
    .out_168(display_control_1_out_168), .out_176(display_control_1_out_176),
    .out_184(display_control_1_out_184), .out_192(display_control_1_out_192),
    .out_200(display_control_1_out_200), .out_208(display_control_1_out_208),
    .out_216(display_control_1_out_216), .out_224(display_control_1_out_224),
    .out_232(display_control_1_out_232), .out_240(display_control_1_out_240),
    .out_248(display_control_1_out_248), .out_256(display_control_1_out_256),
    .out_264(display_control_1_out_264), .out_272(display_control_1_out_272),
    .out_280(display_control_1_out_280), .out_288(display_control_1_out_288),
    .out_296(display_control_1_out_296), .out_304(display_control_1_out_304),
    .out_312(display_control_1_out_312), .out_320(display_control_1_out_320),
    .out_328(display_control_1_out_328), .out_336(display_control_1_out_336),
    .out_344(display_control_1_out_344), .out_352(display_control_1_out_352),
    .out_360(display_control_1_out_360), .out_368(display_control_1_out_368),
    .out_376(display_control_1_out_376), .out_384(display_control_1_out_384),
    .out_392(display_control_1_out_392), .out_400(display_control_1_out_400),
    .out_408(display_control_1_out_408), .out_416(display_control_1_out_416),
    .out_424(display_control_1_out_424), .out_432(display_control_1_out_432),
    .out_440(display_control_1_out_440), .out_448(display_control_1_out_448),
    .out_456(display_control_1_out_456), .out_464(display_control_1_out_464),
    .out_472(display_control_1_out_472), .out_480(display_control_1_out_480),
    .out_488(display_control_1_out_488), .out_496(display_control_1_out_496),
    .out_504(display_control_1_out_504), .out_512(display_control_1_out_512),
    .out_9(display_control_1_out_9), .out_17(display_control_1_out_17), .out_25(display_control_1_out_25),
    .out_33(display_control_1_out_33), .out_41(display_control_1_out_41), .out_49(display_control_1_out_49),
    .out_57(display_control_1_out_57), .out_65(display_control_1_out_65), .out_73(display_control_1_out_73),
    .out_81(display_control_1_out_81), .out_89(display_control_1_out_89), .out_97(display_control_1_out_97),
    .out_105(display_control_1_out_105), .out_113(display_control_1_out_113),
    .out_121(display_control_1_out_121), .out_129(display_control_1_out_129),
    .out_137(display_control_1_out_137), .out_145(display_control_1_out_145),
    .out_153(display_control_1_out_153), .out_161(display_control_1_out_161),
    .out_169(display_control_1_out_169), .out_177(display_control_1_out_177),
    .out_185(display_control_1_out_185), .out_193(display_control_1_out_193),
    .out_201(display_control_1_out_201), .out_209(display_control_1_out_209),
    .out_217(display_control_1_out_217), .out_225(display_control_1_out_225),
    .out_233(display_control_1_out_233), .out_241(display_control_1_out_241),
    .out_249(display_control_1_out_249), .out_257(display_control_1_out_257),
    .out_265(display_control_1_out_265), .out_273(display_control_1_out_273),
    .out_281(display_control_1_out_281), .out_289(display_control_1_out_289),
    .out_297(display_control_1_out_297), .out_305(display_control_1_out_305),
    .out_313(display_control_1_out_313), .out_321(display_control_1_out_321),
    .out_329(display_control_1_out_329), .out_337(display_control_1_out_337),
    .out_345(display_control_1_out_345), .out_353(display_control_1_out_353),
    .out_361(display_control_1_out_361), .out_369(display_control_1_out_369),
    .out_377(display_control_1_out_377), .out_385(display_control_1_out_385),
    .out_393(display_control_1_out_393), .out_401(display_control_1_out_401),
    .out_409(display_control_1_out_409), .out_417(display_control_1_out_417),
    .out_425(display_control_1_out_425), .out_433(display_control_1_out_433),
    .out_441(display_control_1_out_441), .out_449(display_control_1_out_449),
    .out_457(display_control_1_out_457), .out_465(display_control_1_out_465),
    .out_473(display_control_1_out_473), .out_481(display_control_1_out_481),
    .out_489(display_control_1_out_489), .out_497(display_control_1_out_497),
    .out_505(display_control_1_out_505), .out_513(display_control_1_out_513),
    .out_10(display_control_1_out_10), .out_18(display_control_1_out_18), .out_26(display_control_1_out_26),
    .out_34(display_control_1_out_34), .out_42(display_control_1_out_42), .out_50(display_control_1_out_50),
    .out_58(display_control_1_out_58), .out_66(display_control_1_out_66), .out_74(display_control_1_out_74),
    .out_82(display_control_1_out_82), .out_90(display_control_1_out_90), .out_98(display_control_1_out_98),
    .out_106(display_control_1_out_106), .out_114(display_control_1_out_114),
    .out_122(display_control_1_out_122), .out_130(display_control_1_out_130),
    .out_138(display_control_1_out_138), .out_146(display_control_1_out_146),
    .out_154(display_control_1_out_154), .out_162(display_control_1_out_162),
    .out_170(display_control_1_out_170), .out_178(display_control_1_out_178),
    .out_186(display_control_1_out_186), .out_194(display_control_1_out_194),
    .out_202(display_control_1_out_202), .out_210(display_control_1_out_210),
    .out_218(display_control_1_out_218), .out_226(display_control_1_out_226),
    .out_234(display_control_1_out_234), .out_242(display_control_1_out_242),
    .out_250(display_control_1_out_250), .out_258(display_control_1_out_258),
    .out_266(display_control_1_out_266), .out_274(display_control_1_out_274),
    .out_282(display_control_1_out_282), .out_290(display_control_1_out_290),
    .out_298(display_control_1_out_298), .out_306(display_control_1_out_306),
    .out_314(display_control_1_out_314), .out_322(display_control_1_out_322),
    .out_330(display_control_1_out_330), .out_338(display_control_1_out_338),
    .out_346(display_control_1_out_346), .out_354(display_control_1_out_354),
    .out_362(display_control_1_out_362), .out_370(display_control_1_out_370),
    .out_378(display_control_1_out_378), .out_386(display_control_1_out_386),
    .out_394(display_control_1_out_394), .out_402(display_control_1_out_402),
    .out_410(display_control_1_out_410), .out_418(display_control_1_out_418),
    .out_426(display_control_1_out_426), .out_434(display_control_1_out_434),
    .out_442(display_control_1_out_442), .out_450(display_control_1_out_450),
    .out_458(display_control_1_out_458), .out_466(display_control_1_out_466),
    .out_474(display_control_1_out_474), .out_482(display_control_1_out_482),
    .out_490(display_control_1_out_490), .out_498(display_control_1_out_498),
    .out_506(display_control_1_out_506), .out_514(display_control_1_out_514),
    .out_11(display_control_1_out_11), .out_19(display_control_1_out_19), .out_27(display_control_1_out_27),
    .out_35(display_control_1_out_35), .out_43(display_control_1_out_43), .out_51(display_control_1_out_51),
    .out_59(display_control_1_out_59), .out_67(display_control_1_out_67), .out_75(display_control_1_out_75),
    .out_83(display_control_1_out_83), .out_91(display_control_1_out_91), .out_99(display_control_1_out_99),
    .out_107(display_control_1_out_107), .out_115(display_control_1_out_115),
    .out_123(display_control_1_out_123), .out_131(display_control_1_out_131),
    .out_139(display_control_1_out_139), .out_147(display_control_1_out_147),
    .out_155(display_control_1_out_155), .out_163(display_control_1_out_163),
    .out_171(display_control_1_out_171), .out_179(display_control_1_out_179),
    .out_187(display_control_1_out_187), .out_195(display_control_1_out_195),
    .out_203(display_control_1_out_203), .out_211(display_control_1_out_211),
    .out_219(display_control_1_out_219), .out_227(display_control_1_out_227),
    .out_235(display_control_1_out_235), .out_243(display_control_1_out_243),
    .out_251(display_control_1_out_251), .out_259(display_control_1_out_259),
    .out_267(display_control_1_out_267), .out_275(display_control_1_out_275),
    .out_283(display_control_1_out_283), .out_291(display_control_1_out_291),
    .out_299(display_control_1_out_299), .out_307(display_control_1_out_307),
    .out_315(display_control_1_out_315), .out_323(display_control_1_out_323),
    .out_331(display_control_1_out_331), .out_339(display_control_1_out_339),
    .out_347(display_control_1_out_347), .out_355(display_control_1_out_355),
    .out_363(display_control_1_out_363), .out_371(display_control_1_out_371),
    .out_379(display_control_1_out_379), .out_387(display_control_1_out_387),
    .out_395(display_control_1_out_395), .out_403(display_control_1_out_403),
    .out_411(display_control_1_out_411), .out_419(display_control_1_out_419),
    .out_427(display_control_1_out_427), .out_435(display_control_1_out_435),
    .out_443(display_control_1_out_443), .out_451(display_control_1_out_451),
    .out_459(display_control_1_out_459), .out_467(display_control_1_out_467),
    .out_475(display_control_1_out_475), .out_483(display_control_1_out_483),
    .out_491(display_control_1_out_491), .out_499(display_control_1_out_499),
    .out_507(display_control_1_out_507), .out_515(display_control_1_out_515),
    .out_12(display_control_1_out_12), .out_20(display_control_1_out_20), .out_28(display_control_1_out_28),
    .out_36(display_control_1_out_36), .out_44(display_control_1_out_44), .out_52(display_control_1_out_52),
    .out_60(display_control_1_out_60), .out_68(display_control_1_out_68), .out_76(display_control_1_out_76),
    .out_84(display_control_1_out_84), .out_92(display_control_1_out_92),
    .out_100(display_control_1_out_100), .out_108(display_control_1_out_108),
    .out_116(display_control_1_out_116), .out_124(display_control_1_out_124),
    .out_132(display_control_1_out_132), .out_140(display_control_1_out_140),
    .out_148(display_control_1_out_148), .out_156(display_control_1_out_156),
    .out_164(display_control_1_out_164), .out_172(display_control_1_out_172),
    .out_180(display_control_1_out_180), .out_188(display_control_1_out_188),
    .out_196(display_control_1_out_196), .out_204(display_control_1_out_204),
    .out_212(display_control_1_out_212), .out_220(display_control_1_out_220),
    .out_228(display_control_1_out_228), .out_236(display_control_1_out_236),
    .out_244(display_control_1_out_244), .out_252(display_control_1_out_252),
    .out_260(display_control_1_out_260), .out_268(display_control_1_out_268),
    .out_276(display_control_1_out_276), .out_284(display_control_1_out_284),
    .out_292(display_control_1_out_292), .out_300(display_control_1_out_300),
    .out_308(display_control_1_out_308), .out_316(display_control_1_out_316),
    .out_324(display_control_1_out_324), .out_332(display_control_1_out_332),
    .out_340(display_control_1_out_340), .out_348(display_control_1_out_348),
    .out_356(display_control_1_out_356), .out_364(display_control_1_out_364),
    .out_372(display_control_1_out_372), .out_380(display_control_1_out_380),
    .out_388(display_control_1_out_388), .out_396(display_control_1_out_396),
    .out_404(display_control_1_out_404), .out_412(display_control_1_out_412),
    .out_420(display_control_1_out_420), .out_428(display_control_1_out_428),
    .out_436(display_control_1_out_436), .out_444(display_control_1_out_444),
    .out_452(display_control_1_out_452), .out_460(display_control_1_out_460),
    .out_468(display_control_1_out_468), .out_476(display_control_1_out_476),
    .out_484(display_control_1_out_484), .out_492(display_control_1_out_492),
    .out_500(display_control_1_out_500), .out_508(display_control_1_out_508),
    .out_516(display_control_1_out_516), .out_13(display_control_1_out_13),
    .out_21(display_control_1_out_21), .out_29(display_control_1_out_29), .out_37(display_control_1_out_37),
    .out_45(display_control_1_out_45), .out_53(display_control_1_out_53), .out_61(display_control_1_out_61),
    .out_69(display_control_1_out_69), .out_77(display_control_1_out_77), .out_85(display_control_1_out_85),
    .out_93(display_control_1_out_93), .out_101(display_control_1_out_101),
    .out_109(display_control_1_out_109), .out_117(display_control_1_out_117),
    .out_125(display_control_1_out_125), .out_133(display_control_1_out_133),
    .out_141(display_control_1_out_141), .out_149(display_control_1_out_149),
    .out_157(display_control_1_out_157), .out_165(display_control_1_out_165),
    .out_173(display_control_1_out_173), .out_181(display_control_1_out_181),
    .out_189(display_control_1_out_189), .out_197(display_control_1_out_197),
    .out_205(display_control_1_out_205), .out_213(display_control_1_out_213),
    .out_221(display_control_1_out_221), .out_229(display_control_1_out_229),
    .out_237(display_control_1_out_237), .out_245(display_control_1_out_245),
    .out_253(display_control_1_out_253), .out_261(display_control_1_out_261),
    .out_269(display_control_1_out_269), .out_277(display_control_1_out_277),
    .out_285(display_control_1_out_285), .out_293(display_control_1_out_293),
    .out_301(display_control_1_out_301), .out_309(display_control_1_out_309),
    .out_317(display_control_1_out_317), .out_325(display_control_1_out_325),
    .out_333(display_control_1_out_333), .out_341(display_control_1_out_341),
    .out_349(display_control_1_out_349), .out_357(display_control_1_out_357),
    .out_365(display_control_1_out_365), .out_373(display_control_1_out_373),
    .out_381(display_control_1_out_381), .out_389(display_control_1_out_389),
    .out_397(display_control_1_out_397), .out_405(display_control_1_out_405),
    .out_413(display_control_1_out_413), .out_421(display_control_1_out_421),
    .out_429(display_control_1_out_429), .out_437(display_control_1_out_437),
    .out_445(display_control_1_out_445), .out_453(display_control_1_out_453),
    .out_461(display_control_1_out_461), .out_469(display_control_1_out_469),
    .out_477(display_control_1_out_477), .out_485(display_control_1_out_485),
    .out_493(display_control_1_out_493), .out_501(display_control_1_out_501),
    .out_509(display_control_1_out_509), .out_517(display_control_1_out_517),
    .out_14(display_control_1_out_14), .out_22(display_control_1_out_22), .out_30(display_control_1_out_30),
    .out_38(display_control_1_out_38), .out_46(display_control_1_out_46), .out_54(display_control_1_out_54),
    .out_62(display_control_1_out_62), .out_70(display_control_1_out_70), .out_78(display_control_1_out_78),
    .out_86(display_control_1_out_86), .out_94(display_control_1_out_94),
    .out_102(display_control_1_out_102), .out_110(display_control_1_out_110),
    .out_118(display_control_1_out_118), .out_126(display_control_1_out_126),
    .out_134(display_control_1_out_134), .out_142(display_control_1_out_142),
    .out_150(display_control_1_out_150), .out_158(display_control_1_out_158),
    .out_166(display_control_1_out_166), .out_174(display_control_1_out_174),
    .out_182(display_control_1_out_182), .out_190(display_control_1_out_190),
    .out_198(display_control_1_out_198), .out_206(display_control_1_out_206),
    .out_214(display_control_1_out_214), .out_222(display_control_1_out_222),
    .out_230(display_control_1_out_230), .out_238(display_control_1_out_238),
    .out_246(display_control_1_out_246), .out_254(display_control_1_out_254),
    .out_262(display_control_1_out_262), .out_270(display_control_1_out_270),
    .out_278(display_control_1_out_278), .out_286(display_control_1_out_286),
    .out_294(display_control_1_out_294), .out_302(display_control_1_out_302),
    .out_310(display_control_1_out_310), .out_318(display_control_1_out_318),
    .out_326(display_control_1_out_326), .out_334(display_control_1_out_334),
    .out_342(display_control_1_out_342), .out_350(display_control_1_out_350),
    .out_358(display_control_1_out_358), .out_366(display_control_1_out_366),
    .out_374(display_control_1_out_374), .out_382(display_control_1_out_382),
    .out_390(display_control_1_out_390), .out_398(display_control_1_out_398),
    .out_406(display_control_1_out_406), .out_414(display_control_1_out_414),
    .out_422(display_control_1_out_422), .out_430(display_control_1_out_430),
    .out_438(display_control_1_out_438), .out_446(display_control_1_out_446),
    .out_454(display_control_1_out_454), .out_462(display_control_1_out_462),
    .out_470(display_control_1_out_470), .out_478(display_control_1_out_478),
    .out_486(display_control_1_out_486), .out_494(display_control_1_out_494),
    .out_502(display_control_1_out_502), .out_510(display_control_1_out_510),
    .out_518(display_control_1_out_518), .Screen_Width(16'h20));
  DotMatrix #(.inputtype("row"), .matrixcols(16), .matrixrows(16)) dotmatrix_1 (
    .row0(display_control_1_out_7), .row1(display_control_1_out_15), .row2(display_control_1_out_23),
    .row3(display_control_1_out_31), .row4(display_control_1_out_39), .row5(display_control_1_out_47),
    .row6(display_control_1_out_55), .row7(display_control_1_out_63), .row8(display_control_1_out_71),
    .row9(display_control_1_out_79), .row10(display_control_1_out_87), .row11(display_control_1_out_95),
    .row12(display_control_1_out_103), .row13(display_control_1_out_111), .row14(display_control_1_out_119),
    .row15(display_control_1_out_127));
  DotMatrix #(.inputtype("row"), .matrixcols(16), .matrixrows(16)) dotmatrix_2 (
    .row0(display_control_1_out_135), .row1(display_control_1_out_143), .row2(display_control_1_out_151),
    .row3(display_control_1_out_159), .row4(display_control_1_out_167), .row5(display_control_1_out_175),
    .row6(display_control_1_out_183), .row7(display_control_1_out_191), .row8(display_control_1_out_199),
    .row9(display_control_1_out_207), .row10(display_control_1_out_215), .row11(display_control_1_out_223),
    .row12(display_control_1_out_231), .row13(display_control_1_out_239), .row14(display_control_1_out_247),
    .row15(display_control_1_out_255));
  DotMatrix #(.inputtype("row"), .matrixcols(16), .matrixrows(16)) dotmatrix_3 (
    .row0(display_control_1_out_263), .row1(display_control_1_out_271), .row2(display_control_1_out_279),
    .row3(display_control_1_out_287), .row4(display_control_1_out_295), .row5(display_control_1_out_303),
    .row6(display_control_1_out_311), .row7(display_control_1_out_319), .row8(display_control_1_out_327),
    .row9(display_control_1_out_335), .row10(display_control_1_out_343), .row11(display_control_1_out_351),
    .row12(display_control_1_out_359), .row13(display_control_1_out_367), .row14(display_control_1_out_375),
    .row15(display_control_1_out_383));
  DotMatrix #(.inputtype("row"), .matrixcols(16), .matrixrows(16)) dotmatrix_4 (
    .row0(display_control_1_out_391), .row1(display_control_1_out_399), .row2(display_control_1_out_407),
    .row3(display_control_1_out_415), .row4(display_control_1_out_423), .row5(display_control_1_out_431),
    .row6(display_control_1_out_439), .row7(display_control_1_out_447), .row8(display_control_1_out_455),
    .row9(display_control_1_out_463), .row10(display_control_1_out_471), .row11(display_control_1_out_479),
    .row12(display_control_1_out_487), .row13(display_control_1_out_495), .row14(display_control_1_out_503),
    .row15(display_control_1_out_511));
  // Probe on cpu_1_counter
  Button C (.out(C_out));
  not not_1 (not_1_out, cpu_1_break);
  ROM #(.addrWidth(16), .dataWidth(16)) rom_1 (.addr(cpu_1_counter), .data(rom_1_data));  // open: sel
  DotMatrix #(.inputtype("row"), .matrixcols(16), .matrixrows(16)) dotmatrix_5 (
    .row0(display_control_1_out_8), .row1(display_control_1_out_16), .row2(display_control_1_out_24),
    .row3(display_control_1_out_32), .row4(display_control_1_out_40), .row5(display_control_1_out_48),
    .row6(display_control_1_out_56), .row7(display_control_1_out_64), .row8(display_control_1_out_72),
    .row9(display_control_1_out_80), .row10(display_control_1_out_88), .row11(display_control_1_out_96),
    .row12(display_control_1_out_104), .row13(display_control_1_out_112), .row14(display_control_1_out_120),
    .row15(display_control_1_out_128));
  DotMatrix #(.inputtype("row"), .matrixcols(16), .matrixrows(16)) dotmatrix_6 (
    .row0(display_control_1_out_136), .row1(display_control_1_out_144), .row2(display_control_1_out_152),
    .row3(display_control_1_out_160), .row4(display_control_1_out_168), .row5(display_control_1_out_176),
    .row6(display_control_1_out_184), .row7(display_control_1_out_192), .row8(display_control_1_out_200),
    .row9(display_control_1_out_208), .row10(display_control_1_out_216), .row11(display_control_1_out_224),
    .row12(display_control_1_out_232), .row13(display_control_1_out_240), .row14(display_control_1_out_248),
    .row15(display_control_1_out_256));
  DotMatrix #(.inputtype("row"), .matrixcols(16), .matrixrows(16)) dotmatrix_7 (
    .row0(display_control_1_out_264), .row1(display_control_1_out_272), .row2(display_control_1_out_280),
    .row3(display_control_1_out_288), .row4(display_control_1_out_296), .row5(display_control_1_out_304),
    .row6(display_control_1_out_312), .row7(display_control_1_out_320), .row8(display_control_1_out_328),
    .row9(display_control_1_out_336), .row10(display_control_1_out_344), .row11(display_control_1_out_352),
    .row12(display_control_1_out_360), .row13(display_control_1_out_368), .row14(display_control_1_out_376),
    .row15(display_control_1_out_384));
  DotMatrix #(.inputtype("row"), .matrixcols(16), .matrixrows(16)) dotmatrix_8 (
    .row0(display_control_1_out_392), .row1(display_control_1_out_400), .row2(display_control_1_out_408),
    .row3(display_control_1_out_416), .row4(display_control_1_out_424), .row5(display_control_1_out_432),
    .row6(display_control_1_out_440), .row7(display_control_1_out_448), .row8(display_control_1_out_456),
    .row9(display_control_1_out_464), .row10(display_control_1_out_472), .row11(display_control_1_out_480),
    .row12(display_control_1_out_488), .row13(display_control_1_out_496), .row14(display_control_1_out_504),
    .row15(display_control_1_out_512));
  or or_1 (CLK, C_out, and_1_out);
  and and_1 (and_1_out, clock_1_out, not_1_out);
  // Probe on counter_1_q
  Counter_part #(.width(32), .max('hffffffff)) counter_1 (
    .Q(counter_1_q), .clk(CLK), .clr(RESET));  // open: load, D, count, carry
  CPU cpu_1 (
    .instruction(rom_1_data), .inM(ram_1_data), .Write(cpu_1_write), .addressM(cpu_1_addressm),
    .outM(cpu_1_outm), .counter(cpu_1_counter), .CLK(CLK), .RESET(RESET), .BREAK(cpu_1_break));
  DotMatrix #(.inputtype("row"), .matrixcols(16), .matrixrows(16)) dotmatrix_9 (
    .row0(display_control_1_out_9), .row1(display_control_1_out_17), .row2(display_control_1_out_25),
    .row3(display_control_1_out_33), .row4(display_control_1_out_41), .row5(display_control_1_out_49),
    .row6(display_control_1_out_57), .row7(display_control_1_out_65), .row8(display_control_1_out_73),
    .row9(display_control_1_out_81), .row10(display_control_1_out_89), .row11(display_control_1_out_97),
    .row12(display_control_1_out_105), .row13(display_control_1_out_113), .row14(display_control_1_out_121),
    .row15(display_control_1_out_129));
  DotMatrix #(.inputtype("row"), .matrixcols(16), .matrixrows(16)) dotmatrix_10 (
    .row0(display_control_1_out_137), .row1(display_control_1_out_145), .row2(display_control_1_out_153),
    .row3(display_control_1_out_161), .row4(display_control_1_out_169), .row5(display_control_1_out_177),
    .row6(display_control_1_out_185), .row7(display_control_1_out_193), .row8(display_control_1_out_201),
    .row9(display_control_1_out_209), .row10(display_control_1_out_217), .row11(display_control_1_out_225),
    .row12(display_control_1_out_233), .row13(display_control_1_out_241), .row14(display_control_1_out_249),
    .row15(display_control_1_out_257));
  DotMatrix #(.inputtype("row"), .matrixcols(16), .matrixrows(16)) dotmatrix_11 (
    .row0(display_control_1_out_265), .row1(display_control_1_out_273), .row2(display_control_1_out_281),
    .row3(display_control_1_out_289), .row4(display_control_1_out_297), .row5(display_control_1_out_305),
    .row6(display_control_1_out_313), .row7(display_control_1_out_321), .row8(display_control_1_out_329),
    .row9(display_control_1_out_337), .row10(display_control_1_out_345), .row11(display_control_1_out_353),
    .row12(display_control_1_out_361), .row13(display_control_1_out_369), .row14(display_control_1_out_377),
    .row15(display_control_1_out_385));
  DotMatrix #(.inputtype("row"), .matrixcols(16), .matrixrows(16)) dotmatrix_12 (
    .row0(display_control_1_out_393), .row1(display_control_1_out_401), .row2(display_control_1_out_409),
    .row3(display_control_1_out_417), .row4(display_control_1_out_425), .row5(display_control_1_out_433),
    .row6(display_control_1_out_441), .row7(display_control_1_out_449), .row8(display_control_1_out_457),
    .row9(display_control_1_out_465), .row10(display_control_1_out_473), .row11(display_control_1_out_481),
    .row12(display_control_1_out_489), .row13(display_control_1_out_497), .row14(display_control_1_out_505),
    .row15(display_control_1_out_513));
  DotMatrix #(.inputtype("row"), .matrixcols(16), .matrixrows(16)) dotmatrix_13 (
    .row0(display_control_1_out_10), .row1(display_control_1_out_18), .row2(display_control_1_out_26),
    .row3(display_control_1_out_34), .row4(display_control_1_out_42), .row5(display_control_1_out_50),
    .row6(display_control_1_out_58), .row7(display_control_1_out_66), .row8(display_control_1_out_74),
    .row9(display_control_1_out_82), .row10(display_control_1_out_90), .row11(display_control_1_out_98),
    .row12(display_control_1_out_106), .row13(display_control_1_out_114), .row14(display_control_1_out_122),
    .row15(display_control_1_out_130));
  DotMatrix #(.inputtype("row"), .matrixcols(16), .matrixrows(16)) dotmatrix_14 (
    .row0(display_control_1_out_138), .row1(display_control_1_out_146), .row2(display_control_1_out_154),
    .row3(display_control_1_out_162), .row4(display_control_1_out_170), .row5(display_control_1_out_178),
    .row6(display_control_1_out_186), .row7(display_control_1_out_194), .row8(display_control_1_out_202),
    .row9(display_control_1_out_210), .row10(display_control_1_out_218), .row11(display_control_1_out_226),
    .row12(display_control_1_out_234), .row13(display_control_1_out_242), .row14(display_control_1_out_250),
    .row15(display_control_1_out_258));
  DotMatrix #(.inputtype("row"), .matrixcols(16), .matrixrows(16)) dotmatrix_15 (
    .row0(display_control_1_out_266), .row1(display_control_1_out_274), .row2(display_control_1_out_282),
    .row3(display_control_1_out_290), .row4(display_control_1_out_298), .row5(display_control_1_out_306),
    .row6(display_control_1_out_314), .row7(display_control_1_out_322), .row8(display_control_1_out_330),
    .row9(display_control_1_out_338), .row10(display_control_1_out_346), .row11(display_control_1_out_354),
    .row12(display_control_1_out_362), .row13(display_control_1_out_370), .row14(display_control_1_out_378),
    .row15(display_control_1_out_386));
  DotMatrix #(.inputtype("row"), .matrixcols(16), .matrixrows(16)) dotmatrix_16 (
    .row0(display_control_1_out_394), .row1(display_control_1_out_402), .row2(display_control_1_out_410),
    .row3(display_control_1_out_418), .row4(display_control_1_out_426), .row5(display_control_1_out_434),
    .row6(display_control_1_out_442), .row7(display_control_1_out_450), .row8(display_control_1_out_458),
    .row9(display_control_1_out_466), .row10(display_control_1_out_474), .row11(display_control_1_out_482),
    .row12(display_control_1_out_490), .row13(display_control_1_out_498), .row14(display_control_1_out_506),
    .row15(display_control_1_out_514));
  Debug_Board debug_board_1 (
    .Address(cpu_1_addressm), .Data(cpu_1_outm), .Write(cpu_1_write), .CLK(CLK), .RESET(RESET));
  RAM #(.addrWidth(16), .dataWidth(16), .bus("separate")) ram_1 (
    .addr(cpu_1_addressm), .din(cpu_1_outm), .data(ram_1_data), .str(cpu_1_write), .clk(CLK), .ld(1'b1),
    .clr(RESET));  // open: sel
  DotMatrix #(.inputtype("row"), .matrixcols(16), .matrixrows(16)) dotmatrix_17 (
    .row0(display_control_1_out_11), .row1(display_control_1_out_19), .row2(display_control_1_out_27),
    .row3(display_control_1_out_35), .row4(display_control_1_out_43), .row5(display_control_1_out_51),
    .row6(display_control_1_out_59), .row7(display_control_1_out_67), .row8(display_control_1_out_75),
    .row9(display_control_1_out_83), .row10(display_control_1_out_91), .row11(display_control_1_out_99),
    .row12(display_control_1_out_107), .row13(display_control_1_out_115), .row14(display_control_1_out_123),
    .row15(display_control_1_out_131));
  DotMatrix #(.inputtype("row"), .matrixcols(16), .matrixrows(16)) dotmatrix_18 (
    .row0(display_control_1_out_139), .row1(display_control_1_out_147), .row2(display_control_1_out_155),
    .row3(display_control_1_out_163), .row4(display_control_1_out_171), .row5(display_control_1_out_179),
    .row6(display_control_1_out_187), .row7(display_control_1_out_195), .row8(display_control_1_out_203),
    .row9(display_control_1_out_211), .row10(display_control_1_out_219), .row11(display_control_1_out_227),
    .row12(display_control_1_out_235), .row13(display_control_1_out_243), .row14(display_control_1_out_251),
    .row15(display_control_1_out_259));
  DotMatrix #(.inputtype("row"), .matrixcols(16), .matrixrows(16)) dotmatrix_19 (
    .row0(display_control_1_out_267), .row1(display_control_1_out_275), .row2(display_control_1_out_283),
    .row3(display_control_1_out_291), .row4(display_control_1_out_299), .row5(display_control_1_out_307),
    .row6(display_control_1_out_315), .row7(display_control_1_out_323), .row8(display_control_1_out_331),
    .row9(display_control_1_out_339), .row10(display_control_1_out_347), .row11(display_control_1_out_355),
    .row12(display_control_1_out_363), .row13(display_control_1_out_371), .row14(display_control_1_out_379),
    .row15(display_control_1_out_387));
  DotMatrix #(.inputtype("row"), .matrixcols(16), .matrixrows(16)) dotmatrix_20 (
    .row0(display_control_1_out_395), .row1(display_control_1_out_403), .row2(display_control_1_out_411),
    .row3(display_control_1_out_419), .row4(display_control_1_out_427), .row5(display_control_1_out_435),
    .row6(display_control_1_out_443), .row7(display_control_1_out_451), .row8(display_control_1_out_459),
    .row9(display_control_1_out_467), .row10(display_control_1_out_475), .row11(display_control_1_out_483),
    .row12(display_control_1_out_491), .row13(display_control_1_out_499), .row14(display_control_1_out_507),
    .row15(display_control_1_out_515));
  DotMatrix #(.inputtype("row"), .matrixcols(16), .matrixrows(16)) dotmatrix_21 (
    .row0(display_control_1_out_12), .row1(display_control_1_out_20), .row2(display_control_1_out_28),
    .row3(display_control_1_out_36), .row4(display_control_1_out_44), .row5(display_control_1_out_52),
    .row6(display_control_1_out_60), .row7(display_control_1_out_68), .row8(display_control_1_out_76),
    .row9(display_control_1_out_84), .row10(display_control_1_out_92), .row11(display_control_1_out_100),
    .row12(display_control_1_out_108), .row13(display_control_1_out_116), .row14(display_control_1_out_124),
    .row15(display_control_1_out_132));
  DotMatrix #(.inputtype("row"), .matrixcols(16), .matrixrows(16)) dotmatrix_22 (
    .row0(display_control_1_out_140), .row1(display_control_1_out_148), .row2(display_control_1_out_156),
    .row3(display_control_1_out_164), .row4(display_control_1_out_172), .row5(display_control_1_out_180),
    .row6(display_control_1_out_188), .row7(display_control_1_out_196), .row8(display_control_1_out_204),
    .row9(display_control_1_out_212), .row10(display_control_1_out_220), .row11(display_control_1_out_228),
    .row12(display_control_1_out_236), .row13(display_control_1_out_244), .row14(display_control_1_out_252),
    .row15(display_control_1_out_260));
  DotMatrix #(.inputtype("row"), .matrixcols(16), .matrixrows(16)) dotmatrix_23 (
    .row0(display_control_1_out_268), .row1(display_control_1_out_276), .row2(display_control_1_out_284),
    .row3(display_control_1_out_292), .row4(display_control_1_out_300), .row5(display_control_1_out_308),
    .row6(display_control_1_out_316), .row7(display_control_1_out_324), .row8(display_control_1_out_332),
    .row9(display_control_1_out_340), .row10(display_control_1_out_348), .row11(display_control_1_out_356),
    .row12(display_control_1_out_364), .row13(display_control_1_out_372), .row14(display_control_1_out_380),
    .row15(display_control_1_out_388));
  DotMatrix #(.inputtype("row"), .matrixcols(16), .matrixrows(16)) dotmatrix_24 (
    .row0(display_control_1_out_396), .row1(display_control_1_out_404), .row2(display_control_1_out_412),
    .row3(display_control_1_out_420), .row4(display_control_1_out_428), .row5(display_control_1_out_436),
    .row6(display_control_1_out_444), .row7(display_control_1_out_452), .row8(display_control_1_out_460),
    .row9(display_control_1_out_468), .row10(display_control_1_out_476), .row11(display_control_1_out_484),
    .row12(display_control_1_out_492), .row13(display_control_1_out_500), .row14(display_control_1_out_508),
    .row15(display_control_1_out_516));
  DotMatrix #(.inputtype("row"), .matrixcols(16), .matrixrows(16)) dotmatrix_25 (
    .row0(display_control_1_out_13), .row1(display_control_1_out_21), .row2(display_control_1_out_29),
    .row3(display_control_1_out_37), .row4(display_control_1_out_45), .row5(display_control_1_out_53),
    .row6(display_control_1_out_61), .row7(display_control_1_out_69), .row8(display_control_1_out_77),
    .row9(display_control_1_out_85), .row10(display_control_1_out_93), .row11(display_control_1_out_101),
    .row12(display_control_1_out_109), .row13(display_control_1_out_117), .row14(display_control_1_out_125),
    .row15(display_control_1_out_133));
  DotMatrix #(.inputtype("row"), .matrixcols(16), .matrixrows(16)) dotmatrix_26 (
    .row0(display_control_1_out_141), .row1(display_control_1_out_149), .row2(display_control_1_out_157),
    .row3(display_control_1_out_165), .row4(display_control_1_out_173), .row5(display_control_1_out_181),
    .row6(display_control_1_out_189), .row7(display_control_1_out_197), .row8(display_control_1_out_205),
    .row9(display_control_1_out_213), .row10(display_control_1_out_221), .row11(display_control_1_out_229),
    .row12(display_control_1_out_237), .row13(display_control_1_out_245), .row14(display_control_1_out_253),
    .row15(display_control_1_out_261));
  DotMatrix #(.inputtype("row"), .matrixcols(16), .matrixrows(16)) dotmatrix_27 (
    .row0(display_control_1_out_269), .row1(display_control_1_out_277), .row2(display_control_1_out_285),
    .row3(display_control_1_out_293), .row4(display_control_1_out_301), .row5(display_control_1_out_309),
    .row6(display_control_1_out_317), .row7(display_control_1_out_325), .row8(display_control_1_out_333),
    .row9(display_control_1_out_341), .row10(display_control_1_out_349), .row11(display_control_1_out_357),
    .row12(display_control_1_out_365), .row13(display_control_1_out_373), .row14(display_control_1_out_381),
    .row15(display_control_1_out_389));
  DotMatrix #(.inputtype("row"), .matrixcols(16), .matrixrows(16)) dotmatrix_28 (
    .row0(display_control_1_out_397), .row1(display_control_1_out_405), .row2(display_control_1_out_413),
    .row3(display_control_1_out_421), .row4(display_control_1_out_429), .row5(display_control_1_out_437),
    .row6(display_control_1_out_445), .row7(display_control_1_out_453), .row8(display_control_1_out_461),
    .row9(display_control_1_out_469), .row10(display_control_1_out_477), .row11(display_control_1_out_485),
    .row12(display_control_1_out_493), .row13(display_control_1_out_501), .row14(display_control_1_out_509),
    .row15(display_control_1_out_517));
  DotMatrix #(.inputtype("row"), .matrixcols(16), .matrixrows(16)) dotmatrix_29 (
    .row0(display_control_1_out_14), .row1(display_control_1_out_22), .row2(display_control_1_out_30),
    .row3(display_control_1_out_38), .row4(display_control_1_out_46), .row5(display_control_1_out_54),
    .row6(display_control_1_out_62), .row7(display_control_1_out_70), .row8(display_control_1_out_78),
    .row9(display_control_1_out_86), .row10(display_control_1_out_94), .row11(display_control_1_out_102),
    .row12(display_control_1_out_110), .row13(display_control_1_out_118), .row14(display_control_1_out_126),
    .row15(display_control_1_out_134));
  DotMatrix #(.inputtype("row"), .matrixcols(16), .matrixrows(16)) dotmatrix_30 (
    .row0(display_control_1_out_142), .row1(display_control_1_out_150), .row2(display_control_1_out_158),
    .row3(display_control_1_out_166), .row4(display_control_1_out_174), .row5(display_control_1_out_182),
    .row6(display_control_1_out_190), .row7(display_control_1_out_198), .row8(display_control_1_out_206),
    .row9(display_control_1_out_214), .row10(display_control_1_out_222), .row11(display_control_1_out_230),
    .row12(display_control_1_out_238), .row13(display_control_1_out_246), .row14(display_control_1_out_254),
    .row15(display_control_1_out_262));
  DotMatrix #(.inputtype("row"), .matrixcols(16), .matrixrows(16)) dotmatrix_31 (
    .row0(display_control_1_out_270), .row1(display_control_1_out_278), .row2(display_control_1_out_286),
    .row3(display_control_1_out_294), .row4(display_control_1_out_302), .row5(display_control_1_out_310),
    .row6(display_control_1_out_318), .row7(display_control_1_out_326), .row8(display_control_1_out_334),
    .row9(display_control_1_out_342), .row10(display_control_1_out_350), .row11(display_control_1_out_358),
    .row12(display_control_1_out_366), .row13(display_control_1_out_374), .row14(display_control_1_out_382),
    .row15(display_control_1_out_390));
  DotMatrix #(.inputtype("row"), .matrixcols(16), .matrixrows(16)) dotmatrix_32 (
    .row0(display_control_1_out_398), .row1(display_control_1_out_406), .row2(display_control_1_out_414),
    .row3(display_control_1_out_422), .row4(display_control_1_out_430), .row5(display_control_1_out_438),
    .row6(display_control_1_out_446), .row7(display_control_1_out_454), .row8(display_control_1_out_462),
    .row9(display_control_1_out_470), .row10(display_control_1_out_478), .row11(display_control_1_out_486),
    .row12(display_control_1_out_494), .row13(display_control_1_out_502), .row14(display_control_1_out_510),
    .row15(display_control_1_out_518));

  // Notes on the sheet:
  //   Screen Width
  //   ROM
  //   Manual Clock
  //   contents of rom_1 (hex, n*v repeats v):
  //   100 ec10 0 e308 12c ec10 1 e308 190 ec10 2 e308 bb8 ec10 3 e308 bc2 ec10 4 e308 3d75 ec10 f e308 0
  //   ec10 e e308 22 ec10 d e308 4012 ea87 0 ec10 0 fc20 e308 0 fdc8 0 fc88 fc20 fc10 10 e308 800 ec10 0
  //   fc20 e308 0 fdc8 10 fc10 0 fc20 e308 0 fdc8 0 fc88 fc20 fc10 0 fc88 fc20 f088 0 fdc8 37fe ec10 0
  //   fc20 e308 0 fdc8 0 fc88 fc20 fc10 5 e308 0 fc88 fc20 fc10 4 e308 5 fc10 0 fc20 e308 0 fdc8 4 fc10 0
  //   e090 f e308 0 fc88 fc20 fc10 f fc20 e308 801 ec10 0 fc20 e308 0 fdc8 10 fc10 0 fc20 e308 0 fdc8 0
  //   fc88 fc20 fc10 0 fc88 fc20 f088 0 fdc8 802 ec10 0 fc20 e308 0 fdc8 0 fc88 fc20 fc10 5 e308 0 fc88
  //   fc20 fc10 4 e308 5 fc10 0 fc20 e308 0 fdc8 4 fc10 0 e090 f e308 0 fc88 fc20 fc10 f fc20 e308 0 ec10
  //   0 fc20 e308 0 fdc8 3fdd ea87 2 fc10 0 e090 e320 fc10 0 fc20 e308 0 fdc8 10 fc10 0 fc20 e308 0 fdc8 0
  //   fc88 fc20 fc10 0 fc88 fc20 f088 0 fdc8 0 fc88 fc20 fc10 4 e308 4 fc10 0 e090 e320 fc10 0 fc20 e308 0
  //   fdc8 3fdd ea87 2 fc10 0 e090 e320 fc10 0 fc20 e308 0 fdc8 10 fc10 0 fc20 e308 0 fdc8 0 fc88 fc20
  //   fc10 0 fc88 fc20 f088 0 fdc8 2 fc10 1 e090 e320 fc10 0 fc20 e308 0 fdc8 0 fc88 fc20 fc10 5 e308 0
  //   fc88 fc20 fc10 4 e308 5 fc10 0 fc20 e308 0 fdc8 4 fc10 0 e090 f e308 0 fc88 fc20 fc10 f fc20 e308 0
  //   ec10 0 fc20 e308 0 fdc8 3fdd ea87 0 ec10 0 fc20 e308 0 fdc8 2 fc10 0 e090 e320 fc10 0 fc20 e308 0
  //   fdc8 1 ec10 0 fc20 e308 0 fdc8 154 ec10 f e308 4072 ea87 0 fc88 fc20 fc10 15c e305 177 ea87 5 ec10 0
  //   fc20 e308 0 fdc8 3f06 ec10 f e308 1 ec10 e e308 171 ec10 d e308 4012 ea87 0 fc88 fc20 fc10 5 e308
  //   800 ec10 0 fc20 e308 0 fdc8 1 fc10 0 e090 f e308 0 fc88 fc20 fc10 f fc20 e308 0 ec10 0 fc20 e308 0
  //   fdc8 1 fc10 0 e090 e320 fc10 0 fc20 e308 0 fdc8 0 fc88 fc20 fc10 0 fc88 fc20 f088 0 fdc8 0 fc88 fc20
  //   fc10 4 e308 4 fc10 0 e090 e320 fc10 0 fc20 e308 0 fdc8 2 fc10 0 e090 e320 fc10 0 fc20 e308 0 fdc8
  //   1c9 ec10 f e308 4072 ea87 0 fc88 fc20 fc48 0 fdc8 0 fc88 fc20 fc10 211 e305 1 ec10 0 fc20 e308 0
  //   fdc8 1 fc10 0 e090 e320 fc10 0 fc20 e308 0 fdc8 0 fc88 fc20 fc10 0 fc88 fc20 f088 0 fdc8 0 fc88 fc20
  //   fc10 4 e308 4 fc10 0 e090 e320 fc10 0 fc20 e308 0 fdc8 1 fc10 0 e090 f e308 0 fc88 fc20 fc10 f fc20
  //   e308 18b ea87 1 fc10 0 e090 e320 fc10 0 fc20 e308 0 fdc8 2 fc10 0 e090 e320 fc10 0 fc20 e308 0 fdc8
  //   0 fc88 fc20 fc10 0 fc88 fc20 f088 0 fdc8 3ffb ec10 0 fc20 e308 0 fdc8 23e ec10 f e308 405b ea87 0
  //   fc88 fc20 fc10 246 e305 261 ea87 6 ec10 0 fc20 e308 0 fdc8 3f06 ec10 f e308 1 ec10 e e308 25b ec10 d
  //   e308 4012 ea87 0 fc88 fc20 fc10 5 e308 0 ec10 0 fc20 e308 0 fdc8 1 fc10 0 e090 e320 fc10 0 fc20 e308
  //   0 fdc8 0 fc88 fc20 fc10 0 fc88 fc20 f088 0 fdc8 0 fc88 fc20 fc10 4 e308 4 fc10 0 e090 e320 fc10 0
  //   fc20 e308 0 fdc8 2 fc10 0 e090 e320 fc10 0 fc20 e308 0 fdc8 2 ec10 0 fc20 e308 0 fdc8 0 fc88 fc20
  //   fc10 0 fc88 fc20 f088 0 fdc8 2b0 ec10 f e308 405b ea87 0 fc88 fc20 fc10 2b8 e305 524 ea87 2 fc10 0
  //   e090 e320 fc10 0 fc20 e308 0 fdc8 2 ec10 0 fc20 e308 0 fdc8 0 fc88 fc20 fc10 0 fc88 fc20 f088 0 fdc8
  //   1 fc10 0 e090 e320 fc10 0 fc20 e308 0 fdc8 0 fc88 fc20 fc10 0 fc88 fc20 f088 0 fdc8 0 ec10 0 fc20
  //   e308 0 fdc8 1 fc10 0 e090 e320 fc10 0 fc20 e308 0 fdc8 0 fc88 fc20 fc10 0 fc88 fc20 f088 0 fdc8 0
  //   fc88 fc20 fc10 4 e308 4 fc10 0 e090 e320 fc10 0 fc20 e308 0 fdc8 2 fc10 0 e090 e320 fc10 0 fc20 e308
  //   0 fdc8 0 fc88 fc20 fc10 0 fc88 fc20 f4c8 fcc8 0 fdc8 2 ec10 0 fc20 e308 0 fdc8 0 fc88 fc20 fc10 0
  //   fc88 fc20 f4c8 fcc8 0 fdc8 0 fc88 fc20 fc10 5 e308 0 fc88 fc20 fc10 4 e308 5 fc10 0 fc20 e308 0 fdc8
  //   4 fc10 0 e090 f e308 0 fc88 fc20 fc10 f fc20 e308 1 ec10 0 fc20 e308 0 fdc8 1 fc10 0 e090 e320 fc10
  //   0 fc20 e308 0 fdc8 0 fc88 fc20 fc10 0 fc88 fc20 f088 0 fdc8 0 fc88 fc20 fc10 4 e308 4 fc10 0 e090
  //   e320 fc10 0 fc20 e308 0 fdc8 1 fc10 0 e090 e320 fc10 0 fc20 e308 0 fdc8 2 ec10 0 fc20 e308 0 fdc8 0
  //   fc88 fc20 fc10 0 fc88 fc20 f088 0 fdc8 3ad ec10 f e308 4044 ea87 0 fc88 fc20 fc10 3b5 e305 439 ea87
  //   2 fc10 0 e090 e320 fc10 0 fc20 e308 0 fdc8 3 ec10 0 fc20 e308 0 fdc8 0 fc88 fc20 fc10 0 fc88 fc20
  //   f088 0 fdc8 1 fc10 0 e090 e320 fc10 0 fc20 e308 0 fdc8 0 fc88 fc20 fc10 0 fc88 fc20 f088 0 fdc8 1
  //   fc10 0 e090 e320 fc10 0 fc20 e308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
  //   RAM
endmodule

module CPU (
  input  CLK,
  input  RESET,
  input  [15:0] instruction,
  input  [15:0] inM,
  output [15:0] addressM,
  output [15:0] outM,
  output Write,
  output [15:0] counter,
  output BREAK
);

  wire ALU_ng, ALU_zr, nor_1_out, not_1_out, or_1_out;
  wire [15:0] controlled_buffer_1_out, multiplexer_1_out, Register_D_q;

  Multiplexer #(.width(16), .enable("false")) multiplexer_1 (
    .in0({16{1'b0}}), .in1(instruction), .out({multiplexer_1_out[15:4], Write, multiplexer_1_out[2:0]}),
    .sel(instruction[15]));
  not not_1 (not_1_out, instruction[15]);
  assign controlled_buffer_1_out = not_1_out ? {1'b0, instruction[14:0]} : 16'bz;  // Controlled_Buffer controlled_buffer_1
  or or_1 (or_1_out, not_1_out, multiplexer_1_out[5]);
  nor nor_1 (nor_1_out, multiplexer_1_out[13], multiplexer_1_out[14]);
  and and_1 (BREAK, nor_1_out, multiplexer_1_out[15]);
  Register #(.width(16)) Register_A (.D(controlled_buffer_1_out), .en(or_1_out), .Q(addressM), .clk(CLK), .clr(RESET));
  assign controlled_buffer_1_out = instruction[15] ? outM : 16'bz;  // Controlled_Buffer controlled_buffer_2
  Register #(.width(16)) Register_D (.D(outM), .en(multiplexer_1_out[4]), .Q(Register_D_q), .clk(CLK), .clr(RESET));
  Logic ALU (
    .CMP(multiplexer_1_out[12:6]), .A(addressM), .M(inM), .D(Register_D_q), .out(outM), .ng(ALU_ng),
    .zr(ALU_zr));
  Counter counter_1 (
    .jump_control(multiplexer_1_out[2:0]), .out_7(counter), .jump_address(addressM), .zr(ALU_zr),
    .ng(ALU_ng), .in_1(CLK), .in_2(RESET));

  // Notes on the sheet:
  //   100 = BREAK
endmodule

module ALU (
  input  zx,
  input  nx,
  input  zy,
  input  ny,
  input  f,
  input  no,
  input  [15:0] x,
  input  [15:0] y,
  output [15:0] out,
  output zr,
  output ng
);

  wire not_3_out;
  wire [15:0] adder_1_out, and_1_out, multiplexer_1_out, multiplexer_2_out, multiplexer_3_out,
       multiplexer_4_out, multiplexer_5_out, not_1_out, not_2_out, not_4_out;

  Multiplexer #(.width(16), .enable("false")) multiplexer_1 (
    .in0(x), .in1({16{1'b0}}), .out(multiplexer_1_out), .sel(zx));
  assign not_1_out = ~multiplexer_1_out;  // NOT_Gate not_1, 16 bits wide
  Multiplexer #(.width(16), .enable("false")) multiplexer_2 (
    .in0(y), .in1({16{1'b0}}), .out(multiplexer_2_out), .sel(zy));
  assign not_2_out = ~multiplexer_2_out;  // NOT_Gate not_2, 16 bits wide
  Multiplexer #(.width(16), .enable("false")) multiplexer_3 (
    .in0(multiplexer_1_out), .in1(not_1_out), .out(multiplexer_3_out), .sel(nx));
  Multiplexer #(.width(16), .enable("false")) multiplexer_4 (
    .in0(multiplexer_2_out), .in1(not_2_out), .out(multiplexer_4_out), .sel(ny));
  Adder #(.width(16)) adder_1 (.a(multiplexer_3_out), .b(multiplexer_4_out), .out(adder_1_out));  // open: cin, cout
  assign and_1_out = multiplexer_3_out & multiplexer_4_out;  // AND_Gate and_1, 16 bits wide
  not not_3 (not_3_out, f);
  Multiplexer #(.width(16), .enable("false")) multiplexer_5 (
    .in0(adder_1_out), .in1(and_1_out), .out(multiplexer_5_out), .sel(not_3_out));
  Multiplexer #(.width(16), .enable("false")) multiplexer_6 (
    .in0(multiplexer_5_out), .in1(not_4_out), .out({ng, out[14:0]}), .sel(no));
  assign not_4_out = ~multiplexer_5_out;  // NOT_Gate not_4, 16 bits wide
  nor nor_1 (zr, ng, out[14], out[13], out[12], out[11], out[10], out[9], out[8], out[7], out[6], out[5], out[4], out[3], out[2], out[1], out[0]);

  assign out[15] = ng;
endmodule

module Logic (
  input  [6:0] CMP,
  input  [15:0] A,
  input  [15:0] M,
  input  [15:0] D,
  output [15:0] out,
  output ng,
  output zr
);

  wire [15:0] multiplexer_1_out;

  Multiplexer #(.width(16), .enable("false")) multiplexer_1 (.in0(A), .in1(M), .out(multiplexer_1_out), .sel(CMP[6]));
  ALU alu_1 (
    .x(D), .out(out), .zx(CMP[5]), .nx(CMP[4]), .zy(CMP[3]), .ny(CMP[2]), .f(CMP[1]), .no(CMP[0]), .zr(zr),
    .ng(ng), .y(multiplexer_1_out));
endmodule

module Counter (
  input  in_1,
  input  in_2,
  input  zr,
  input  ng,
  input  [15:0] jump_address,
  input  [2:0] jump_control,
  output [15:0] out_7
);

  wire not_1_out, not_2_out, rom_1_data;

  ROM #(.addrWidth(5), .dataWidth(1)) rom_1 (.addr({jump_control, zr, ng}), .data(rom_1_data));  // open: sel
  not not_1 (not_1_out, rom_1_data);
  Counter_part #(.width(16), .max('hffff)) counter_1 (
    .load(rom_1_data), .D(jump_address), .count(not_1_out), .Q(out_7), .clk(not_2_out), .clr(in_2));  // open: carry
  not not_2 (not_2_out, in_1);
  // Probe on out_7

  // Other names for the same wires on the sheet: CLK = in_1; RESET = in_2

  // Notes on the sheet:
  //   Control counter and jump logic
  //   contents of rom_1 (hex, n*v repeats v):
  //   4*0 1 5*0 1 0 1 0 1 0 0 1 0 0 1 1 0 0 0 1 1 0 4*1
  //   ROM contains jump logic (this is simply a truth table)
  //   Here need to invert the clock signal to prevent the next instruction reach CPU too early
endmodule

module ScreenControl_old (
  input  CLK,
  input  Reset,
  input  [15:0] Data,
  input  Enable,
  input  [15:0] Address,
  output [15:0] out_6,
  output [15:0] out_7,
  output [15:0] out_8,
  output [15:0] out_9,
  output [15:0] out_10,
  output [15:0] out_11,
  output [15:0] out_12,
  output [15:0] out_13,
  output [15:0] out_14,
  output [15:0] out_15,
  output [15:0] out_16,
  output [15:0] out_17,
  output [15:0] out_18,
  output [15:0] out_19,
  output [15:0] out_20,
  output [15:0] out_21
);

  wire and_1_out, and_2_out, and_3_out, and_4_out, and_5_out, and_6_out, and_7_out, and_8_out, and_9_out,
       and_10_out, and_11_out, and_12_out, and_13_out, and_14_out, and_15_out, and_16_out;

  and and_1 (and_1_out, Enable, Address[15]);
  Register #(.width(16)) register_1 (.D(Data), .en(and_1_out), .Q(out_6), .clk(CLK), .clr(Reset));
  and and_2 (and_2_out, Enable, Address[14]);
  Register #(.width(16)) register_2 (.D(Data), .en(and_2_out), .Q(out_7), .clk(CLK), .clr(Reset));
  and and_3 (and_3_out, Enable, Address[13]);
  Register #(.width(16)) register_3 (.D(Data), .en(and_3_out), .Q(out_8), .clk(CLK), .clr(Reset));
  Register #(.width(16)) register_4 (.D(Data), .en(and_4_out), .Q(out_9), .clk(CLK), .clr(Reset));
  and and_4 (and_4_out, Enable, Address[12]);
  Register #(.width(16)) register_5 (.D(Data), .en(and_5_out), .Q(out_10), .clk(CLK), .clr(Reset));
  and and_5 (and_5_out, Enable, Address[11]);
  Register #(.width(16)) register_6 (.D(Data), .en(and_6_out), .Q(out_11), .clk(CLK), .clr(Reset));
  and and_6 (and_6_out, Enable, Address[10]);
  and and_7 (and_7_out, Enable, Address[9]);
  Register #(.width(16)) register_7 (.D(Data), .en(and_7_out), .Q(out_12), .clk(CLK), .clr(Reset));
  and and_8 (and_8_out, Enable, Address[8]);
  Register #(.width(16)) register_8 (.D(Data), .en(and_8_out), .Q(out_13), .clk(CLK), .clr(Reset));
  and and_9 (and_9_out, Enable, Address[7]);
  Register #(.width(16)) register_9 (.D(Data), .en(and_9_out), .Q(out_14), .clk(CLK), .clr(Reset));
  and and_10 (and_10_out, Enable, Address[6]);
  Register #(.width(16)) register_10 (.D(Data), .en(and_10_out), .Q(out_15), .clk(CLK), .clr(Reset));
  and and_11 (and_11_out, Enable, Address[5]);
  Register #(.width(16)) register_11 (.D(Data), .en(and_11_out), .Q(out_16), .clk(CLK), .clr(Reset));
  Register #(.width(16)) register_12 (.D(Data), .en(and_12_out), .Q(out_17), .clk(CLK), .clr(Reset));
  and and_12 (and_12_out, Enable, Address[4]);
  Register #(.width(16)) register_13 (.D(Data), .en(and_13_out), .Q(out_18), .clk(CLK), .clr(Reset));
  and and_13 (and_13_out, Enable, Address[3]);
  Register #(.width(16)) register_14 (.D(Data), .en(and_14_out), .Q(out_19), .clk(CLK), .clr(Reset));
  and and_14 (and_14_out, Enable, Address[2]);
  and and_15 (and_15_out, Enable, Address[1]);
  Register #(.width(16)) register_15 (.D(Data), .en(and_15_out), .Q(out_20), .clk(CLK), .clr(Reset));
  and and_16 (and_16_out, Enable, Address[0]);
  Register #(.width(16)) register_16 (.D(Data), .en(and_16_out), .Q(out_21), .clk(CLK), .clr(Reset));

  // Other names for the same wires on the sheet: RST = Reset
endmodule
module Display_old (
  input  [15:0] Address,
  input  [15:0] Data,
  input  Write,
  input  CLK,
  input  RESET
);

  wire address_translator_1_active___1_means_address_in_range, and_1_out;
  wire [3:0] pane_decoder_1_pane_address, pane_decoder_1_pane_address_3;
  wire [15:0] address_translator_1_translated_address, Local_Address, pane_register_1_out_6,
       pane_register_1_out_7, pane_register_1_out_8, pane_register_1_out_9, pane_register_1_out_10,
       pane_register_1_out_11, pane_register_1_out_12, pane_register_1_out_13, pane_register_1_out_14,
       pane_register_1_out_15, pane_register_1_out_16, pane_register_1_out_17, pane_register_1_out_18,
       pane_register_1_out_19, pane_register_1_out_20, pane_register_1_out_21, pane_register_2_out_6,
       pane_register_2_out_7, pane_register_2_out_8, pane_register_2_out_9, pane_register_2_out_10,
       pane_register_2_out_11, pane_register_2_out_12, pane_register_2_out_13, pane_register_2_out_14,
       pane_register_2_out_15, pane_register_2_out_16, pane_register_2_out_17, pane_register_2_out_18,
       pane_register_2_out_19, pane_register_2_out_20, pane_register_2_out_21, pane_register_3_out_6,
       pane_register_3_out_7, pane_register_3_out_8, pane_register_3_out_9, pane_register_3_out_10,
       pane_register_3_out_11, pane_register_3_out_12, pane_register_3_out_13, pane_register_3_out_14,
       pane_register_3_out_15, pane_register_3_out_16, pane_register_3_out_17, pane_register_3_out_18,
       pane_register_3_out_19, pane_register_3_out_20, pane_register_3_out_21, pane_register_4_out_6,
       pane_register_4_out_7, pane_register_4_out_8, pane_register_4_out_9, pane_register_4_out_10,
       pane_register_4_out_11, pane_register_4_out_12, pane_register_4_out_13, pane_register_4_out_14,
       pane_register_4_out_15, pane_register_4_out_16, pane_register_4_out_17, pane_register_4_out_18,
       pane_register_4_out_19, pane_register_4_out_20, pane_register_4_out_21, pane_register_5_out_6,
       pane_register_5_out_7, pane_register_5_out_8, pane_register_5_out_9, pane_register_5_out_10,
       pane_register_5_out_11, pane_register_5_out_12, pane_register_5_out_13, pane_register_5_out_14,
       pane_register_5_out_15, pane_register_5_out_16, pane_register_5_out_17, pane_register_5_out_18,
       pane_register_5_out_19, pane_register_5_out_20, pane_register_5_out_21, pane_register_6_out_6,
       pane_register_6_out_7, pane_register_6_out_8, pane_register_6_out_9, pane_register_6_out_10,
       pane_register_6_out_11, pane_register_6_out_12, pane_register_6_out_13, pane_register_6_out_14,
       pane_register_6_out_15, pane_register_6_out_16, pane_register_6_out_17, pane_register_6_out_18,
       pane_register_6_out_19, pane_register_6_out_20, pane_register_6_out_21, pane_register_7_out_6,
       pane_register_7_out_7, pane_register_7_out_8, pane_register_7_out_9, pane_register_7_out_10,
       pane_register_7_out_11, pane_register_7_out_12, pane_register_7_out_13, pane_register_7_out_14,
       pane_register_7_out_15, pane_register_7_out_16, pane_register_7_out_17, pane_register_7_out_18,
       pane_register_7_out_19, pane_register_7_out_20, pane_register_7_out_21, pane_register_8_out_6,
       pane_register_8_out_7, pane_register_8_out_8, pane_register_8_out_9, pane_register_8_out_10,
       pane_register_8_out_11, pane_register_8_out_12, pane_register_8_out_13, pane_register_8_out_14,
       pane_register_8_out_15, pane_register_8_out_16, pane_register_8_out_17, pane_register_8_out_18,
       pane_register_8_out_19, pane_register_8_out_20, pane_register_8_out_21, pane_register_9_out_6,
       pane_register_9_out_7, pane_register_9_out_8, pane_register_9_out_9, pane_register_9_out_10,
       pane_register_9_out_11, pane_register_9_out_12, pane_register_9_out_13, pane_register_9_out_14,
       pane_register_9_out_15, pane_register_9_out_16, pane_register_9_out_17, pane_register_9_out_18,
       pane_register_9_out_19, pane_register_9_out_20, pane_register_9_out_21, pane_register_10_out_6,
       pane_register_10_out_7, pane_register_10_out_8, pane_register_10_out_9, pane_register_10_out_10,
       pane_register_10_out_11, pane_register_10_out_12, pane_register_10_out_13, pane_register_10_out_14,
       pane_register_10_out_15, pane_register_10_out_16, pane_register_10_out_17, pane_register_10_out_18,
       pane_register_10_out_19, pane_register_10_out_20, pane_register_10_out_21, pane_register_11_out_6,
       pane_register_11_out_7, pane_register_11_out_8, pane_register_11_out_9, pane_register_11_out_10,
       pane_register_11_out_11, pane_register_11_out_12, pane_register_11_out_13, pane_register_11_out_14,
       pane_register_11_out_15, pane_register_11_out_16, pane_register_11_out_17, pane_register_11_out_18,
       pane_register_11_out_19, pane_register_11_out_20, pane_register_11_out_21, pane_register_12_out_6,
       pane_register_12_out_7, pane_register_12_out_8, pane_register_12_out_9, pane_register_12_out_10,
       pane_register_12_out_11, pane_register_12_out_12, pane_register_12_out_13, pane_register_12_out_14,
       pane_register_12_out_15, pane_register_12_out_16, pane_register_12_out_17, pane_register_12_out_18,
       pane_register_12_out_19, pane_register_12_out_20, pane_register_12_out_21, pane_register_13_out_6,
       pane_register_13_out_7, pane_register_13_out_8, pane_register_13_out_9, pane_register_13_out_10,
       pane_register_13_out_11, pane_register_13_out_12, pane_register_13_out_13, pane_register_13_out_14,
       pane_register_13_out_15, pane_register_13_out_16, pane_register_13_out_17, pane_register_13_out_18,
       pane_register_13_out_19, pane_register_13_out_20, pane_register_13_out_21, pane_register_14_out_6,
       pane_register_14_out_7, pane_register_14_out_8, pane_register_14_out_9, pane_register_14_out_10,
       pane_register_14_out_11, pane_register_14_out_12, pane_register_14_out_13, pane_register_14_out_14,
       pane_register_14_out_15, pane_register_14_out_16, pane_register_14_out_17, pane_register_14_out_18,
       pane_register_14_out_19, pane_register_14_out_20, pane_register_14_out_21, pane_register_15_out_6,
       pane_register_15_out_7, pane_register_15_out_8, pane_register_15_out_9, pane_register_15_out_10,
       pane_register_15_out_11, pane_register_15_out_12, pane_register_15_out_13, pane_register_15_out_14,
       pane_register_15_out_15, pane_register_15_out_16, pane_register_15_out_17, pane_register_15_out_18,
       pane_register_15_out_19, pane_register_15_out_20, pane_register_15_out_21, pane_register_16_out_6,
       pane_register_16_out_7, pane_register_16_out_8, pane_register_16_out_9, pane_register_16_out_10,
       pane_register_16_out_11, pane_register_16_out_12, pane_register_16_out_13, pane_register_16_out_14,
       pane_register_16_out_15, pane_register_16_out_16, pane_register_16_out_17, pane_register_16_out_18,
       pane_register_16_out_19, pane_register_16_out_20, pane_register_16_out_21, pane_register_17_out_6,
       pane_register_17_out_7, pane_register_17_out_8, pane_register_17_out_9, pane_register_17_out_10,
       pane_register_17_out_11, pane_register_17_out_12, pane_register_17_out_13, pane_register_17_out_14,
       pane_register_17_out_15, pane_register_17_out_16, pane_register_17_out_17, pane_register_17_out_18,
       pane_register_17_out_19, pane_register_17_out_20, pane_register_17_out_21, pane_register_18_out_6,
       pane_register_18_out_7, pane_register_18_out_8, pane_register_18_out_9, pane_register_18_out_10,
       pane_register_18_out_11, pane_register_18_out_12, pane_register_18_out_13, pane_register_18_out_14,
       pane_register_18_out_15, pane_register_18_out_16, pane_register_18_out_17, pane_register_18_out_18,
       pane_register_18_out_19, pane_register_18_out_20, pane_register_18_out_21, pane_register_19_out_6,
       pane_register_19_out_7, pane_register_19_out_8, pane_register_19_out_9, pane_register_19_out_10,
       pane_register_19_out_11, pane_register_19_out_12, pane_register_19_out_13, pane_register_19_out_14,
       pane_register_19_out_15, pane_register_19_out_16, pane_register_19_out_17, pane_register_19_out_18,
       pane_register_19_out_19, pane_register_19_out_20, pane_register_19_out_21, pane_register_20_out_6,
       pane_register_20_out_7, pane_register_20_out_8, pane_register_20_out_9, pane_register_20_out_10,
       pane_register_20_out_11, pane_register_20_out_12, pane_register_20_out_13, pane_register_20_out_14,
       pane_register_20_out_15, pane_register_20_out_16, pane_register_20_out_17, pane_register_20_out_18,
       pane_register_20_out_19, pane_register_20_out_20, pane_register_20_out_21, pane_register_21_out_6,
       pane_register_21_out_7, pane_register_21_out_8, pane_register_21_out_9, pane_register_21_out_10,
       pane_register_21_out_11, pane_register_21_out_12, pane_register_21_out_13, pane_register_21_out_14,
       pane_register_21_out_15, pane_register_21_out_16, pane_register_21_out_17, pane_register_21_out_18,
       pane_register_21_out_19, pane_register_21_out_20, pane_register_21_out_21, pane_register_22_out_6,
       pane_register_22_out_7, pane_register_22_out_8, pane_register_22_out_9, pane_register_22_out_10,
       pane_register_22_out_11, pane_register_22_out_12, pane_register_22_out_13, pane_register_22_out_14,
       pane_register_22_out_15, pane_register_22_out_16, pane_register_22_out_17, pane_register_22_out_18,
       pane_register_22_out_19, pane_register_22_out_20, pane_register_22_out_21, pane_register_23_out_6,
       pane_register_23_out_7, pane_register_23_out_8, pane_register_23_out_9, pane_register_23_out_10,
       pane_register_23_out_11, pane_register_23_out_12, pane_register_23_out_13, pane_register_23_out_14,
       pane_register_23_out_15, pane_register_23_out_16, pane_register_23_out_17, pane_register_23_out_18,
       pane_register_23_out_19, pane_register_23_out_20, pane_register_23_out_21, pane_register_24_out_6,
       pane_register_24_out_7, pane_register_24_out_8, pane_register_24_out_9, pane_register_24_out_10,
       pane_register_24_out_11, pane_register_24_out_12, pane_register_24_out_13, pane_register_24_out_14,
       pane_register_24_out_15, pane_register_24_out_16, pane_register_24_out_17, pane_register_24_out_18,
       pane_register_24_out_19, pane_register_24_out_20, pane_register_24_out_21, pane_register_25_out_6,
       pane_register_25_out_7, pane_register_25_out_8, pane_register_25_out_9, pane_register_25_out_10,
       pane_register_25_out_11, pane_register_25_out_12, pane_register_25_out_13, pane_register_25_out_14,
       pane_register_25_out_15, pane_register_25_out_16, pane_register_25_out_17, pane_register_25_out_18,
       pane_register_25_out_19, pane_register_25_out_20, pane_register_25_out_21, pane_register_26_out_6,
       pane_register_26_out_7, pane_register_26_out_8, pane_register_26_out_9, pane_register_26_out_10,
       pane_register_26_out_11, pane_register_26_out_12, pane_register_26_out_13, pane_register_26_out_14,
       pane_register_26_out_15, pane_register_26_out_16, pane_register_26_out_17, pane_register_26_out_18,
       pane_register_26_out_19, pane_register_26_out_20, pane_register_26_out_21, pane_register_27_out_6,
       pane_register_27_out_7, pane_register_27_out_8, pane_register_27_out_9, pane_register_27_out_10,
       pane_register_27_out_11, pane_register_27_out_12, pane_register_27_out_13, pane_register_27_out_14,
       pane_register_27_out_15, pane_register_27_out_16, pane_register_27_out_17, pane_register_27_out_18,
       pane_register_27_out_19, pane_register_27_out_20, pane_register_27_out_21, pane_register_28_out_6,
       pane_register_28_out_7, pane_register_28_out_8, pane_register_28_out_9, pane_register_28_out_10,
       pane_register_28_out_11, pane_register_28_out_12, pane_register_28_out_13, pane_register_28_out_14,
       pane_register_28_out_15, pane_register_28_out_16, pane_register_28_out_17, pane_register_28_out_18,
       pane_register_28_out_19, pane_register_28_out_20, pane_register_28_out_21, pane_register_29_out_6,
       pane_register_29_out_7, pane_register_29_out_8, pane_register_29_out_9, pane_register_29_out_10,
       pane_register_29_out_11, pane_register_29_out_12, pane_register_29_out_13, pane_register_29_out_14,
       pane_register_29_out_15, pane_register_29_out_16, pane_register_29_out_17, pane_register_29_out_18,
       pane_register_29_out_19, pane_register_29_out_20, pane_register_29_out_21, pane_register_30_out_6,
       pane_register_30_out_7, pane_register_30_out_8, pane_register_30_out_9, pane_register_30_out_10,
       pane_register_30_out_11, pane_register_30_out_12, pane_register_30_out_13, pane_register_30_out_14,
       pane_register_30_out_15, pane_register_30_out_16, pane_register_30_out_17, pane_register_30_out_18,
       pane_register_30_out_19, pane_register_30_out_20, pane_register_30_out_21, pane_register_31_out_6,
       pane_register_31_out_7, pane_register_31_out_8, pane_register_31_out_9, pane_register_31_out_10,
       pane_register_31_out_11, pane_register_31_out_12, pane_register_31_out_13, pane_register_31_out_14,
       pane_register_31_out_15, pane_register_31_out_16, pane_register_31_out_17, pane_register_31_out_18,
       pane_register_31_out_19, pane_register_31_out_20, pane_register_31_out_21, pane_register_32_out_6,
       pane_register_32_out_7, pane_register_32_out_8, pane_register_32_out_9, pane_register_32_out_10,
       pane_register_32_out_11, pane_register_32_out_12, pane_register_32_out_13, pane_register_32_out_14,
       pane_register_32_out_15, pane_register_32_out_16, pane_register_32_out_17, pane_register_32_out_18,
       pane_register_32_out_19, pane_register_32_out_20, pane_register_32_out_21;
  wire [27:4] pane_decoder_1_pane_address_2;

  and and_1 (and_1_out, Write, CLK);
  Address_Translator address_translator_1 (
    .Address(Address), .Offset(16'h4000), .Limit(16'h2000),
    .Translated_Address(address_translator_1_translated_address),
    .Active___1_means_address_in_range(address_translator_1_active___1_means_address_in_range));
  Pane_Decoder pane_decoder_1 (
    .Enable(address_translator_1_active___1_means_address_in_range),
    .Address(address_translator_1_translated_address), .Pane_Local_Address(Local_Address),
    .Pane_Address({pane_decoder_1_pane_address, pane_decoder_1_pane_address_2, pane_decoder_1_pane_address_3}));  // open: Screen_Width
  DotMatrix #(.inputtype("row"), .matrixcols(16), .matrixrows(16)) dotmatrix_1 (
    .row0(pane_register_1_out_6), .row1(pane_register_1_out_7), .row2(pane_register_1_out_8),
    .row3(pane_register_1_out_9), .row4(pane_register_1_out_10), .row5(pane_register_1_out_11),
    .row6(pane_register_1_out_12), .row7(pane_register_1_out_13), .row8(pane_register_1_out_14),
    .row9(pane_register_1_out_15), .row10(pane_register_1_out_16), .row11(pane_register_1_out_17),
    .row12(pane_register_1_out_18), .row13(pane_register_1_out_19), .row14(pane_register_1_out_20),
    .row15(pane_register_1_out_21));
  Pane_Register pane_register_1 (
    .CLK(and_1_out), .Data(Data), .Reset(RESET), .Enable(pane_decoder_1_pane_address[0]),
    .Address(Local_Address), .out_6(pane_register_1_out_6), .out_7(pane_register_1_out_7),
    .out_8(pane_register_1_out_8), .out_9(pane_register_1_out_9), .out_10(pane_register_1_out_10),
    .out_11(pane_register_1_out_11), .out_12(pane_register_1_out_12), .out_13(pane_register_1_out_13),
    .out_14(pane_register_1_out_14), .out_15(pane_register_1_out_15), .out_16(pane_register_1_out_16),
    .out_17(pane_register_1_out_17), .out_18(pane_register_1_out_18), .out_19(pane_register_1_out_19),
    .out_20(pane_register_1_out_20), .out_21(pane_register_1_out_21));
  DotMatrix #(.inputtype("row"), .matrixcols(16), .matrixrows(16)) dotmatrix_2 (
    .row0(pane_register_2_out_6), .row1(pane_register_2_out_7), .row2(pane_register_2_out_8),
    .row3(pane_register_2_out_9), .row4(pane_register_2_out_10), .row5(pane_register_2_out_11),
    .row6(pane_register_2_out_12), .row7(pane_register_2_out_13), .row8(pane_register_2_out_14),
    .row9(pane_register_2_out_15), .row10(pane_register_2_out_16), .row11(pane_register_2_out_17),
    .row12(pane_register_2_out_18), .row13(pane_register_2_out_19), .row14(pane_register_2_out_20),
    .row15(pane_register_2_out_21));
  Pane_Register pane_register_2 (
    .CLK(and_1_out), .Data(Data), .Reset(RESET), .Enable(pane_decoder_1_pane_address[1]),
    .Address(Local_Address), .out_6(pane_register_2_out_6), .out_7(pane_register_2_out_7),
    .out_8(pane_register_2_out_8), .out_9(pane_register_2_out_9), .out_10(pane_register_2_out_10),
    .out_11(pane_register_2_out_11), .out_12(pane_register_2_out_12), .out_13(pane_register_2_out_13),
    .out_14(pane_register_2_out_14), .out_15(pane_register_2_out_15), .out_16(pane_register_2_out_16),
    .out_17(pane_register_2_out_17), .out_18(pane_register_2_out_18), .out_19(pane_register_2_out_19),
    .out_20(pane_register_2_out_20), .out_21(pane_register_2_out_21));
  DotMatrix #(.inputtype("row"), .matrixcols(16), .matrixrows(16)) dotmatrix_3 (
    .row0(pane_register_3_out_6), .row1(pane_register_3_out_7), .row2(pane_register_3_out_8),
    .row3(pane_register_3_out_9), .row4(pane_register_3_out_10), .row5(pane_register_3_out_11),
    .row6(pane_register_3_out_12), .row7(pane_register_3_out_13), .row8(pane_register_3_out_14),
    .row9(pane_register_3_out_15), .row10(pane_register_3_out_16), .row11(pane_register_3_out_17),
    .row12(pane_register_3_out_18), .row13(pane_register_3_out_19), .row14(pane_register_3_out_20),
    .row15(pane_register_3_out_21));
  Pane_Register pane_register_3 (
    .CLK(and_1_out), .Data(Data), .Reset(RESET), .Enable(pane_decoder_1_pane_address[2]),
    .Address(Local_Address), .out_6(pane_register_3_out_6), .out_7(pane_register_3_out_7),
    .out_8(pane_register_3_out_8), .out_9(pane_register_3_out_9), .out_10(pane_register_3_out_10),
    .out_11(pane_register_3_out_11), .out_12(pane_register_3_out_12), .out_13(pane_register_3_out_13),
    .out_14(pane_register_3_out_14), .out_15(pane_register_3_out_15), .out_16(pane_register_3_out_16),
    .out_17(pane_register_3_out_17), .out_18(pane_register_3_out_18), .out_19(pane_register_3_out_19),
    .out_20(pane_register_3_out_20), .out_21(pane_register_3_out_21));
  Pane_Register pane_register_4 (
    .CLK(and_1_out), .Data(Data), .Reset(RESET), .Enable(pane_decoder_1_pane_address[3]),
    .Address(Local_Address), .out_6(pane_register_4_out_6), .out_7(pane_register_4_out_7),
    .out_8(pane_register_4_out_8), .out_9(pane_register_4_out_9), .out_10(pane_register_4_out_10),
    .out_11(pane_register_4_out_11), .out_12(pane_register_4_out_12), .out_13(pane_register_4_out_13),
    .out_14(pane_register_4_out_14), .out_15(pane_register_4_out_15), .out_16(pane_register_4_out_16),
    .out_17(pane_register_4_out_17), .out_18(pane_register_4_out_18), .out_19(pane_register_4_out_19),
    .out_20(pane_register_4_out_20), .out_21(pane_register_4_out_21));
  DotMatrix #(.inputtype("row"), .matrixcols(16), .matrixrows(16)) dotmatrix_4 (
    .row0(pane_register_4_out_6), .row1(pane_register_4_out_7), .row2(pane_register_4_out_8),
    .row3(pane_register_4_out_9), .row4(pane_register_4_out_10), .row5(pane_register_4_out_11),
    .row6(pane_register_4_out_12), .row7(pane_register_4_out_13), .row8(pane_register_4_out_14),
    .row9(pane_register_4_out_15), .row10(pane_register_4_out_16), .row11(pane_register_4_out_17),
    .row12(pane_register_4_out_18), .row13(pane_register_4_out_19), .row14(pane_register_4_out_20),
    .row15(pane_register_4_out_21));
  Pane_Register pane_register_5 (
    .CLK(and_1_out), .Data(Data), .Reset(RESET), .Enable(pane_decoder_1_pane_address_2[24]),
    .Address(Local_Address), .out_6(pane_register_5_out_6), .out_7(pane_register_5_out_7),
    .out_8(pane_register_5_out_8), .out_9(pane_register_5_out_9), .out_10(pane_register_5_out_10),
    .out_11(pane_register_5_out_11), .out_12(pane_register_5_out_12), .out_13(pane_register_5_out_13),
    .out_14(pane_register_5_out_14), .out_15(pane_register_5_out_15), .out_16(pane_register_5_out_16),
    .out_17(pane_register_5_out_17), .out_18(pane_register_5_out_18), .out_19(pane_register_5_out_19),
    .out_20(pane_register_5_out_20), .out_21(pane_register_5_out_21));
  DotMatrix #(.inputtype("row"), .matrixcols(16), .matrixrows(16)) dotmatrix_5 (
    .row0(pane_register_5_out_6), .row1(pane_register_5_out_7), .row2(pane_register_5_out_8),
    .row3(pane_register_5_out_9), .row4(pane_register_5_out_10), .row5(pane_register_5_out_11),
    .row6(pane_register_5_out_12), .row7(pane_register_5_out_13), .row8(pane_register_5_out_14),
    .row9(pane_register_5_out_15), .row10(pane_register_5_out_16), .row11(pane_register_5_out_17),
    .row12(pane_register_5_out_18), .row13(pane_register_5_out_19), .row14(pane_register_5_out_20),
    .row15(pane_register_5_out_21));
  Pane_Register pane_register_6 (
    .CLK(and_1_out), .Data(Data), .Reset(RESET), .Enable(pane_decoder_1_pane_address_2[25]),
    .Address(Local_Address), .out_6(pane_register_6_out_6), .out_7(pane_register_6_out_7),
    .out_8(pane_register_6_out_8), .out_9(pane_register_6_out_9), .out_10(pane_register_6_out_10),
    .out_11(pane_register_6_out_11), .out_12(pane_register_6_out_12), .out_13(pane_register_6_out_13),
    .out_14(pane_register_6_out_14), .out_15(pane_register_6_out_15), .out_16(pane_register_6_out_16),
    .out_17(pane_register_6_out_17), .out_18(pane_register_6_out_18), .out_19(pane_register_6_out_19),
    .out_20(pane_register_6_out_20), .out_21(pane_register_6_out_21));
  DotMatrix #(.inputtype("row"), .matrixcols(16), .matrixrows(16)) dotmatrix_6 (
    .row0(pane_register_6_out_6), .row1(pane_register_6_out_7), .row2(pane_register_6_out_8),
    .row3(pane_register_6_out_9), .row4(pane_register_6_out_10), .row5(pane_register_6_out_11),
    .row6(pane_register_6_out_12), .row7(pane_register_6_out_13), .row8(pane_register_6_out_14),
    .row9(pane_register_6_out_15), .row10(pane_register_6_out_16), .row11(pane_register_6_out_17),
    .row12(pane_register_6_out_18), .row13(pane_register_6_out_19), .row14(pane_register_6_out_20),
    .row15(pane_register_6_out_21));
  DotMatrix #(.inputtype("row"), .matrixcols(16), .matrixrows(16)) dotmatrix_7 (
    .row0(pane_register_7_out_6), .row1(pane_register_7_out_7), .row2(pane_register_7_out_8),
    .row3(pane_register_7_out_9), .row4(pane_register_7_out_10), .row5(pane_register_7_out_11),
    .row6(pane_register_7_out_12), .row7(pane_register_7_out_13), .row8(pane_register_7_out_14),
    .row9(pane_register_7_out_15), .row10(pane_register_7_out_16), .row11(pane_register_7_out_17),
    .row12(pane_register_7_out_18), .row13(pane_register_7_out_19), .row14(pane_register_7_out_20),
    .row15(pane_register_7_out_21));
  Pane_Register pane_register_7 (
    .CLK(and_1_out), .Data(Data), .Reset(RESET), .Enable(pane_decoder_1_pane_address_2[26]),
    .Address(Local_Address), .out_6(pane_register_7_out_6), .out_7(pane_register_7_out_7),
    .out_8(pane_register_7_out_8), .out_9(pane_register_7_out_9), .out_10(pane_register_7_out_10),
    .out_11(pane_register_7_out_11), .out_12(pane_register_7_out_12), .out_13(pane_register_7_out_13),
    .out_14(pane_register_7_out_14), .out_15(pane_register_7_out_15), .out_16(pane_register_7_out_16),
    .out_17(pane_register_7_out_17), .out_18(pane_register_7_out_18), .out_19(pane_register_7_out_19),
    .out_20(pane_register_7_out_20), .out_21(pane_register_7_out_21));
  Pane_Register pane_register_8 (
    .CLK(and_1_out), .Data(Data), .Reset(RESET), .Enable(pane_decoder_1_pane_address_2[27]),
    .Address(Local_Address), .out_6(pane_register_8_out_6), .out_7(pane_register_8_out_7),
    .out_8(pane_register_8_out_8), .out_9(pane_register_8_out_9), .out_10(pane_register_8_out_10),
    .out_11(pane_register_8_out_11), .out_12(pane_register_8_out_12), .out_13(pane_register_8_out_13),
    .out_14(pane_register_8_out_14), .out_15(pane_register_8_out_15), .out_16(pane_register_8_out_16),
    .out_17(pane_register_8_out_17), .out_18(pane_register_8_out_18), .out_19(pane_register_8_out_19),
    .out_20(pane_register_8_out_20), .out_21(pane_register_8_out_21));
  DotMatrix #(.inputtype("row"), .matrixcols(16), .matrixrows(16)) dotmatrix_8 (
    .row0(pane_register_8_out_6), .row1(pane_register_8_out_7), .row2(pane_register_8_out_8),
    .row3(pane_register_8_out_9), .row4(pane_register_8_out_10), .row5(pane_register_8_out_11),
    .row6(pane_register_8_out_12), .row7(pane_register_8_out_13), .row8(pane_register_8_out_14),
    .row9(pane_register_8_out_15), .row10(pane_register_8_out_16), .row11(pane_register_8_out_17),
    .row12(pane_register_8_out_18), .row13(pane_register_8_out_19), .row14(pane_register_8_out_20),
    .row15(pane_register_8_out_21));
  Pane_Register pane_register_9 (
    .CLK(and_1_out), .Data(Data), .Reset(RESET), .Enable(pane_decoder_1_pane_address_2[20]),
    .Address(Local_Address), .out_6(pane_register_9_out_6), .out_7(pane_register_9_out_7),
    .out_8(pane_register_9_out_8), .out_9(pane_register_9_out_9), .out_10(pane_register_9_out_10),
    .out_11(pane_register_9_out_11), .out_12(pane_register_9_out_12), .out_13(pane_register_9_out_13),
    .out_14(pane_register_9_out_14), .out_15(pane_register_9_out_15), .out_16(pane_register_9_out_16),
    .out_17(pane_register_9_out_17), .out_18(pane_register_9_out_18), .out_19(pane_register_9_out_19),
    .out_20(pane_register_9_out_20), .out_21(pane_register_9_out_21));
  DotMatrix #(.inputtype("row"), .matrixcols(16), .matrixrows(16)) dotmatrix_9 (
    .row0(pane_register_9_out_6), .row1(pane_register_9_out_7), .row2(pane_register_9_out_8),
    .row3(pane_register_9_out_9), .row4(pane_register_9_out_10), .row5(pane_register_9_out_11),
    .row6(pane_register_9_out_12), .row7(pane_register_9_out_13), .row8(pane_register_9_out_14),
    .row9(pane_register_9_out_15), .row10(pane_register_9_out_16), .row11(pane_register_9_out_17),
    .row12(pane_register_9_out_18), .row13(pane_register_9_out_19), .row14(pane_register_9_out_20),
    .row15(pane_register_9_out_21));
  DotMatrix #(.inputtype("row"), .matrixcols(16), .matrixrows(16)) dotmatrix_10 (
    .row0(pane_register_10_out_6), .row1(pane_register_10_out_7), .row2(pane_register_10_out_8),
    .row3(pane_register_10_out_9), .row4(pane_register_10_out_10), .row5(pane_register_10_out_11),
    .row6(pane_register_10_out_12), .row7(pane_register_10_out_13), .row8(pane_register_10_out_14),
    .row9(pane_register_10_out_15), .row10(pane_register_10_out_16), .row11(pane_register_10_out_17),
    .row12(pane_register_10_out_18), .row13(pane_register_10_out_19), .row14(pane_register_10_out_20),
    .row15(pane_register_10_out_21));
  Pane_Register pane_register_10 (
    .CLK(and_1_out), .Data(Data), .Reset(RESET), .Enable(pane_decoder_1_pane_address_2[21]),
    .Address(Local_Address), .out_6(pane_register_10_out_6), .out_7(pane_register_10_out_7),
    .out_8(pane_register_10_out_8), .out_9(pane_register_10_out_9), .out_10(pane_register_10_out_10),
    .out_11(pane_register_10_out_11), .out_12(pane_register_10_out_12), .out_13(pane_register_10_out_13),
    .out_14(pane_register_10_out_14), .out_15(pane_register_10_out_15), .out_16(pane_register_10_out_16),
    .out_17(pane_register_10_out_17), .out_18(pane_register_10_out_18), .out_19(pane_register_10_out_19),
    .out_20(pane_register_10_out_20), .out_21(pane_register_10_out_21));
  DotMatrix #(.inputtype("row"), .matrixcols(16), .matrixrows(16)) dotmatrix_11 (
    .row0(pane_register_11_out_6), .row1(pane_register_11_out_7), .row2(pane_register_11_out_8),
    .row3(pane_register_11_out_9), .row4(pane_register_11_out_10), .row5(pane_register_11_out_11),
    .row6(pane_register_11_out_12), .row7(pane_register_11_out_13), .row8(pane_register_11_out_14),
    .row9(pane_register_11_out_15), .row10(pane_register_11_out_16), .row11(pane_register_11_out_17),
    .row12(pane_register_11_out_18), .row13(pane_register_11_out_19), .row14(pane_register_11_out_20),
    .row15(pane_register_11_out_21));
  Pane_Register pane_register_11 (
    .CLK(and_1_out), .Data(Data), .Reset(RESET), .Enable(pane_decoder_1_pane_address_2[22]),
    .Address(Local_Address), .out_6(pane_register_11_out_6), .out_7(pane_register_11_out_7),
    .out_8(pane_register_11_out_8), .out_9(pane_register_11_out_9), .out_10(pane_register_11_out_10),
    .out_11(pane_register_11_out_11), .out_12(pane_register_11_out_12), .out_13(pane_register_11_out_13),
    .out_14(pane_register_11_out_14), .out_15(pane_register_11_out_15), .out_16(pane_register_11_out_16),
    .out_17(pane_register_11_out_17), .out_18(pane_register_11_out_18), .out_19(pane_register_11_out_19),
    .out_20(pane_register_11_out_20), .out_21(pane_register_11_out_21));
  Pane_Register pane_register_12 (
    .CLK(and_1_out), .Data(Data), .Reset(RESET), .Enable(pane_decoder_1_pane_address_2[23]),
    .Address(Local_Address), .out_6(pane_register_12_out_6), .out_7(pane_register_12_out_7),
    .out_8(pane_register_12_out_8), .out_9(pane_register_12_out_9), .out_10(pane_register_12_out_10),
    .out_11(pane_register_12_out_11), .out_12(pane_register_12_out_12), .out_13(pane_register_12_out_13),
    .out_14(pane_register_12_out_14), .out_15(pane_register_12_out_15), .out_16(pane_register_12_out_16),
    .out_17(pane_register_12_out_17), .out_18(pane_register_12_out_18), .out_19(pane_register_12_out_19),
    .out_20(pane_register_12_out_20), .out_21(pane_register_12_out_21));
  DotMatrix #(.inputtype("row"), .matrixcols(16), .matrixrows(16)) dotmatrix_12 (
    .row0(pane_register_12_out_6), .row1(pane_register_12_out_7), .row2(pane_register_12_out_8),
    .row3(pane_register_12_out_9), .row4(pane_register_12_out_10), .row5(pane_register_12_out_11),
    .row6(pane_register_12_out_12), .row7(pane_register_12_out_13), .row8(pane_register_12_out_14),
    .row9(pane_register_12_out_15), .row10(pane_register_12_out_16), .row11(pane_register_12_out_17),
    .row12(pane_register_12_out_18), .row13(pane_register_12_out_19), .row14(pane_register_12_out_20),
    .row15(pane_register_12_out_21));
  Pane_Register pane_register_13 (
    .CLK(and_1_out), .Data(Data), .Reset(RESET), .Enable(pane_decoder_1_pane_address_2[16]),
    .Address(Local_Address), .out_6(pane_register_13_out_6), .out_7(pane_register_13_out_7),
    .out_8(pane_register_13_out_8), .out_9(pane_register_13_out_9), .out_10(pane_register_13_out_10),
    .out_11(pane_register_13_out_11), .out_12(pane_register_13_out_12), .out_13(pane_register_13_out_13),
    .out_14(pane_register_13_out_14), .out_15(pane_register_13_out_15), .out_16(pane_register_13_out_16),
    .out_17(pane_register_13_out_17), .out_18(pane_register_13_out_18), .out_19(pane_register_13_out_19),
    .out_20(pane_register_13_out_20), .out_21(pane_register_13_out_21));
  DotMatrix #(.inputtype("row"), .matrixcols(16), .matrixrows(16)) dotmatrix_13 (
    .row0(pane_register_13_out_6), .row1(pane_register_13_out_7), .row2(pane_register_13_out_8),
    .row3(pane_register_13_out_9), .row4(pane_register_13_out_10), .row5(pane_register_13_out_11),
    .row6(pane_register_13_out_12), .row7(pane_register_13_out_13), .row8(pane_register_13_out_14),
    .row9(pane_register_13_out_15), .row10(pane_register_13_out_16), .row11(pane_register_13_out_17),
    .row12(pane_register_13_out_18), .row13(pane_register_13_out_19), .row14(pane_register_13_out_20),
    .row15(pane_register_13_out_21));
  Pane_Register pane_register_14 (
    .CLK(and_1_out), .Data(Data), .Reset(RESET), .Enable(pane_decoder_1_pane_address_2[17]),
    .Address(Local_Address), .out_6(pane_register_14_out_6), .out_7(pane_register_14_out_7),
    .out_8(pane_register_14_out_8), .out_9(pane_register_14_out_9), .out_10(pane_register_14_out_10),
    .out_11(pane_register_14_out_11), .out_12(pane_register_14_out_12), .out_13(pane_register_14_out_13),
    .out_14(pane_register_14_out_14), .out_15(pane_register_14_out_15), .out_16(pane_register_14_out_16),
    .out_17(pane_register_14_out_17), .out_18(pane_register_14_out_18), .out_19(pane_register_14_out_19),
    .out_20(pane_register_14_out_20), .out_21(pane_register_14_out_21));
  DotMatrix #(.inputtype("row"), .matrixcols(16), .matrixrows(16)) dotmatrix_14 (
    .row0(pane_register_14_out_6), .row1(pane_register_14_out_7), .row2(pane_register_14_out_8),
    .row3(pane_register_14_out_9), .row4(pane_register_14_out_10), .row5(pane_register_14_out_11),
    .row6(pane_register_14_out_12), .row7(pane_register_14_out_13), .row8(pane_register_14_out_14),
    .row9(pane_register_14_out_15), .row10(pane_register_14_out_16), .row11(pane_register_14_out_17),
    .row12(pane_register_14_out_18), .row13(pane_register_14_out_19), .row14(pane_register_14_out_20),
    .row15(pane_register_14_out_21));
  Pane_Register pane_register_15 (
    .CLK(and_1_out), .Data(Data), .Reset(RESET), .Enable(pane_decoder_1_pane_address_2[18]),
    .Address(Local_Address), .out_6(pane_register_15_out_6), .out_7(pane_register_15_out_7),
    .out_8(pane_register_15_out_8), .out_9(pane_register_15_out_9), .out_10(pane_register_15_out_10),
    .out_11(pane_register_15_out_11), .out_12(pane_register_15_out_12), .out_13(pane_register_15_out_13),
    .out_14(pane_register_15_out_14), .out_15(pane_register_15_out_15), .out_16(pane_register_15_out_16),
    .out_17(pane_register_15_out_17), .out_18(pane_register_15_out_18), .out_19(pane_register_15_out_19),
    .out_20(pane_register_15_out_20), .out_21(pane_register_15_out_21));
  DotMatrix #(.inputtype("row"), .matrixcols(16), .matrixrows(16)) dotmatrix_15 (
    .row0(pane_register_15_out_6), .row1(pane_register_15_out_7), .row2(pane_register_15_out_8),
    .row3(pane_register_15_out_9), .row4(pane_register_15_out_10), .row5(pane_register_15_out_11),
    .row6(pane_register_15_out_12), .row7(pane_register_15_out_13), .row8(pane_register_15_out_14),
    .row9(pane_register_15_out_15), .row10(pane_register_15_out_16), .row11(pane_register_15_out_17),
    .row12(pane_register_15_out_18), .row13(pane_register_15_out_19), .row14(pane_register_15_out_20),
    .row15(pane_register_15_out_21));
  Pane_Register pane_register_16 (
    .CLK(and_1_out), .Data(Data), .Reset(RESET), .Enable(pane_decoder_1_pane_address_2[19]),
    .Address(Local_Address), .out_6(pane_register_16_out_6), .out_7(pane_register_16_out_7),
    .out_8(pane_register_16_out_8), .out_9(pane_register_16_out_9), .out_10(pane_register_16_out_10),
    .out_11(pane_register_16_out_11), .out_12(pane_register_16_out_12), .out_13(pane_register_16_out_13),
    .out_14(pane_register_16_out_14), .out_15(pane_register_16_out_15), .out_16(pane_register_16_out_16),
    .out_17(pane_register_16_out_17), .out_18(pane_register_16_out_18), .out_19(pane_register_16_out_19),
    .out_20(pane_register_16_out_20), .out_21(pane_register_16_out_21));
  DotMatrix #(.inputtype("row"), .matrixcols(16), .matrixrows(16)) dotmatrix_16 (
    .row0(pane_register_16_out_6), .row1(pane_register_16_out_7), .row2(pane_register_16_out_8),
    .row3(pane_register_16_out_9), .row4(pane_register_16_out_10), .row5(pane_register_16_out_11),
    .row6(pane_register_16_out_12), .row7(pane_register_16_out_13), .row8(pane_register_16_out_14),
    .row9(pane_register_16_out_15), .row10(pane_register_16_out_16), .row11(pane_register_16_out_17),
    .row12(pane_register_16_out_18), .row13(pane_register_16_out_19), .row14(pane_register_16_out_20),
    .row15(pane_register_16_out_21));
  DotMatrix #(.inputtype("row"), .matrixcols(16), .matrixrows(16)) dotmatrix_17 (
    .row0(pane_register_17_out_6), .row1(pane_register_17_out_7), .row2(pane_register_17_out_8),
    .row3(pane_register_17_out_9), .row4(pane_register_17_out_10), .row5(pane_register_17_out_11),
    .row6(pane_register_17_out_12), .row7(pane_register_17_out_13), .row8(pane_register_17_out_14),
    .row9(pane_register_17_out_15), .row10(pane_register_17_out_16), .row11(pane_register_17_out_17),
    .row12(pane_register_17_out_18), .row13(pane_register_17_out_19), .row14(pane_register_17_out_20),
    .row15(pane_register_17_out_21));
  Pane_Register pane_register_17 (
    .CLK(and_1_out), .Data(Data), .Reset(RESET), .Enable(pane_decoder_1_pane_address_2[12]),
    .Address(Local_Address), .out_6(pane_register_17_out_6), .out_7(pane_register_17_out_7),
    .out_8(pane_register_17_out_8), .out_9(pane_register_17_out_9), .out_10(pane_register_17_out_10),
    .out_11(pane_register_17_out_11), .out_12(pane_register_17_out_12), .out_13(pane_register_17_out_13),
    .out_14(pane_register_17_out_14), .out_15(pane_register_17_out_15), .out_16(pane_register_17_out_16),
    .out_17(pane_register_17_out_17), .out_18(pane_register_17_out_18), .out_19(pane_register_17_out_19),
    .out_20(pane_register_17_out_20), .out_21(pane_register_17_out_21));
  DotMatrix #(.inputtype("row"), .matrixcols(16), .matrixrows(16)) dotmatrix_18 (
    .row0(pane_register_18_out_6), .row1(pane_register_18_out_7), .row2(pane_register_18_out_8),
    .row3(pane_register_18_out_9), .row4(pane_register_18_out_10), .row5(pane_register_18_out_11),
    .row6(pane_register_18_out_12), .row7(pane_register_18_out_13), .row8(pane_register_18_out_14),
    .row9(pane_register_18_out_15), .row10(pane_register_18_out_16), .row11(pane_register_18_out_17),
    .row12(pane_register_18_out_18), .row13(pane_register_18_out_19), .row14(pane_register_18_out_20),
    .row15(pane_register_18_out_21));
  Pane_Register pane_register_18 (
    .CLK(and_1_out), .Data(Data), .Reset(RESET), .Enable(pane_decoder_1_pane_address_2[13]),
    .Address(Local_Address), .out_6(pane_register_18_out_6), .out_7(pane_register_18_out_7),
    .out_8(pane_register_18_out_8), .out_9(pane_register_18_out_9), .out_10(pane_register_18_out_10),
    .out_11(pane_register_18_out_11), .out_12(pane_register_18_out_12), .out_13(pane_register_18_out_13),
    .out_14(pane_register_18_out_14), .out_15(pane_register_18_out_15), .out_16(pane_register_18_out_16),
    .out_17(pane_register_18_out_17), .out_18(pane_register_18_out_18), .out_19(pane_register_18_out_19),
    .out_20(pane_register_18_out_20), .out_21(pane_register_18_out_21));
  DotMatrix #(.inputtype("row"), .matrixcols(16), .matrixrows(16)) dotmatrix_19 (
    .row0(pane_register_19_out_6), .row1(pane_register_19_out_7), .row2(pane_register_19_out_8),
    .row3(pane_register_19_out_9), .row4(pane_register_19_out_10), .row5(pane_register_19_out_11),
    .row6(pane_register_19_out_12), .row7(pane_register_19_out_13), .row8(pane_register_19_out_14),
    .row9(pane_register_19_out_15), .row10(pane_register_19_out_16), .row11(pane_register_19_out_17),
    .row12(pane_register_19_out_18), .row13(pane_register_19_out_19), .row14(pane_register_19_out_20),
    .row15(pane_register_19_out_21));
  Pane_Register pane_register_19 (
    .CLK(and_1_out), .Data(Data), .Reset(RESET), .Enable(pane_decoder_1_pane_address_2[14]),
    .Address(Local_Address), .out_6(pane_register_19_out_6), .out_7(pane_register_19_out_7),
    .out_8(pane_register_19_out_8), .out_9(pane_register_19_out_9), .out_10(pane_register_19_out_10),
    .out_11(pane_register_19_out_11), .out_12(pane_register_19_out_12), .out_13(pane_register_19_out_13),
    .out_14(pane_register_19_out_14), .out_15(pane_register_19_out_15), .out_16(pane_register_19_out_16),
    .out_17(pane_register_19_out_17), .out_18(pane_register_19_out_18), .out_19(pane_register_19_out_19),
    .out_20(pane_register_19_out_20), .out_21(pane_register_19_out_21));
  Pane_Register pane_register_20 (
    .CLK(and_1_out), .Data(Data), .Reset(RESET), .Enable(pane_decoder_1_pane_address_2[15]),
    .Address(Local_Address), .out_6(pane_register_20_out_6), .out_7(pane_register_20_out_7),
    .out_8(pane_register_20_out_8), .out_9(pane_register_20_out_9), .out_10(pane_register_20_out_10),
    .out_11(pane_register_20_out_11), .out_12(pane_register_20_out_12), .out_13(pane_register_20_out_13),
    .out_14(pane_register_20_out_14), .out_15(pane_register_20_out_15), .out_16(pane_register_20_out_16),
    .out_17(pane_register_20_out_17), .out_18(pane_register_20_out_18), .out_19(pane_register_20_out_19),
    .out_20(pane_register_20_out_20), .out_21(pane_register_20_out_21));
  DotMatrix #(.inputtype("row"), .matrixcols(16), .matrixrows(16)) dotmatrix_20 (
    .row0(pane_register_20_out_6), .row1(pane_register_20_out_7), .row2(pane_register_20_out_8),
    .row3(pane_register_20_out_9), .row4(pane_register_20_out_10), .row5(pane_register_20_out_11),
    .row6(pane_register_20_out_12), .row7(pane_register_20_out_13), .row8(pane_register_20_out_14),
    .row9(pane_register_20_out_15), .row10(pane_register_20_out_16), .row11(pane_register_20_out_17),
    .row12(pane_register_20_out_18), .row13(pane_register_20_out_19), .row14(pane_register_20_out_20),
    .row15(pane_register_20_out_21));
  Pane_Register pane_register_21 (
    .CLK(and_1_out), .Data(Data), .Reset(RESET), .Enable(pane_decoder_1_pane_address_2[8]),
    .Address(Local_Address), .out_6(pane_register_21_out_6), .out_7(pane_register_21_out_7),
    .out_8(pane_register_21_out_8), .out_9(pane_register_21_out_9), .out_10(pane_register_21_out_10),
    .out_11(pane_register_21_out_11), .out_12(pane_register_21_out_12), .out_13(pane_register_21_out_13),
    .out_14(pane_register_21_out_14), .out_15(pane_register_21_out_15), .out_16(pane_register_21_out_16),
    .out_17(pane_register_21_out_17), .out_18(pane_register_21_out_18), .out_19(pane_register_21_out_19),
    .out_20(pane_register_21_out_20), .out_21(pane_register_21_out_21));
  DotMatrix #(.inputtype("row"), .matrixcols(16), .matrixrows(16)) dotmatrix_21 (
    .row0(pane_register_21_out_6), .row1(pane_register_21_out_7), .row2(pane_register_21_out_8),
    .row3(pane_register_21_out_9), .row4(pane_register_21_out_10), .row5(pane_register_21_out_11),
    .row6(pane_register_21_out_12), .row7(pane_register_21_out_13), .row8(pane_register_21_out_14),
    .row9(pane_register_21_out_15), .row10(pane_register_21_out_16), .row11(pane_register_21_out_17),
    .row12(pane_register_21_out_18), .row13(pane_register_21_out_19), .row14(pane_register_21_out_20),
    .row15(pane_register_21_out_21));
  DotMatrix #(.inputtype("row"), .matrixcols(16), .matrixrows(16)) dotmatrix_22 (
    .row0(pane_register_22_out_6), .row1(pane_register_22_out_7), .row2(pane_register_22_out_8),
    .row3(pane_register_22_out_9), .row4(pane_register_22_out_10), .row5(pane_register_22_out_11),
    .row6(pane_register_22_out_12), .row7(pane_register_22_out_13), .row8(pane_register_22_out_14),
    .row9(pane_register_22_out_15), .row10(pane_register_22_out_16), .row11(pane_register_22_out_17),
    .row12(pane_register_22_out_18), .row13(pane_register_22_out_19), .row14(pane_register_22_out_20),
    .row15(pane_register_22_out_21));
  Pane_Register pane_register_22 (
    .CLK(and_1_out), .Data(Data), .Reset(RESET), .Enable(pane_decoder_1_pane_address_2[9]),
    .Address(Local_Address), .out_6(pane_register_22_out_6), .out_7(pane_register_22_out_7),
    .out_8(pane_register_22_out_8), .out_9(pane_register_22_out_9), .out_10(pane_register_22_out_10),
    .out_11(pane_register_22_out_11), .out_12(pane_register_22_out_12), .out_13(pane_register_22_out_13),
    .out_14(pane_register_22_out_14), .out_15(pane_register_22_out_15), .out_16(pane_register_22_out_16),
    .out_17(pane_register_22_out_17), .out_18(pane_register_22_out_18), .out_19(pane_register_22_out_19),
    .out_20(pane_register_22_out_20), .out_21(pane_register_22_out_21));
  DotMatrix #(.inputtype("row"), .matrixcols(16), .matrixrows(16)) dotmatrix_23 (
    .row0(pane_register_23_out_6), .row1(pane_register_23_out_7), .row2(pane_register_23_out_8),
    .row3(pane_register_23_out_9), .row4(pane_register_23_out_10), .row5(pane_register_23_out_11),
    .row6(pane_register_23_out_12), .row7(pane_register_23_out_13), .row8(pane_register_23_out_14),
    .row9(pane_register_23_out_15), .row10(pane_register_23_out_16), .row11(pane_register_23_out_17),
    .row12(pane_register_23_out_18), .row13(pane_register_23_out_19), .row14(pane_register_23_out_20),
    .row15(pane_register_23_out_21));
  Pane_Register pane_register_23 (
    .CLK(and_1_out), .Data(Data), .Reset(RESET), .Enable(pane_decoder_1_pane_address_2[10]),
    .Address(Local_Address), .out_6(pane_register_23_out_6), .out_7(pane_register_23_out_7),
    .out_8(pane_register_23_out_8), .out_9(pane_register_23_out_9), .out_10(pane_register_23_out_10),
    .out_11(pane_register_23_out_11), .out_12(pane_register_23_out_12), .out_13(pane_register_23_out_13),
    .out_14(pane_register_23_out_14), .out_15(pane_register_23_out_15), .out_16(pane_register_23_out_16),
    .out_17(pane_register_23_out_17), .out_18(pane_register_23_out_18), .out_19(pane_register_23_out_19),
    .out_20(pane_register_23_out_20), .out_21(pane_register_23_out_21));
  DotMatrix #(.inputtype("row"), .matrixcols(16), .matrixrows(16)) dotmatrix_24 (
    .row0(pane_register_24_out_6), .row1(pane_register_24_out_7), .row2(pane_register_24_out_8),
    .row3(pane_register_24_out_9), .row4(pane_register_24_out_10), .row5(pane_register_24_out_11),
    .row6(pane_register_24_out_12), .row7(pane_register_24_out_13), .row8(pane_register_24_out_14),
    .row9(pane_register_24_out_15), .row10(pane_register_24_out_16), .row11(pane_register_24_out_17),
    .row12(pane_register_24_out_18), .row13(pane_register_24_out_19), .row14(pane_register_24_out_20),
    .row15(pane_register_24_out_21));
  Pane_Register pane_register_24 (
    .CLK(and_1_out), .Data(Data), .Reset(RESET), .Enable(pane_decoder_1_pane_address_2[11]),
    .Address(Local_Address), .out_6(pane_register_24_out_6), .out_7(pane_register_24_out_7),
    .out_8(pane_register_24_out_8), .out_9(pane_register_24_out_9), .out_10(pane_register_24_out_10),
    .out_11(pane_register_24_out_11), .out_12(pane_register_24_out_12), .out_13(pane_register_24_out_13),
    .out_14(pane_register_24_out_14), .out_15(pane_register_24_out_15), .out_16(pane_register_24_out_16),
    .out_17(pane_register_24_out_17), .out_18(pane_register_24_out_18), .out_19(pane_register_24_out_19),
    .out_20(pane_register_24_out_20), .out_21(pane_register_24_out_21));
  DotMatrix #(.inputtype("row"), .matrixcols(16), .matrixrows(16)) dotmatrix_25 (
    .row0(pane_register_25_out_6), .row1(pane_register_25_out_7), .row2(pane_register_25_out_8),
    .row3(pane_register_25_out_9), .row4(pane_register_25_out_10), .row5(pane_register_25_out_11),
    .row6(pane_register_25_out_12), .row7(pane_register_25_out_13), .row8(pane_register_25_out_14),
    .row9(pane_register_25_out_15), .row10(pane_register_25_out_16), .row11(pane_register_25_out_17),
    .row12(pane_register_25_out_18), .row13(pane_register_25_out_19), .row14(pane_register_25_out_20),
    .row15(pane_register_25_out_21));
  Pane_Register pane_register_25 (
    .CLK(and_1_out), .Data(Data), .Reset(RESET), .Enable(pane_decoder_1_pane_address_2[4]),
    .Address(Local_Address), .out_6(pane_register_25_out_6), .out_7(pane_register_25_out_7),
    .out_8(pane_register_25_out_8), .out_9(pane_register_25_out_9), .out_10(pane_register_25_out_10),
    .out_11(pane_register_25_out_11), .out_12(pane_register_25_out_12), .out_13(pane_register_25_out_13),
    .out_14(pane_register_25_out_14), .out_15(pane_register_25_out_15), .out_16(pane_register_25_out_16),
    .out_17(pane_register_25_out_17), .out_18(pane_register_25_out_18), .out_19(pane_register_25_out_19),
    .out_20(pane_register_25_out_20), .out_21(pane_register_25_out_21));
  DotMatrix #(.inputtype("row"), .matrixcols(16), .matrixrows(16)) dotmatrix_26 (
    .row0(pane_register_26_out_6), .row1(pane_register_26_out_7), .row2(pane_register_26_out_8),
    .row3(pane_register_26_out_9), .row4(pane_register_26_out_10), .row5(pane_register_26_out_11),
    .row6(pane_register_26_out_12), .row7(pane_register_26_out_13), .row8(pane_register_26_out_14),
    .row9(pane_register_26_out_15), .row10(pane_register_26_out_16), .row11(pane_register_26_out_17),
    .row12(pane_register_26_out_18), .row13(pane_register_26_out_19), .row14(pane_register_26_out_20),
    .row15(pane_register_26_out_21));
  Pane_Register pane_register_26 (
    .CLK(and_1_out), .Data(Data), .Reset(RESET), .Enable(pane_decoder_1_pane_address_2[5]),
    .Address(Local_Address), .out_6(pane_register_26_out_6), .out_7(pane_register_26_out_7),
    .out_8(pane_register_26_out_8), .out_9(pane_register_26_out_9), .out_10(pane_register_26_out_10),
    .out_11(pane_register_26_out_11), .out_12(pane_register_26_out_12), .out_13(pane_register_26_out_13),
    .out_14(pane_register_26_out_14), .out_15(pane_register_26_out_15), .out_16(pane_register_26_out_16),
    .out_17(pane_register_26_out_17), .out_18(pane_register_26_out_18), .out_19(pane_register_26_out_19),
    .out_20(pane_register_26_out_20), .out_21(pane_register_26_out_21));
  Pane_Register pane_register_27 (
    .CLK(and_1_out), .Data(Data), .Reset(RESET), .Enable(pane_decoder_1_pane_address_2[6]),
    .Address(Local_Address), .out_6(pane_register_27_out_6), .out_7(pane_register_27_out_7),
    .out_8(pane_register_27_out_8), .out_9(pane_register_27_out_9), .out_10(pane_register_27_out_10),
    .out_11(pane_register_27_out_11), .out_12(pane_register_27_out_12), .out_13(pane_register_27_out_13),
    .out_14(pane_register_27_out_14), .out_15(pane_register_27_out_15), .out_16(pane_register_27_out_16),
    .out_17(pane_register_27_out_17), .out_18(pane_register_27_out_18), .out_19(pane_register_27_out_19),
    .out_20(pane_register_27_out_20), .out_21(pane_register_27_out_21));
  DotMatrix #(.inputtype("row"), .matrixcols(16), .matrixrows(16)) dotmatrix_27 (
    .row0(pane_register_27_out_6), .row1(pane_register_27_out_7), .row2(pane_register_27_out_8),
    .row3(pane_register_27_out_9), .row4(pane_register_27_out_10), .row5(pane_register_27_out_11),
    .row6(pane_register_27_out_12), .row7(pane_register_27_out_13), .row8(pane_register_27_out_14),
    .row9(pane_register_27_out_15), .row10(pane_register_27_out_16), .row11(pane_register_27_out_17),
    .row12(pane_register_27_out_18), .row13(pane_register_27_out_19), .row14(pane_register_27_out_20),
    .row15(pane_register_27_out_21));
  DotMatrix #(.inputtype("row"), .matrixcols(16), .matrixrows(16)) dotmatrix_28 (
    .row0(pane_register_28_out_6), .row1(pane_register_28_out_7), .row2(pane_register_28_out_8),
    .row3(pane_register_28_out_9), .row4(pane_register_28_out_10), .row5(pane_register_28_out_11),
    .row6(pane_register_28_out_12), .row7(pane_register_28_out_13), .row8(pane_register_28_out_14),
    .row9(pane_register_28_out_15), .row10(pane_register_28_out_16), .row11(pane_register_28_out_17),
    .row12(pane_register_28_out_18), .row13(pane_register_28_out_19), .row14(pane_register_28_out_20),
    .row15(pane_register_28_out_21));
  Pane_Register pane_register_28 (
    .CLK(and_1_out), .Data(Data), .Reset(RESET), .Enable(pane_decoder_1_pane_address_2[7]),
    .Address(Local_Address), .out_6(pane_register_28_out_6), .out_7(pane_register_28_out_7),
    .out_8(pane_register_28_out_8), .out_9(pane_register_28_out_9), .out_10(pane_register_28_out_10),
    .out_11(pane_register_28_out_11), .out_12(pane_register_28_out_12), .out_13(pane_register_28_out_13),
    .out_14(pane_register_28_out_14), .out_15(pane_register_28_out_15), .out_16(pane_register_28_out_16),
    .out_17(pane_register_28_out_17), .out_18(pane_register_28_out_18), .out_19(pane_register_28_out_19),
    .out_20(pane_register_28_out_20), .out_21(pane_register_28_out_21));
  Pane_Register pane_register_29 (
    .CLK(and_1_out), .Data(Data), .Reset(RESET), .Enable(pane_decoder_1_pane_address_3[0]),
    .Address(Local_Address), .out_6(pane_register_29_out_6), .out_7(pane_register_29_out_7),
    .out_8(pane_register_29_out_8), .out_9(pane_register_29_out_9), .out_10(pane_register_29_out_10),
    .out_11(pane_register_29_out_11), .out_12(pane_register_29_out_12), .out_13(pane_register_29_out_13),
    .out_14(pane_register_29_out_14), .out_15(pane_register_29_out_15), .out_16(pane_register_29_out_16),
    .out_17(pane_register_29_out_17), .out_18(pane_register_29_out_18), .out_19(pane_register_29_out_19),
    .out_20(pane_register_29_out_20), .out_21(pane_register_29_out_21));
  DotMatrix #(.inputtype("row"), .matrixcols(16), .matrixrows(16)) dotmatrix_29 (
    .row0(pane_register_29_out_6), .row1(pane_register_29_out_7), .row2(pane_register_29_out_8),
    .row3(pane_register_29_out_9), .row4(pane_register_29_out_10), .row5(pane_register_29_out_11),
    .row6(pane_register_29_out_12), .row7(pane_register_29_out_13), .row8(pane_register_29_out_14),
    .row9(pane_register_29_out_15), .row10(pane_register_29_out_16), .row11(pane_register_29_out_17),
    .row12(pane_register_29_out_18), .row13(pane_register_29_out_19), .row14(pane_register_29_out_20),
    .row15(pane_register_29_out_21));
  Pane_Register pane_register_30 (
    .CLK(and_1_out), .Data(Data), .Reset(RESET), .Enable(pane_decoder_1_pane_address_3[1]),
    .Address(Local_Address), .out_6(pane_register_30_out_6), .out_7(pane_register_30_out_7),
    .out_8(pane_register_30_out_8), .out_9(pane_register_30_out_9), .out_10(pane_register_30_out_10),
    .out_11(pane_register_30_out_11), .out_12(pane_register_30_out_12), .out_13(pane_register_30_out_13),
    .out_14(pane_register_30_out_14), .out_15(pane_register_30_out_15), .out_16(pane_register_30_out_16),
    .out_17(pane_register_30_out_17), .out_18(pane_register_30_out_18), .out_19(pane_register_30_out_19),
    .out_20(pane_register_30_out_20), .out_21(pane_register_30_out_21));
  DotMatrix #(.inputtype("row"), .matrixcols(16), .matrixrows(16)) dotmatrix_30 (
    .row0(pane_register_30_out_6), .row1(pane_register_30_out_7), .row2(pane_register_30_out_8),
    .row3(pane_register_30_out_9), .row4(pane_register_30_out_10), .row5(pane_register_30_out_11),
    .row6(pane_register_30_out_12), .row7(pane_register_30_out_13), .row8(pane_register_30_out_14),
    .row9(pane_register_30_out_15), .row10(pane_register_30_out_16), .row11(pane_register_30_out_17),
    .row12(pane_register_30_out_18), .row13(pane_register_30_out_19), .row14(pane_register_30_out_20),
    .row15(pane_register_30_out_21));
  Pane_Register pane_register_31 (
    .CLK(and_1_out), .Data(Data), .Reset(RESET), .Enable(pane_decoder_1_pane_address_3[2]),
    .Address(Local_Address), .out_6(pane_register_31_out_6), .out_7(pane_register_31_out_7),
    .out_8(pane_register_31_out_8), .out_9(pane_register_31_out_9), .out_10(pane_register_31_out_10),
    .out_11(pane_register_31_out_11), .out_12(pane_register_31_out_12), .out_13(pane_register_31_out_13),
    .out_14(pane_register_31_out_14), .out_15(pane_register_31_out_15), .out_16(pane_register_31_out_16),
    .out_17(pane_register_31_out_17), .out_18(pane_register_31_out_18), .out_19(pane_register_31_out_19),
    .out_20(pane_register_31_out_20), .out_21(pane_register_31_out_21));
  DotMatrix #(.inputtype("row"), .matrixcols(16), .matrixrows(16)) dotmatrix_31 (
    .row0(pane_register_31_out_6), .row1(pane_register_31_out_7), .row2(pane_register_31_out_8),
    .row3(pane_register_31_out_9), .row4(pane_register_31_out_10), .row5(pane_register_31_out_11),
    .row6(pane_register_31_out_12), .row7(pane_register_31_out_13), .row8(pane_register_31_out_14),
    .row9(pane_register_31_out_15), .row10(pane_register_31_out_16), .row11(pane_register_31_out_17),
    .row12(pane_register_31_out_18), .row13(pane_register_31_out_19), .row14(pane_register_31_out_20),
    .row15(pane_register_31_out_21));
  DotMatrix #(.inputtype("row"), .matrixcols(16), .matrixrows(16)) dotmatrix_32 (
    .row0(pane_register_32_out_6), .row1(pane_register_32_out_7), .row2(pane_register_32_out_8),
    .row3(pane_register_32_out_9), .row4(pane_register_32_out_10), .row5(pane_register_32_out_11),
    .row6(pane_register_32_out_12), .row7(pane_register_32_out_13), .row8(pane_register_32_out_14),
    .row9(pane_register_32_out_15), .row10(pane_register_32_out_16), .row11(pane_register_32_out_17),
    .row12(pane_register_32_out_18), .row13(pane_register_32_out_19), .row14(pane_register_32_out_20),
    .row15(pane_register_32_out_21));
  Pane_Register pane_register_32 (
    .CLK(and_1_out), .Data(Data), .Reset(RESET), .Enable(pane_decoder_1_pane_address_3[3]),
    .Address(Local_Address), .out_6(pane_register_32_out_6), .out_7(pane_register_32_out_7),
    .out_8(pane_register_32_out_8), .out_9(pane_register_32_out_9), .out_10(pane_register_32_out_10),
    .out_11(pane_register_32_out_11), .out_12(pane_register_32_out_12), .out_13(pane_register_32_out_13),
    .out_14(pane_register_32_out_14), .out_15(pane_register_32_out_15), .out_16(pane_register_32_out_16),
    .out_17(pane_register_32_out_17), .out_18(pane_register_32_out_18), .out_19(pane_register_32_out_19),
    .out_20(pane_register_32_out_20), .out_21(pane_register_32_out_21));

  // Notes on the sheet:
  //   Screen Offset
  //   Screen Size
endmodule

module Pane_Register (
  input  [15:0] Data,
  input  CLK,
  input  Enable,
  input  Reset,
  input  [15:0] Address,
  output [15:0] out_6,
  output [15:0] out_7,
  output [15:0] out_8,
  output [15:0] out_9,
  output [15:0] out_10,
  output [15:0] out_11,
  output [15:0] out_12,
  output [15:0] out_13,
  output [15:0] out_14,
  output [15:0] out_15,
  output [15:0] out_16,
  output [15:0] out_17,
  output [15:0] out_18,
  output [15:0] out_19,
  output [15:0] out_20,
  output [15:0] out_21
);

  wire and_1_out, and_2_out, and_3_out, and_4_out, and_5_out, and_6_out, and_7_out, and_8_out, and_9_out,
       and_10_out, and_11_out, and_12_out, and_13_out, and_14_out, and_15_out, and_16_out;
  wire [3:0] decoder_1_out0, decoder_1_out4, decoder_1_out8, decoder_1_out12;

  Decoder #(.select(4), .enable("false")) decoder_1 (
    .out0(decoder_1_out0[0]), .out1(decoder_1_out0[1]), .out2(decoder_1_out0[2]), .out3(decoder_1_out0[3]),
    .out4(decoder_1_out4[0]), .out5(decoder_1_out4[1]), .out6(decoder_1_out4[2]), .out7(decoder_1_out4[3]),
    .out8(decoder_1_out8[0]), .out9(decoder_1_out8[1]), .out10(decoder_1_out8[2]), .out11(decoder_1_out8[3]),
    .out12(decoder_1_out12[0]), .out13(decoder_1_out12[1]), .out14(decoder_1_out12[2]),
    .out15(decoder_1_out12[3]), .sel(Address[3:0]));
  and and_1 (and_1_out, Enable, decoder_1_out0[0]);
  and and_2 (and_2_out, Enable, decoder_1_out0[1]);
  and and_3 (and_3_out, Enable, decoder_1_out0[2]);
  and and_4 (and_4_out, Enable, decoder_1_out0[3]);
  and and_5 (and_5_out, Enable, decoder_1_out4[0]);
  and and_6 (and_6_out, Enable, decoder_1_out4[1]);
  and and_7 (and_7_out, Enable, decoder_1_out4[2]);
  and and_8 (and_8_out, Enable, decoder_1_out4[3]);
  and and_9 (and_9_out, Enable, decoder_1_out8[0]);
  and and_10 (and_10_out, Enable, decoder_1_out8[1]);
  and and_11 (and_11_out, Enable, decoder_1_out8[2]);
  and and_12 (and_12_out, Enable, decoder_1_out8[3]);
  and and_13 (and_13_out, Enable, decoder_1_out12[0]);
  and and_14 (and_14_out, Enable, decoder_1_out12[1]);
  and and_15 (and_15_out, Enable, decoder_1_out12[2]);
  and and_16 (and_16_out, Enable, decoder_1_out12[3]);
  Register #(.width(16)) register_1 (
    .D({Data[0], Data[1], Data[2], Data[3], Data[4], Data[5], Data[6], Data[7], Data[8], Data[9], Data[10], Data[11], Data[12], Data[13], Data[14], Data[15]}),
    .en(and_1_out), .Q(out_6), .clk(CLK), .clr(Reset));
  Register #(.width(16)) register_2 (
    .D({Data[0], Data[1], Data[2], Data[3], Data[4], Data[5], Data[6], Data[7], Data[8], Data[9], Data[10], Data[11], Data[12], Data[13], Data[14], Data[15]}),
    .en(and_2_out), .Q(out_7), .clk(CLK), .clr(Reset));
  Register #(.width(16)) register_3 (
    .D({Data[0], Data[1], Data[2], Data[3], Data[4], Data[5], Data[6], Data[7], Data[8], Data[9], Data[10], Data[11], Data[12], Data[13], Data[14], Data[15]}),
    .en(and_3_out), .Q(out_8), .clk(CLK), .clr(Reset));
  Register #(.width(16)) register_4 (
    .D({Data[0], Data[1], Data[2], Data[3], Data[4], Data[5], Data[6], Data[7], Data[8], Data[9], Data[10], Data[11], Data[12], Data[13], Data[14], Data[15]}),
    .en(and_4_out), .Q(out_9), .clk(CLK), .clr(Reset));
  Register #(.width(16)) register_5 (
    .D({Data[0], Data[1], Data[2], Data[3], Data[4], Data[5], Data[6], Data[7], Data[8], Data[9], Data[10], Data[11], Data[12], Data[13], Data[14], Data[15]}),
    .en(and_5_out), .Q(out_10), .clk(CLK), .clr(Reset));
  Register #(.width(16)) register_6 (
    .D({Data[0], Data[1], Data[2], Data[3], Data[4], Data[5], Data[6], Data[7], Data[8], Data[9], Data[10], Data[11], Data[12], Data[13], Data[14], Data[15]}),
    .en(and_6_out), .Q(out_11), .clk(CLK), .clr(Reset));
  Register #(.width(16)) register_7 (
    .D({Data[0], Data[1], Data[2], Data[3], Data[4], Data[5], Data[6], Data[7], Data[8], Data[9], Data[10], Data[11], Data[12], Data[13], Data[14], Data[15]}),
    .en(and_7_out), .Q(out_12), .clk(CLK), .clr(Reset));
  Register #(.width(16)) register_8 (
    .D({Data[0], Data[1], Data[2], Data[3], Data[4], Data[5], Data[6], Data[7], Data[8], Data[9], Data[10], Data[11], Data[12], Data[13], Data[14], Data[15]}),
    .en(and_8_out), .Q(out_13), .clk(CLK), .clr(Reset));
  Register #(.width(16)) register_9 (
    .D({Data[0], Data[1], Data[2], Data[3], Data[4], Data[5], Data[6], Data[7], Data[8], Data[9], Data[10], Data[11], Data[12], Data[13], Data[14], Data[15]}),
    .en(and_9_out), .Q(out_14), .clk(CLK), .clr(Reset));
  Register #(.width(16)) register_10 (
    .D({Data[0], Data[1], Data[2], Data[3], Data[4], Data[5], Data[6], Data[7], Data[8], Data[9], Data[10], Data[11], Data[12], Data[13], Data[14], Data[15]}),
    .en(and_10_out), .Q(out_15), .clk(CLK), .clr(Reset));
  Register #(.width(16)) register_11 (
    .D({Data[0], Data[1], Data[2], Data[3], Data[4], Data[5], Data[6], Data[7], Data[8], Data[9], Data[10], Data[11], Data[12], Data[13], Data[14], Data[15]}),
    .en(and_11_out), .Q(out_16), .clk(CLK), .clr(Reset));
  Register #(.width(16)) register_12 (
    .D({Data[0], Data[1], Data[2], Data[3], Data[4], Data[5], Data[6], Data[7], Data[8], Data[9], Data[10], Data[11], Data[12], Data[13], Data[14], Data[15]}),
    .en(and_12_out), .Q(out_17), .clk(CLK), .clr(Reset));
  Register #(.width(16)) register_13 (
    .D({Data[0], Data[1], Data[2], Data[3], Data[4], Data[5], Data[6], Data[7], Data[8], Data[9], Data[10], Data[11], Data[12], Data[13], Data[14], Data[15]}),
    .en(and_13_out), .Q(out_18), .clk(CLK), .clr(Reset));
  Register #(.width(16)) register_14 (
    .D({Data[0], Data[1], Data[2], Data[3], Data[4], Data[5], Data[6], Data[7], Data[8], Data[9], Data[10], Data[11], Data[12], Data[13], Data[14], Data[15]}),
    .en(and_14_out), .Q(out_19), .clk(CLK), .clr(Reset));
  Register #(.width(16)) register_15 (
    .D({Data[0], Data[1], Data[2], Data[3], Data[4], Data[5], Data[6], Data[7], Data[8], Data[9], Data[10], Data[11], Data[12], Data[13], Data[14], Data[15]}),
    .en(and_15_out), .Q(out_20), .clk(CLK), .clr(Reset));
  Register #(.width(16)) register_16 (
    .D({Data[0], Data[1], Data[2], Data[3], Data[4], Data[5], Data[6], Data[7], Data[8], Data[9], Data[10], Data[11], Data[12], Data[13], Data[14], Data[15]}),
    .en(and_16_out), .Q(out_21), .clk(CLK), .clr(Reset));

  // Other names for the same wires on the sheet: RST = Reset

  // Notes on the sheet:
  //   Store the state for a 16x16 LED matrix (a pane).
  //   LED matrix must be set as rows input.
  //   Each line has a corresponding 16 bits state register
  //   Subcircuit layout is designed to make the component linkable horizontally by
  //   adding a large space between the input and output
endmodule

module ScreenControl_test (
  input  [15:0] Data,
  input  CLK,
  input  Reset,
  input  Enable,
  input  [15:0] Address,
  output [15:0] out_6,
  output [15:0] out_7,
  output [15:0] out_8,
  output [15:0] out_9,
  output [15:0] out_10,
  output [15:0] out_11,
  output [15:0] out_12,
  output [15:0] out_13,
  output [15:0] out_14,
  output [15:0] out_15,
  output [15:0] out_16,
  output [15:0] out_17,
  output [15:0] out_18,
  output [15:0] out_19,
  output [15:0] out_20,
  output [15:0] out_21
);

  wire and_1_out, and_2_out, and_3_out, and_4_out, and_5_out, and_6_out, and_7_out, and_8_out, and_9_out,
       and_10_out, and_11_out, and_12_out, and_13_out, and_14_out, and_15_out, and_16_out;
  wire [3:0] decoder_1_out0, decoder_1_out4, decoder_1_out8, decoder_1_out12;

  Decoder #(.select(4), .enable("false")) decoder_1 (
    .out0(decoder_1_out0[0]), .out1(decoder_1_out0[1]), .out2(decoder_1_out0[2]), .out3(decoder_1_out0[3]),
    .out4(decoder_1_out4[0]), .out5(decoder_1_out4[1]), .out6(decoder_1_out4[2]), .out7(decoder_1_out4[3]),
    .out8(decoder_1_out8[0]), .out9(decoder_1_out8[1]), .out10(decoder_1_out8[2]), .out11(decoder_1_out8[3]),
    .out12(decoder_1_out12[0]), .out13(decoder_1_out12[1]), .out14(decoder_1_out12[2]),
    .out15(decoder_1_out12[3]), .sel(Address[3:0]));
  and and_1 (and_1_out, Enable, decoder_1_out0[0]);
  and and_2 (and_2_out, Enable, decoder_1_out0[1]);
  and and_3 (and_3_out, Enable, decoder_1_out0[2]);
  and and_4 (and_4_out, Enable, decoder_1_out0[3]);
  and and_5 (and_5_out, Enable, decoder_1_out4[0]);
  and and_6 (and_6_out, Enable, decoder_1_out4[1]);
  and and_7 (and_7_out, Enable, decoder_1_out4[2]);
  and and_8 (and_8_out, Enable, decoder_1_out4[3]);
  and and_9 (and_9_out, Enable, decoder_1_out8[0]);
  and and_10 (and_10_out, Enable, decoder_1_out8[1]);
  and and_11 (and_11_out, Enable, decoder_1_out8[2]);
  and and_12 (and_12_out, Enable, decoder_1_out8[3]);
  and and_13 (and_13_out, Enable, decoder_1_out12[0]);
  and and_14 (and_14_out, Enable, decoder_1_out12[1]);
  and and_15 (and_15_out, Enable, decoder_1_out12[2]);
  and and_16 (and_16_out, Enable, decoder_1_out12[3]);
  Register #(.width(16)) register_1 (
    .D({Data[0], Data[1], Data[2], Data[3], Data[4], Data[5], Data[6], Data[7], Data[8], Data[9], Data[10], Data[11], Data[12], Data[13], Data[14], Data[15]}),
    .en(and_1_out), .Q(out_6), .clk(CLK), .clr(Reset));
  Register #(.width(16)) register_2 (
    .D({Data[0], Data[1], Data[2], Data[3], Data[4], Data[5], Data[6], Data[7], Data[8], Data[9], Data[10], Data[11], Data[12], Data[13], Data[14], Data[15]}),
    .en(and_2_out), .Q(out_7), .clk(CLK), .clr(Reset));
  Register #(.width(16)) register_3 (
    .D({Data[0], Data[1], Data[2], Data[3], Data[4], Data[5], Data[6], Data[7], Data[8], Data[9], Data[10], Data[11], Data[12], Data[13], Data[14], Data[15]}),
    .en(and_3_out), .Q(out_8), .clk(CLK), .clr(Reset));
  Register #(.width(16)) register_4 (
    .D({Data[0], Data[1], Data[2], Data[3], Data[4], Data[5], Data[6], Data[7], Data[8], Data[9], Data[10], Data[11], Data[12], Data[13], Data[14], Data[15]}),
    .en(and_4_out), .Q(out_9), .clk(CLK), .clr(Reset));
  Register #(.width(16)) register_5 (
    .D({Data[0], Data[1], Data[2], Data[3], Data[4], Data[5], Data[6], Data[7], Data[8], Data[9], Data[10], Data[11], Data[12], Data[13], Data[14], Data[15]}),
    .en(and_5_out), .Q(out_10), .clk(CLK), .clr(Reset));
  Register #(.width(16)) register_6 (
    .D({Data[0], Data[1], Data[2], Data[3], Data[4], Data[5], Data[6], Data[7], Data[8], Data[9], Data[10], Data[11], Data[12], Data[13], Data[14], Data[15]}),
    .en(and_6_out), .Q(out_11), .clk(CLK), .clr(Reset));
  Register #(.width(16)) register_7 (
    .D({Data[0], Data[1], Data[2], Data[3], Data[4], Data[5], Data[6], Data[7], Data[8], Data[9], Data[10], Data[11], Data[12], Data[13], Data[14], Data[15]}),
    .en(and_7_out), .Q(out_12), .clk(CLK), .clr(Reset));
  Register #(.width(16)) register_8 (
    .D({Data[0], Data[1], Data[2], Data[3], Data[4], Data[5], Data[6], Data[7], Data[8], Data[9], Data[10], Data[11], Data[12], Data[13], Data[14], Data[15]}),
    .en(and_8_out), .Q(out_13), .clk(CLK), .clr(Reset));
  Register #(.width(16)) register_9 (
    .D({Data[0], Data[1], Data[2], Data[3], Data[4], Data[5], Data[6], Data[7], Data[8], Data[9], Data[10], Data[11], Data[12], Data[13], Data[14], Data[15]}),
    .en(and_9_out), .Q(out_14), .clk(CLK), .clr(Reset));
  Register #(.width(16)) register_10 (
    .D({Data[0], Data[1], Data[2], Data[3], Data[4], Data[5], Data[6], Data[7], Data[8], Data[9], Data[10], Data[11], Data[12], Data[13], Data[14], Data[15]}),
    .en(and_10_out), .Q(out_15), .clk(CLK), .clr(Reset));
  Register #(.width(16)) register_11 (
    .D({Data[0], Data[1], Data[2], Data[3], Data[4], Data[5], Data[6], Data[7], Data[8], Data[9], Data[10], Data[11], Data[12], Data[13], Data[14], Data[15]}),
    .en(and_11_out), .Q(out_16), .clk(CLK), .clr(Reset));
  Register #(.width(16)) register_12 (
    .D({Data[0], Data[1], Data[2], Data[3], Data[4], Data[5], Data[6], Data[7], Data[8], Data[9], Data[10], Data[11], Data[12], Data[13], Data[14], Data[15]}),
    .en(and_12_out), .Q(out_17), .clk(CLK), .clr(Reset));
  Register #(.width(16)) register_13 (
    .D({Data[0], Data[1], Data[2], Data[3], Data[4], Data[5], Data[6], Data[7], Data[8], Data[9], Data[10], Data[11], Data[12], Data[13], Data[14], Data[15]}),
    .en(and_13_out), .Q(out_18), .clk(CLK), .clr(Reset));
  Register #(.width(16)) register_14 (
    .D({Data[0], Data[1], Data[2], Data[3], Data[4], Data[5], Data[6], Data[7], Data[8], Data[9], Data[10], Data[11], Data[12], Data[13], Data[14], Data[15]}),
    .en(and_14_out), .Q(out_19), .clk(CLK), .clr(Reset));
  Register #(.width(16)) register_15 (
    .D({Data[0], Data[1], Data[2], Data[3], Data[4], Data[5], Data[6], Data[7], Data[8], Data[9], Data[10], Data[11], Data[12], Data[13], Data[14], Data[15]}),
    .en(and_15_out), .Q(out_20), .clk(CLK), .clr(Reset));
  Register #(.width(16)) register_16 (
    .D({Data[0], Data[1], Data[2], Data[3], Data[4], Data[5], Data[6], Data[7], Data[8], Data[9], Data[10], Data[11], Data[12], Data[13], Data[14], Data[15]}),
    .en(and_16_out), .Q(out_21), .clk(CLK), .clr(Reset));

  // Other names for the same wires on the sheet: RST = Reset
endmodule

// Panel Address Mapper
module Pane_Address_Mapper (
  input  in_1,
  input  in_2,
  input  in_3,
  input  in_4,
  input  in_5,
  input  in_6,
  input  in_7,
  input  in_8,
  input  in_9,
  input  in_10,
  input  in_11,
  input  in_12,
  output out_13,
  output out_14,
  output out_15,
  output out_16,
  output out_17,
  output out_18,
  output out_19,
  output out_20,
  output out_21,
  output out_22,
  output out_23,
  output out_24,
  output out_25,
  output out_26,
  output out_27,
  output out_28,
  output out_29,
  output out_30,
  output out_31,
  output out_32,
  output out_33,
  output out_34,
  output out_35,
  output out_36,
  output out_37,
  output out_38,
  output out_39,
  output out_40,
  output out_41,
  output out_42,
  output out_43,
  output out_44
);

  and and_1 (out_13, in_9, in_1);
  and and_2 (out_21, in_10, in_1);
  and and_3 (out_29, in_11, in_1);
  and and_4 (out_37, in_12, in_1);
  and and_5 (out_14, in_9, in_2);
  and and_6 (out_22, in_10, in_2);
  and and_7 (out_30, in_11, in_2);
  and and_8 (out_38, in_12, in_2);
  and and_9 (out_15, in_9, in_3);
  and and_10 (out_23, in_10, in_3);
  and and_11 (out_31, in_11, in_3);
  and and_12 (out_39, in_12, in_3);
  and and_13 (out_16, in_9, in_4);
  and and_14 (out_24, in_10, in_4);
  and and_15 (out_32, in_11, in_4);
  and and_16 (out_40, in_12, in_4);
  and and_17 (out_17, in_9, in_5);
  and and_18 (out_25, in_10, in_5);
  and and_19 (out_33, in_11, in_5);
  and and_20 (out_41, in_12, in_5);
  and and_21 (out_18, in_9, in_6);
  and and_22 (out_26, in_10, in_6);
  and and_23 (out_34, in_11, in_6);
  and and_24 (out_42, in_12, in_6);
  and and_25 (out_19, in_9, in_7);
  and and_26 (out_27, in_10, in_7);
  and and_27 (out_35, in_11, in_7);
  and and_28 (out_43, in_12, in_7);
  and and_29 (out_20, in_9, in_8);
  and and_30 (out_28, in_10, in_8);
  and and_31 (out_36, in_11, in_8);
  and and_32 (out_44, in_12, in_8);

  // Notes on the sheet:
  //   Map a pane address matrix into a 32 bits output
endmodule

module Pane_Decoder (
  input  [15:0] Address,
  input  Enable,
  input  [15:0] Screen_Width,
  output [15:0] Pane_Local_Address,
  output [31:0] Pane_Address
);

  wire decoder_1_out0, decoder_1_out1, decoder_1_out2, decoder_1_out3, decoder_2_out0, decoder_2_out1,
       decoder_2_out2, decoder_2_out3, decoder_2_out4, decoder_2_out5, decoder_2_out6, decoder_2_out7,
       not_1_out;
  wire [1:0] divider_2_out;
  wire [15:0] divider_1_rem;
  wire [15:2] divider_2_out_2;
  wire [31:0] pane_address_mapper_1_out_20, pull_resistor_1_node;

  Divider #(.width(16)) divider_1 (
    .a(Address), .b(Screen_Width), .out(Pane_Local_Address), .rem(divider_1_rem));  // open: upper
  Divider #(.width(16)) divider_2 (
    .a(Pane_Local_Address), .b(16'h10), .out({divider_2_out_2, divider_2_out}));  // open: upper, rem
  Decoder #(.select(2), .enable("false")) decoder_1 (
    .out0(decoder_1_out0), .out1(decoder_1_out1), .out2(decoder_1_out2), .out3(decoder_1_out3),
    .sel(divider_2_out));
  Decoder #(.select(5), .enable("false")) decoder_2 (
    .out0(decoder_2_out0), .out1(decoder_2_out1), .out2(decoder_2_out2), .out3(decoder_2_out3),
    .out4(decoder_2_out4), .out5(decoder_2_out5), .out6(decoder_2_out6), .out7(decoder_2_out7),
    .sel(divider_1_rem[4:0]));  // open: out8, out9, out10, out11, out12, out13, out14, out15, out16, out17, out18, out19, out20, out21, out22, out23, out24, out25, out26, out27, out28, out29, out30, out31
  Pane_Address_Mapper pane_address_mapper_1 (
    .in_9(decoder_1_out0), .in_10(decoder_1_out1), .in_11(decoder_1_out2), .in_12(decoder_1_out3),
    .in_1(decoder_2_out0), .in_2(decoder_2_out1), .in_3(decoder_2_out2), .in_4(decoder_2_out3),
    .in_5(decoder_2_out4), .in_6(decoder_2_out5), .in_7(decoder_2_out6), .in_8(decoder_2_out7),
    .out_37(pane_address_mapper_1_out_20[31]), .out_29(pane_address_mapper_1_out_20[30]),
    .out_21(pane_address_mapper_1_out_20[29]), .out_13(pane_address_mapper_1_out_20[28]),
    .out_38(pane_address_mapper_1_out_20[27]), .out_30(pane_address_mapper_1_out_20[26]),
    .out_22(pane_address_mapper_1_out_20[25]), .out_14(pane_address_mapper_1_out_20[24]),
    .out_39(pane_address_mapper_1_out_20[23]), .out_31(pane_address_mapper_1_out_20[22]),
    .out_23(pane_address_mapper_1_out_20[21]), .out_15(pane_address_mapper_1_out_20[20]),
    .out_40(pane_address_mapper_1_out_20[19]), .out_32(pane_address_mapper_1_out_20[18]),
    .out_24(pane_address_mapper_1_out_20[17]), .out_16(pane_address_mapper_1_out_20[16]),
    .out_41(pane_address_mapper_1_out_20[15]), .out_33(pane_address_mapper_1_out_20[14]),
    .out_25(pane_address_mapper_1_out_20[13]), .out_17(pane_address_mapper_1_out_20[12]),
    .out_42(pane_address_mapper_1_out_20[11]), .out_34(pane_address_mapper_1_out_20[10]),
    .out_26(pane_address_mapper_1_out_20[9]), .out_18(pane_address_mapper_1_out_20[8]),
    .out_43(pane_address_mapper_1_out_20[7]), .out_35(pane_address_mapper_1_out_20[6]),
    .out_27(pane_address_mapper_1_out_20[5]), .out_19(pane_address_mapper_1_out_20[4]),
    .out_44(pane_address_mapper_1_out_20[3]), .out_36(pane_address_mapper_1_out_20[2]),
    .out_28(pane_address_mapper_1_out_20[1]), .out_20(pane_address_mapper_1_out_20[0]));
  Pull_Resistor pull_resistor_1 (.node(pull_resistor_1_node));
  Multiplexer #(.width(32), .enable("false")) multiplexer_1 (
    .in0(pane_address_mapper_1_out_20), .in1(pull_resistor_1_node), .out(Pane_Address), .sel(not_1_out));
  not not_1 (not_1_out, Enable);

  // Notes on the sheet:
  //   Decode RAM address into Pane Address (where the pane is located) and Pane Local Address (which line of the pane to update)
  //   Panel height (fixed at 16)
  //   This decoder works with maximum 32 columns, but currently only use 8 columns as 32 is too big for logism
endmodule

module SR_Latch_old (
  input  S,
  input  R,
  output Q,
  output minus_Q
);

  nor nor_1 (minus_Q, S, Q);
  nor nor_2 (Q, minus_Q, R);
endmodule

module Replicator (
  input  [15:0] Address,
  input  [15:0] Data,
  input  Write,
  input  [15:0] Offset,
  input  CLK,
  input  RESET,
  output [15:0] out_7,
  output [15:0] out_8,
  output [15:0] out_9,
  output [15:0] out_10,
  output [15:0] out_11,
  output [15:0] out_12,
  output [15:0] out_13,
  output [15:0] out_14,
  output [15:0] out_15,
  output [15:0] out_16,
  output [15:0] out_17,
  output [15:0] out_18,
  output [15:0] out_19,
  output [15:0] out_20,
  output [15:0] out_21,
  output [15:0] out_22,
  output [15:0] out_23,
  output [15:0] out_24,
  output [15:0] out_25,
  output [15:0] out_26,
  output [15:0] out_27,
  output [15:0] out_28,
  output [15:0] out_29,
  output [15:0] out_30,
  output [15:0] out_31,
  output [15:0] out_32,
  output [15:0] out_33,
  output [15:0] out_34,
  output [15:0] out_35,
  output [15:0] out_36,
  output [15:0] out_37,
  output [15:0] out_38
);

  wire address_translator_1_active___1_means_address_in_range, and_1_out;
  wire [15:0] address_translator_1_translated_address;
  wire [31:0] decoder_1_out0, multiplexer_1_out, pull_resistor_1_node;

  Address_Translator address_translator_1 (
    .Address(Address), .Offset(Offset), .Limit(16'h20),
    .Translated_Address(address_translator_1_translated_address),
    .Active___1_means_address_in_range(address_translator_1_active___1_means_address_in_range));
  Decoder #(.select(5), .enable("false")) decoder_1 (
    .out0(decoder_1_out0[0]), .out1(decoder_1_out0[1]), .out2(decoder_1_out0[2]), .out3(decoder_1_out0[3]),
    .out4(decoder_1_out0[4]), .out5(decoder_1_out0[5]), .out6(decoder_1_out0[6]), .out7(decoder_1_out0[7]),
    .out8(decoder_1_out0[8]), .out9(decoder_1_out0[9]), .out10(decoder_1_out0[10]),
    .out11(decoder_1_out0[11]), .out12(decoder_1_out0[12]), .out13(decoder_1_out0[13]),
    .out14(decoder_1_out0[14]), .out15(decoder_1_out0[15]), .out16(decoder_1_out0[16]),
    .out17(decoder_1_out0[17]), .out18(decoder_1_out0[18]), .out19(decoder_1_out0[19]),
    .out20(decoder_1_out0[20]), .out21(decoder_1_out0[21]), .out22(decoder_1_out0[22]),
    .out23(decoder_1_out0[23]), .out24(decoder_1_out0[24]), .out25(decoder_1_out0[25]),
    .out26(decoder_1_out0[26]), .out27(decoder_1_out0[27]), .out28(decoder_1_out0[28]),
    .out29(decoder_1_out0[29]), .out30(decoder_1_out0[30]), .out31(decoder_1_out0[31]),
    .sel(address_translator_1_translated_address[4:0]));
  Pull_Resistor pull_resistor_1 (.node(pull_resistor_1_node));
  Multiplexer #(.width(32), .enable("false")) multiplexer_1 (
    .in0(pull_resistor_1_node), .in1(decoder_1_out0), .out(multiplexer_1_out), .sel(and_1_out));
  and and_1 (and_1_out, address_translator_1_active___1_means_address_in_range, Write);
  Register #(.width(16)) register_1 (.D(Data), .en(multiplexer_1_out[0]), .Q(out_7), .clk(CLK), .clr(RESET));
  Register #(.width(16)) register_2 (.D(Data), .en(multiplexer_1_out[1]), .Q(out_8), .clk(CLK), .clr(RESET));
  Register #(.width(16)) register_3 (.D(Data), .en(multiplexer_1_out[2]), .Q(out_9), .clk(CLK), .clr(RESET));
  Register #(.width(16)) register_4 (.D(Data), .en(multiplexer_1_out[3]), .Q(out_10), .clk(CLK), .clr(RESET));
  Register #(.width(16)) register_5 (.D(Data), .en(multiplexer_1_out[4]), .Q(out_11), .clk(CLK), .clr(RESET));
  Register #(.width(16)) register_6 (.D(Data), .en(multiplexer_1_out[5]), .Q(out_12), .clk(CLK), .clr(RESET));
  Register #(.width(16)) register_7 (.D(Data), .en(multiplexer_1_out[6]), .Q(out_13), .clk(CLK), .clr(RESET));
  Register #(.width(16)) register_8 (.D(Data), .en(multiplexer_1_out[7]), .Q(out_14), .clk(CLK), .clr(RESET));
  Register #(.width(16)) register_9 (.D(Data), .en(multiplexer_1_out[8]), .Q(out_15), .clk(CLK), .clr(RESET));
  Register #(.width(16)) register_10 (.D(Data), .en(multiplexer_1_out[9]), .Q(out_16), .clk(CLK), .clr(RESET));
  Register #(.width(16)) register_11 (.D(Data), .en(multiplexer_1_out[10]), .Q(out_17), .clk(CLK), .clr(RESET));
  Register #(.width(16)) register_12 (.D(Data), .en(multiplexer_1_out[11]), .Q(out_18), .clk(CLK), .clr(RESET));
  Register #(.width(16)) register_13 (.D(Data), .en(multiplexer_1_out[12]), .Q(out_19), .clk(CLK), .clr(RESET));
  Register #(.width(16)) register_14 (.D(Data), .en(multiplexer_1_out[13]), .Q(out_20), .clk(CLK), .clr(RESET));
  Register #(.width(16)) register_15 (.D(Data), .en(multiplexer_1_out[14]), .Q(out_21), .clk(CLK), .clr(RESET));
  Register #(.width(16)) register_16 (.D(Data), .en(multiplexer_1_out[15]), .Q(out_22), .clk(CLK), .clr(RESET));
  Register #(.width(16)) register_17 (.D(Data), .en(multiplexer_1_out[16]), .Q(out_23), .clk(CLK), .clr(RESET));
  Register #(.width(16)) register_18 (.D(Data), .en(multiplexer_1_out[17]), .Q(out_24), .clk(CLK), .clr(RESET));
  Register #(.width(16)) register_19 (.D(Data), .en(multiplexer_1_out[18]), .Q(out_25), .clk(CLK), .clr(RESET));
  Register #(.width(16)) register_20 (.D(Data), .en(multiplexer_1_out[19]), .Q(out_26), .clk(CLK), .clr(RESET));
  Register #(.width(16)) register_21 (.D(Data), .en(multiplexer_1_out[20]), .Q(out_27), .clk(CLK), .clr(RESET));
  Register #(.width(16)) register_22 (.D(Data), .en(multiplexer_1_out[21]), .Q(out_28), .clk(CLK), .clr(RESET));
  Register #(.width(16)) register_23 (.D(Data), .en(multiplexer_1_out[22]), .Q(out_29), .clk(CLK), .clr(RESET));
  Register #(.width(16)) register_24 (.D(Data), .en(multiplexer_1_out[23]), .Q(out_30), .clk(CLK), .clr(RESET));
  Register #(.width(16)) register_25 (.D(Data), .en(multiplexer_1_out[24]), .Q(out_31), .clk(CLK), .clr(RESET));
  Register #(.width(16)) register_26 (.D(Data), .en(multiplexer_1_out[25]), .Q(out_32), .clk(CLK), .clr(RESET));
  Register #(.width(16)) register_27 (.D(Data), .en(multiplexer_1_out[26]), .Q(out_33), .clk(CLK), .clr(RESET));
  Register #(.width(16)) register_28 (.D(Data), .en(multiplexer_1_out[27]), .Q(out_34), .clk(CLK), .clr(RESET));
  Register #(.width(16)) register_29 (.D(Data), .en(multiplexer_1_out[28]), .Q(out_35), .clk(CLK), .clr(RESET));
  Register #(.width(16)) register_30 (.D(Data), .en(multiplexer_1_out[29]), .Q(out_36), .clk(CLK), .clr(RESET));
  Register #(.width(16)) register_31 (.D(Data), .en(multiplexer_1_out[30]), .Q(out_37), .clk(CLK), .clr(RESET));
  Register #(.width(16)) register_32 (.D(Data), .en(multiplexer_1_out[31]), .Q(out_38), .clk(CLK), .clr(RESET));

  // Notes on the sheet:
  //   32 values
  //   Maximum 32 addresses can be replicated. If need more, concatinate this component with continuous offsets.
  //   Replicate a segment of RAM, by using a combination of Adress+Data(16bits)+Write+Offset. Out put is stored in 32 registers, each 16 bits in size.
endmodule
module Debug_Board (
  input  [15:0] Address,
  input  [15:0] Data,
  input  Write,
  input  CLK,
  input  RESET
);

  wire [15:0] adapter_1_out_33, adapter_1_out_34, adapter_1_out_35, adapter_1_out_36, adapter_1_out_37,
       adapter_1_out_38, adapter_1_out_39, adapter_1_out_40, adapter_1_out_41, adapter_1_out_42,
       adapter_1_out_43, adapter_1_out_44, adapter_1_out_45, adapter_1_out_46, adapter_1_out_47,
       adapter_1_out_48, adapter_1_out_49, adapter_1_out_50, adapter_1_out_51, adapter_1_out_52,
       adapter_1_out_53, adapter_1_out_54, adapter_1_out_55, adapter_1_out_56, adapter_1_out_57,
       adapter_1_out_58, adapter_1_out_59, adapter_1_out_60, adapter_1_out_61, adapter_1_out_62,
       adapter_1_out_63, adapter_1_out_64, adapter_2_out_33, adapter_2_out_34, adapter_2_out_35,
       adapter_2_out_36, adapter_2_out_37, adapter_2_out_38, adapter_2_out_39, adapter_2_out_40,
       adapter_2_out_41, adapter_2_out_42, adapter_2_out_43, adapter_2_out_44, adapter_2_out_45,
       adapter_2_out_46, adapter_2_out_47, adapter_2_out_48, adapter_2_out_49, adapter_2_out_50,
       adapter_2_out_51, adapter_2_out_52, adapter_2_out_53, adapter_2_out_54, adapter_2_out_55,
       adapter_2_out_56, adapter_2_out_57, adapter_2_out_58, adapter_2_out_59, adapter_2_out_60,
       adapter_2_out_61, adapter_2_out_62, adapter_2_out_63, adapter_2_out_64, adapter_3_out_33,
       adapter_3_out_34, adapter_3_out_35, adapter_3_out_36, adapter_3_out_37, adapter_3_out_38,
       adapter_3_out_39, adapter_3_out_40, adapter_3_out_41, adapter_3_out_42, adapter_3_out_43,
       adapter_3_out_44, adapter_3_out_45, adapter_3_out_46, adapter_3_out_47, adapter_3_out_48,
       adapter_3_out_49, adapter_3_out_50, adapter_3_out_51, adapter_3_out_52, adapter_3_out_53,
       adapter_3_out_54, adapter_3_out_55, adapter_3_out_56, adapter_3_out_57, adapter_3_out_58,
       adapter_3_out_59, adapter_3_out_60, adapter_3_out_61, adapter_3_out_62, adapter_3_out_63,
       adapter_3_out_64, adapter_4_out_33, adapter_4_out_34, adapter_4_out_35, adapter_4_out_36,
       adapter_4_out_37, adapter_4_out_38, adapter_4_out_39, adapter_4_out_40, adapter_4_out_41,
       adapter_4_out_42, adapter_4_out_43, adapter_4_out_44, adapter_4_out_45, adapter_4_out_46,
       adapter_4_out_47, adapter_4_out_48, adapter_4_out_49, adapter_4_out_50, adapter_4_out_51,
       adapter_4_out_52, adapter_4_out_53, adapter_4_out_54, adapter_4_out_55, adapter_4_out_56,
       adapter_4_out_57, adapter_4_out_58, adapter_4_out_59, adapter_4_out_60, adapter_4_out_61,
       adapter_4_out_62, adapter_4_out_63, adapter_4_out_64, adapter_5_out_33, adapter_5_out_34,
       adapter_5_out_35, adapter_5_out_36, adapter_5_out_37, adapter_5_out_38, adapter_5_out_39,
       adapter_5_out_40, adapter_5_out_41, adapter_5_out_42, adapter_6_out_33, adapter_6_out_34,
       adapter_6_out_35, adapter_6_out_36, adapter_6_out_37, adapter_6_out_38, adapter_6_out_39,
       adapter_6_out_40, adapter_6_out_41, adapter_6_out_42, replicator_1_out_7, replicator_1_out_8,
       replicator_1_out_9, replicator_1_out_10, replicator_1_out_11, replicator_1_out_12,
       replicator_1_out_13, replicator_1_out_14, replicator_1_out_15, replicator_1_out_16,
       replicator_1_out_17, replicator_1_out_18, replicator_1_out_19, replicator_1_out_20,
       replicator_1_out_21, replicator_1_out_22, replicator_1_out_23, replicator_1_out_24,
       replicator_1_out_25, replicator_1_out_26, replicator_1_out_27, replicator_1_out_28,
       replicator_1_out_29, replicator_1_out_30, replicator_1_out_31, replicator_1_out_32,
       replicator_1_out_33, replicator_1_out_34, replicator_1_out_35, replicator_1_out_36,
       replicator_1_out_37, replicator_1_out_38, replicator_2_out_7, replicator_2_out_8, replicator_2_out_9,
       replicator_2_out_10, replicator_2_out_11, replicator_2_out_12, replicator_2_out_13,
       replicator_2_out_14, replicator_2_out_15, replicator_2_out_16, replicator_2_out_17,
       replicator_2_out_18, replicator_2_out_19, replicator_2_out_20, replicator_2_out_21,
       replicator_2_out_22, replicator_2_out_23, replicator_2_out_24, replicator_2_out_25,
       replicator_2_out_26, replicator_2_out_27, replicator_2_out_28, replicator_2_out_29,
       replicator_2_out_30, replicator_2_out_31, replicator_2_out_32, replicator_2_out_33,
       replicator_2_out_34, replicator_2_out_35, replicator_2_out_36, replicator_2_out_37,
       replicator_2_out_38, replicator_3_out_7, replicator_3_out_8, replicator_3_out_9, replicator_3_out_10,
       replicator_3_out_11, replicator_3_out_12, replicator_3_out_13, replicator_3_out_14,
       replicator_3_out_15, replicator_3_out_16, replicator_3_out_17, replicator_3_out_18,
       replicator_3_out_19, replicator_3_out_20, replicator_3_out_21, replicator_3_out_22,
       replicator_3_out_23, replicator_3_out_24, replicator_3_out_25, replicator_3_out_26,
       replicator_3_out_27, replicator_3_out_28, replicator_3_out_29, replicator_3_out_30,
       replicator_3_out_31, replicator_3_out_32, replicator_3_out_33, replicator_3_out_34,
       replicator_3_out_35, replicator_3_out_36, replicator_3_out_37, replicator_3_out_38,
       replicator_4_out_7, replicator_4_out_8, replicator_4_out_9, replicator_4_out_10, replicator_4_out_11,
       replicator_4_out_12, replicator_4_out_13, replicator_4_out_14, replicator_4_out_15,
       replicator_4_out_16, replicator_4_out_17, replicator_4_out_18, replicator_4_out_19,
       replicator_4_out_20, replicator_4_out_21, replicator_4_out_22, replicator_4_out_23,
       replicator_4_out_24, replicator_4_out_25, replicator_4_out_26, replicator_4_out_27,
       replicator_4_out_28, replicator_4_out_29, replicator_4_out_30, replicator_4_out_31,
       replicator_4_out_32, replicator_4_out_33, replicator_4_out_34, replicator_4_out_35,
       replicator_4_out_36, replicator_4_out_37, replicator_4_out_38, replicator_5_out_7, replicator_5_out_8,
       replicator_5_out_9, replicator_5_out_10, replicator_5_out_11, replicator_5_out_12,
       replicator_5_out_13, replicator_5_out_14, replicator_5_out_15, replicator_5_out_16,
       replicator_5_out_17, replicator_5_out_18, replicator_5_out_19, replicator_5_out_20,
       replicator_5_out_21, replicator_5_out_22, replicator_5_out_23, replicator_5_out_24,
       replicator_5_out_25, replicator_5_out_26, replicator_5_out_27, replicator_5_out_28,
       replicator_5_out_29, replicator_5_out_30, replicator_5_out_31, replicator_5_out_32,
       replicator_5_out_33, replicator_5_out_34, replicator_5_out_35, replicator_5_out_36,
       replicator_5_out_37, replicator_5_out_38, replicator_6_out_7, replicator_6_out_8, replicator_6_out_9,
       replicator_6_out_10, replicator_6_out_11, replicator_6_out_12, replicator_6_out_13,
       replicator_6_out_14, replicator_6_out_15, replicator_6_out_16, replicator_6_out_17,
       replicator_6_out_18, replicator_6_out_19, replicator_6_out_20, replicator_6_out_21,
       replicator_6_out_22, replicator_6_out_23, replicator_6_out_24, replicator_6_out_25,
       replicator_6_out_26, replicator_6_out_27, replicator_6_out_28, replicator_6_out_29,
       replicator_6_out_30, replicator_6_out_31, replicator_6_out_32, replicator_6_out_33,
       replicator_6_out_34, replicator_6_out_35, replicator_6_out_36, replicator_6_out_37,
       replicator_6_out_38;

  // Probe on Address
  Replicator replicator_1 (
    .Address(Address), .Data(Data), .Write(Write), .Offset({16{1'b0}}), .CLK(CLK), .RESET(RESET),
    .out_7(replicator_1_out_7), .out_8(replicator_1_out_8), .out_9(replicator_1_out_9),
    .out_10(replicator_1_out_10), .out_11(replicator_1_out_11), .out_12(replicator_1_out_12),
    .out_13(replicator_1_out_13), .out_14(replicator_1_out_14), .out_15(replicator_1_out_15),
    .out_16(replicator_1_out_16), .out_17(replicator_1_out_17), .out_18(replicator_1_out_18),
    .out_19(replicator_1_out_19), .out_20(replicator_1_out_20), .out_21(replicator_1_out_21),
    .out_22(replicator_1_out_22), .out_23(replicator_1_out_23), .out_24(replicator_1_out_24),
    .out_25(replicator_1_out_25), .out_26(replicator_1_out_26), .out_27(replicator_1_out_27),
    .out_28(replicator_1_out_28), .out_29(replicator_1_out_29), .out_30(replicator_1_out_30),
    .out_31(replicator_1_out_31), .out_32(replicator_1_out_32), .out_33(replicator_1_out_33),
    .out_34(replicator_1_out_34), .out_35(replicator_1_out_35), .out_36(replicator_1_out_36),
    .out_37(replicator_1_out_37), .out_38(replicator_1_out_38));
  // Probe on adapter_1_out_33
  Adapter adapter_1 (
    .out_33(adapter_1_out_33), .out_34(adapter_1_out_34), .out_35(adapter_1_out_35),
    .out_36(adapter_1_out_36), .out_37(adapter_1_out_37), .out_38(adapter_1_out_38),
    .out_39(adapter_1_out_39), .out_40(adapter_1_out_40), .out_41(adapter_1_out_41),
    .out_42(adapter_1_out_42), .out_43(adapter_1_out_43), .out_44(adapter_1_out_44),
    .out_45(adapter_1_out_45), .out_46(adapter_1_out_46), .out_47(adapter_1_out_47),
    .out_48(adapter_1_out_48), .out_49(adapter_1_out_49), .out_50(adapter_1_out_50),
    .out_51(adapter_1_out_51), .out_52(adapter_1_out_52), .out_53(adapter_1_out_53),
    .out_54(adapter_1_out_54), .out_55(adapter_1_out_55), .out_56(adapter_1_out_56),
    .out_57(adapter_1_out_57), .out_58(adapter_1_out_58), .out_59(adapter_1_out_59),
    .out_60(adapter_1_out_60), .out_61(adapter_1_out_61), .out_62(adapter_1_out_62),
    .out_63(adapter_1_out_63), .out_64(adapter_1_out_64), .in_1(replicator_1_out_7),
    .in_2(replicator_1_out_8), .in_3(replicator_1_out_9), .in_4(replicator_1_out_10),
    .in_5(replicator_1_out_11), .in_6(replicator_1_out_12), .in_7(replicator_1_out_13),
    .in_8(replicator_1_out_14), .in_9(replicator_1_out_15), .in_10(replicator_1_out_16),
    .in_11(replicator_1_out_17), .in_12(replicator_1_out_18), .in_13(replicator_1_out_19),
    .in_14(replicator_1_out_20), .in_15(replicator_1_out_21), .in_16(replicator_1_out_22),
    .in_17(replicator_1_out_23), .in_18(replicator_1_out_24), .in_19(replicator_1_out_25),
    .in_20(replicator_1_out_26), .in_21(replicator_1_out_27), .in_22(replicator_1_out_28),
    .in_23(replicator_1_out_29), .in_24(replicator_1_out_30), .in_25(replicator_1_out_31),
    .in_26(replicator_1_out_32), .in_27(replicator_1_out_33), .in_28(replicator_1_out_34),
    .in_29(replicator_1_out_35), .in_30(replicator_1_out_36), .in_31(replicator_1_out_37),
    .in_32(replicator_1_out_38));
  // Probe on adapter_1_out_34
  // Probe on adapter_1_out_35
  // Probe on adapter_1_out_36
  // Probe on adapter_1_out_37
  // Probe on adapter_1_out_38
  // Probe on adapter_1_out_39
  // Probe on adapter_1_out_40
  // Probe on adapter_1_out_41
  // Probe on adapter_1_out_42
  // Probe on adapter_1_out_43
  // Probe on adapter_1_out_44
  // Probe on adapter_1_out_45
  // Probe on adapter_1_out_46
  // Probe on adapter_1_out_47
  // Probe on adapter_1_out_48
  // Probe on adapter_1_out_49
  // Probe on adapter_1_out_50
  // Probe on adapter_1_out_51
  // Probe on adapter_1_out_52
  // Probe on adapter_1_out_53
  // Probe on adapter_1_out_54
  // Probe on adapter_1_out_55
  // Probe on adapter_1_out_56
  // Probe on adapter_1_out_57
  // Probe on adapter_1_out_58
  // Probe on adapter_1_out_59
  // Probe on adapter_1_out_60
  // Probe on adapter_1_out_61
  // Probe on adapter_1_out_62
  // Probe on adapter_1_out_63
  // Probe on adapter_1_out_64
  Replicator replicator_2 (
    .Address(Address), .Data(Data), .Write(Write), .Offset(16'h100), .CLK(CLK), .RESET(RESET),
    .out_7(replicator_2_out_7), .out_8(replicator_2_out_8), .out_9(replicator_2_out_9),
    .out_10(replicator_2_out_10), .out_11(replicator_2_out_11), .out_12(replicator_2_out_12),
    .out_13(replicator_2_out_13), .out_14(replicator_2_out_14), .out_15(replicator_2_out_15),
    .out_16(replicator_2_out_16), .out_17(replicator_2_out_17), .out_18(replicator_2_out_18),
    .out_19(replicator_2_out_19), .out_20(replicator_2_out_20), .out_21(replicator_2_out_21),
    .out_22(replicator_2_out_22), .out_23(replicator_2_out_23), .out_24(replicator_2_out_24),
    .out_25(replicator_2_out_25), .out_26(replicator_2_out_26), .out_27(replicator_2_out_27),
    .out_28(replicator_2_out_28), .out_29(replicator_2_out_29), .out_30(replicator_2_out_30),
    .out_31(replicator_2_out_31), .out_32(replicator_2_out_32), .out_33(replicator_2_out_33),
    .out_34(replicator_2_out_34), .out_35(replicator_2_out_35), .out_36(replicator_2_out_36),
    .out_37(replicator_2_out_37), .out_38(replicator_2_out_38));
  Adapter adapter_2 (
    .out_33(adapter_2_out_33), .out_34(adapter_2_out_34), .out_35(adapter_2_out_35),
    .out_36(adapter_2_out_36), .out_37(adapter_2_out_37), .out_38(adapter_2_out_38),
    .out_39(adapter_2_out_39), .out_40(adapter_2_out_40), .out_41(adapter_2_out_41),
    .out_42(adapter_2_out_42), .out_43(adapter_2_out_43), .out_44(adapter_2_out_44),
    .out_45(adapter_2_out_45), .out_46(adapter_2_out_46), .out_47(adapter_2_out_47),
    .out_48(adapter_2_out_48), .out_49(adapter_2_out_49), .out_50(adapter_2_out_50),
    .out_51(adapter_2_out_51), .out_52(adapter_2_out_52), .out_53(adapter_2_out_53),
    .out_54(adapter_2_out_54), .out_55(adapter_2_out_55), .out_56(adapter_2_out_56),
    .out_57(adapter_2_out_57), .out_58(adapter_2_out_58), .out_59(adapter_2_out_59),
    .out_60(adapter_2_out_60), .out_61(adapter_2_out_61), .out_62(adapter_2_out_62),
    .out_63(adapter_2_out_63), .out_64(adapter_2_out_64), .in_1(replicator_2_out_7),
    .in_2(replicator_2_out_8), .in_3(replicator_2_out_9), .in_4(replicator_2_out_10),
    .in_5(replicator_2_out_11), .in_6(replicator_2_out_12), .in_7(replicator_2_out_13),
    .in_8(replicator_2_out_14), .in_9(replicator_2_out_15), .in_10(replicator_2_out_16),
    .in_11(replicator_2_out_17), .in_12(replicator_2_out_18), .in_13(replicator_2_out_19),
    .in_14(replicator_2_out_20), .in_15(replicator_2_out_21), .in_16(replicator_2_out_22),
    .in_17(replicator_2_out_23), .in_18(replicator_2_out_24), .in_19(replicator_2_out_25),
    .in_20(replicator_2_out_26), .in_21(replicator_2_out_27), .in_22(replicator_2_out_28),
    .in_23(replicator_2_out_29), .in_24(replicator_2_out_30), .in_25(replicator_2_out_31),
    .in_26(replicator_2_out_32), .in_27(replicator_2_out_33), .in_28(replicator_2_out_34),
    .in_29(replicator_2_out_35), .in_30(replicator_2_out_36), .in_31(replicator_2_out_37),
    .in_32(replicator_2_out_38));
  // Probe on adapter_2_out_33
  // Probe on adapter_2_out_34
  // Probe on adapter_2_out_35
  // Probe on adapter_2_out_36
  // Probe on adapter_2_out_37
  // Probe on adapter_2_out_38
  // Probe on adapter_2_out_39
  // Probe on adapter_2_out_40
  // Probe on adapter_2_out_41
  // Probe on adapter_2_out_42
  // Probe on adapter_2_out_43
  // Probe on adapter_2_out_44
  // Probe on adapter_2_out_45
  // Probe on adapter_2_out_46
  // Probe on adapter_2_out_47
  // Probe on adapter_2_out_48
  // Probe on adapter_2_out_49
  // Probe on adapter_2_out_50
  // Probe on adapter_2_out_51
  // Probe on adapter_2_out_52
  // Probe on adapter_2_out_53
  // Probe on adapter_2_out_54
  // Probe on adapter_2_out_55
  // Probe on adapter_2_out_56
  // Probe on adapter_2_out_57
  // Probe on adapter_2_out_58
  // Probe on adapter_2_out_59
  // Probe on adapter_2_out_60
  // Probe on adapter_2_out_61
  // Probe on adapter_2_out_62
  // Probe on adapter_2_out_63
  // Probe on adapter_2_out_64
  Adapter adapter_3 (
    .out_33(adapter_3_out_33), .out_34(adapter_3_out_34), .out_35(adapter_3_out_35),
    .out_36(adapter_3_out_36), .out_37(adapter_3_out_37), .out_38(adapter_3_out_38),
    .out_39(adapter_3_out_39), .out_40(adapter_3_out_40), .out_41(adapter_3_out_41),
    .out_42(adapter_3_out_42), .out_43(adapter_3_out_43), .out_44(adapter_3_out_44),
    .out_45(adapter_3_out_45), .out_46(adapter_3_out_46), .out_47(adapter_3_out_47),
    .out_48(adapter_3_out_48), .out_49(adapter_3_out_49), .out_50(adapter_3_out_50),
    .out_51(adapter_3_out_51), .out_52(adapter_3_out_52), .out_53(adapter_3_out_53),
    .out_54(adapter_3_out_54), .out_55(adapter_3_out_55), .out_56(adapter_3_out_56),
    .out_57(adapter_3_out_57), .out_58(adapter_3_out_58), .out_59(adapter_3_out_59),
    .out_60(adapter_3_out_60), .out_61(adapter_3_out_61), .out_62(adapter_3_out_62),
    .out_63(adapter_3_out_63), .out_64(adapter_3_out_64), .in_1(replicator_3_out_7),
    .in_2(replicator_3_out_8), .in_3(replicator_3_out_9), .in_4(replicator_3_out_10),
    .in_5(replicator_3_out_11), .in_6(replicator_3_out_12), .in_7(replicator_3_out_13),
    .in_8(replicator_3_out_14), .in_9(replicator_3_out_15), .in_10(replicator_3_out_16),
    .in_11(replicator_3_out_17), .in_12(replicator_3_out_18), .in_13(replicator_3_out_19),
    .in_14(replicator_3_out_20), .in_15(replicator_3_out_21), .in_16(replicator_3_out_22),
    .in_17(replicator_3_out_23), .in_18(replicator_3_out_24), .in_19(replicator_3_out_25),
    .in_20(replicator_3_out_26), .in_21(replicator_3_out_27), .in_22(replicator_3_out_28),
    .in_23(replicator_3_out_29), .in_24(replicator_3_out_30), .in_25(replicator_3_out_31),
    .in_26(replicator_3_out_32), .in_27(replicator_3_out_33), .in_28(replicator_3_out_34),
    .in_29(replicator_3_out_35), .in_30(replicator_3_out_36), .in_31(replicator_3_out_37),
    .in_32(replicator_3_out_38));
  // Probe on adapter_3_out_33
  Replicator replicator_3 (
    .Address(Address), .Data(Data), .Write(Write), .Offset(16'h12c), .CLK(CLK), .RESET(RESET),
    .out_7(replicator_3_out_7), .out_8(replicator_3_out_8), .out_9(replicator_3_out_9),
    .out_10(replicator_3_out_10), .out_11(replicator_3_out_11), .out_12(replicator_3_out_12),
    .out_13(replicator_3_out_13), .out_14(replicator_3_out_14), .out_15(replicator_3_out_15),
    .out_16(replicator_3_out_16), .out_17(replicator_3_out_17), .out_18(replicator_3_out_18),
    .out_19(replicator_3_out_19), .out_20(replicator_3_out_20), .out_21(replicator_3_out_21),
    .out_22(replicator_3_out_22), .out_23(replicator_3_out_23), .out_24(replicator_3_out_24),
    .out_25(replicator_3_out_25), .out_26(replicator_3_out_26), .out_27(replicator_3_out_27),
    .out_28(replicator_3_out_28), .out_29(replicator_3_out_29), .out_30(replicator_3_out_30),
    .out_31(replicator_3_out_31), .out_32(replicator_3_out_32), .out_33(replicator_3_out_33),
    .out_34(replicator_3_out_34), .out_35(replicator_3_out_35), .out_36(replicator_3_out_36),
    .out_37(replicator_3_out_37), .out_38(replicator_3_out_38));
  // Probe on adapter_3_out_34
  // Probe on adapter_3_out_35
  // Probe on adapter_3_out_36
  // Probe on adapter_3_out_37
  // Probe on adapter_3_out_38
  // Probe on adapter_3_out_39
  // Probe on adapter_3_out_40
  // Probe on adapter_3_out_41
  // Probe on adapter_3_out_42
  // Probe on adapter_3_out_43
  // Probe on adapter_3_out_44
  // Probe on adapter_3_out_45
  // Probe on adapter_3_out_46
  // Probe on adapter_3_out_47
  // Probe on adapter_3_out_48
  // Probe on adapter_3_out_49
  // Probe on adapter_3_out_50
  // Probe on adapter_3_out_51
  // Probe on adapter_3_out_52
  // Probe on adapter_3_out_53
  // Probe on adapter_3_out_54
  // Probe on adapter_3_out_55
  // Probe on adapter_3_out_56
  // Probe on adapter_3_out_57
  // Probe on adapter_3_out_58
  // Probe on adapter_3_out_59
  // Probe on adapter_3_out_60
  // Probe on adapter_3_out_61
  // Probe on adapter_3_out_62
  // Probe on adapter_3_out_63
  // Probe on adapter_3_out_64
  Replicator replicator_4 (
    .Address(Address), .Data(Data), .Write(Write), .Offset(16'h190), .CLK(CLK), .RESET(RESET),
    .out_7(replicator_4_out_7), .out_8(replicator_4_out_8), .out_9(replicator_4_out_9),
    .out_10(replicator_4_out_10), .out_11(replicator_4_out_11), .out_12(replicator_4_out_12),
    .out_13(replicator_4_out_13), .out_14(replicator_4_out_14), .out_15(replicator_4_out_15),
    .out_16(replicator_4_out_16), .out_17(replicator_4_out_17), .out_18(replicator_4_out_18),
    .out_19(replicator_4_out_19), .out_20(replicator_4_out_20), .out_21(replicator_4_out_21),
    .out_22(replicator_4_out_22), .out_23(replicator_4_out_23), .out_24(replicator_4_out_24),
    .out_25(replicator_4_out_25), .out_26(replicator_4_out_26), .out_27(replicator_4_out_27),
    .out_28(replicator_4_out_28), .out_29(replicator_4_out_29), .out_30(replicator_4_out_30),
    .out_31(replicator_4_out_31), .out_32(replicator_4_out_32), .out_33(replicator_4_out_33),
    .out_34(replicator_4_out_34), .out_35(replicator_4_out_35), .out_36(replicator_4_out_36),
    .out_37(replicator_4_out_37), .out_38(replicator_4_out_38));
  Adapter adapter_4 (
    .out_33(adapter_4_out_33), .out_34(adapter_4_out_34), .out_35(adapter_4_out_35),
    .out_36(adapter_4_out_36), .out_37(adapter_4_out_37), .out_38(adapter_4_out_38),
    .out_39(adapter_4_out_39), .out_40(adapter_4_out_40), .out_41(adapter_4_out_41),
    .out_42(adapter_4_out_42), .out_43(adapter_4_out_43), .out_44(adapter_4_out_44),
    .out_45(adapter_4_out_45), .out_46(adapter_4_out_46), .out_47(adapter_4_out_47),
    .out_48(adapter_4_out_48), .out_49(adapter_4_out_49), .out_50(adapter_4_out_50),
    .out_51(adapter_4_out_51), .out_52(adapter_4_out_52), .out_53(adapter_4_out_53),
    .out_54(adapter_4_out_54), .out_55(adapter_4_out_55), .out_56(adapter_4_out_56),
    .out_57(adapter_4_out_57), .out_58(adapter_4_out_58), .out_59(adapter_4_out_59),
    .out_60(adapter_4_out_60), .out_61(adapter_4_out_61), .out_62(adapter_4_out_62),
    .out_63(adapter_4_out_63), .out_64(adapter_4_out_64), .in_1(replicator_4_out_7),
    .in_2(replicator_4_out_8), .in_3(replicator_4_out_9), .in_4(replicator_4_out_10),
    .in_5(replicator_4_out_11), .in_6(replicator_4_out_12), .in_7(replicator_4_out_13),
    .in_8(replicator_4_out_14), .in_9(replicator_4_out_15), .in_10(replicator_4_out_16),
    .in_11(replicator_4_out_17), .in_12(replicator_4_out_18), .in_13(replicator_4_out_19),
    .in_14(replicator_4_out_20), .in_15(replicator_4_out_21), .in_16(replicator_4_out_22),
    .in_17(replicator_4_out_23), .in_18(replicator_4_out_24), .in_19(replicator_4_out_25),
    .in_20(replicator_4_out_26), .in_21(replicator_4_out_27), .in_22(replicator_4_out_28),
    .in_23(replicator_4_out_29), .in_24(replicator_4_out_30), .in_25(replicator_4_out_31),
    .in_26(replicator_4_out_32), .in_27(replicator_4_out_33), .in_28(replicator_4_out_34),
    .in_29(replicator_4_out_35), .in_30(replicator_4_out_36), .in_31(replicator_4_out_37),
    .in_32(replicator_4_out_38));
  // Probe on adapter_4_out_33
  // Probe on adapter_4_out_34
  // Probe on adapter_4_out_35
  // Probe on adapter_4_out_36
  // Probe on adapter_4_out_37
  // Probe on adapter_4_out_38
  // Probe on adapter_4_out_39
  // Probe on adapter_4_out_40
  // Probe on adapter_4_out_41
  // Probe on adapter_4_out_42
  // Probe on adapter_4_out_43
  // Probe on adapter_4_out_44
  // Probe on adapter_4_out_45
  // Probe on adapter_4_out_46
  // Probe on adapter_4_out_47
  // Probe on adapter_4_out_48
  // Probe on adapter_4_out_49
  // Probe on adapter_4_out_50
  // Probe on adapter_4_out_51
  // Probe on adapter_4_out_52
  // Probe on adapter_4_out_53
  // Probe on adapter_4_out_54
  // Probe on adapter_4_out_55
  // Probe on adapter_4_out_56
  // Probe on adapter_4_out_57
  // Probe on adapter_4_out_58
  // Probe on adapter_4_out_59
  // Probe on adapter_4_out_60
  // Probe on adapter_4_out_61
  // Probe on adapter_4_out_62
  // Probe on adapter_4_out_63
  // Probe on adapter_4_out_64
  Replicator replicator_5 (
    .Address(Address), .Data(Data), .Write(Write), .Offset(16'hbb8), .CLK(CLK), .RESET(RESET),
    .out_7(replicator_5_out_7), .out_8(replicator_5_out_8), .out_9(replicator_5_out_9),
    .out_10(replicator_5_out_10), .out_11(replicator_5_out_11), .out_12(replicator_5_out_12),
    .out_13(replicator_5_out_13), .out_14(replicator_5_out_14), .out_15(replicator_5_out_15),
    .out_16(replicator_5_out_16), .out_17(replicator_5_out_17), .out_18(replicator_5_out_18),
    .out_19(replicator_5_out_19), .out_20(replicator_5_out_20), .out_21(replicator_5_out_21),
    .out_22(replicator_5_out_22), .out_23(replicator_5_out_23), .out_24(replicator_5_out_24),
    .out_25(replicator_5_out_25), .out_26(replicator_5_out_26), .out_27(replicator_5_out_27),
    .out_28(replicator_5_out_28), .out_29(replicator_5_out_29), .out_30(replicator_5_out_30),
    .out_31(replicator_5_out_31), .out_32(replicator_5_out_32), .out_33(replicator_5_out_33),
    .out_34(replicator_5_out_34), .out_35(replicator_5_out_35), .out_36(replicator_5_out_36),
    .out_37(replicator_5_out_37), .out_38(replicator_5_out_38));
  Adapter adapter_5 (
    .out_33(adapter_5_out_33), .out_34(adapter_5_out_34), .out_35(adapter_5_out_35),
    .out_36(adapter_5_out_36), .out_37(adapter_5_out_37), .out_38(adapter_5_out_38),
    .out_39(adapter_5_out_39), .out_40(adapter_5_out_40), .out_41(adapter_5_out_41),
    .out_42(adapter_5_out_42), .in_1(replicator_5_out_7), .in_2(replicator_5_out_8),
    .in_3(replicator_5_out_9), .in_4(replicator_5_out_10), .in_5(replicator_5_out_11),
    .in_6(replicator_5_out_12), .in_7(replicator_5_out_13), .in_8(replicator_5_out_14),
    .in_9(replicator_5_out_15), .in_10(replicator_5_out_16), .in_11(replicator_5_out_17),
    .in_12(replicator_5_out_18), .in_13(replicator_5_out_19), .in_14(replicator_5_out_20),
    .in_15(replicator_5_out_21), .in_16(replicator_5_out_22), .in_17(replicator_5_out_23),
    .in_18(replicator_5_out_24), .in_19(replicator_5_out_25), .in_20(replicator_5_out_26),
    .in_21(replicator_5_out_27), .in_22(replicator_5_out_28), .in_23(replicator_5_out_29),
    .in_24(replicator_5_out_30), .in_25(replicator_5_out_31), .in_26(replicator_5_out_32),
    .in_27(replicator_5_out_33), .in_28(replicator_5_out_34), .in_29(replicator_5_out_35),
    .in_30(replicator_5_out_36), .in_31(replicator_5_out_37), .in_32(replicator_5_out_38));  // open: out_43, out_44, out_45, out_46, out_47, out_48, out_49, out_50, out_51, out_52, out_53, out_54, out_55, out_56, out_57, out_58, out_59, out_60, out_61, out_62, out_63, out_64
  // Probe on adapter_5_out_33
  // Probe on adapter_5_out_34
  // Probe on adapter_5_out_35
  // Probe on adapter_5_out_36
  // Probe on adapter_5_out_37
  // Probe on adapter_5_out_38
  // Probe on adapter_5_out_39
  // Probe on adapter_5_out_40
  // Probe on adapter_5_out_41
  // Probe on adapter_5_out_42
  // Probe on adapter_6_out_33
  Replicator replicator_6 (
    .Address(Address), .Data(Data), .Write(Write), .Offset(16'hfa0), .CLK(CLK), .RESET(RESET),
    .out_7(replicator_6_out_7), .out_8(replicator_6_out_8), .out_9(replicator_6_out_9),
    .out_10(replicator_6_out_10), .out_11(replicator_6_out_11), .out_12(replicator_6_out_12),
    .out_13(replicator_6_out_13), .out_14(replicator_6_out_14), .out_15(replicator_6_out_15),
    .out_16(replicator_6_out_16), .out_17(replicator_6_out_17), .out_18(replicator_6_out_18),
    .out_19(replicator_6_out_19), .out_20(replicator_6_out_20), .out_21(replicator_6_out_21),
    .out_22(replicator_6_out_22), .out_23(replicator_6_out_23), .out_24(replicator_6_out_24),
    .out_25(replicator_6_out_25), .out_26(replicator_6_out_26), .out_27(replicator_6_out_27),
    .out_28(replicator_6_out_28), .out_29(replicator_6_out_29), .out_30(replicator_6_out_30),
    .out_31(replicator_6_out_31), .out_32(replicator_6_out_32), .out_33(replicator_6_out_33),
    .out_34(replicator_6_out_34), .out_35(replicator_6_out_35), .out_36(replicator_6_out_36),
    .out_37(replicator_6_out_37), .out_38(replicator_6_out_38));
  Adapter adapter_6 (
    .out_33(adapter_6_out_33), .out_34(adapter_6_out_34), .out_35(adapter_6_out_35),
    .out_36(adapter_6_out_36), .out_37(adapter_6_out_37), .out_38(adapter_6_out_38),
    .out_39(adapter_6_out_39), .out_40(adapter_6_out_40), .out_41(adapter_6_out_41),
    .out_42(adapter_6_out_42), .in_1(replicator_6_out_7), .in_2(replicator_6_out_8),
    .in_3(replicator_6_out_9), .in_4(replicator_6_out_10), .in_5(replicator_6_out_11),
    .in_6(replicator_6_out_12), .in_7(replicator_6_out_13), .in_8(replicator_6_out_14),
    .in_9(replicator_6_out_15), .in_10(replicator_6_out_16), .in_11(replicator_6_out_17),
    .in_12(replicator_6_out_18), .in_13(replicator_6_out_19), .in_14(replicator_6_out_20),
    .in_15(replicator_6_out_21), .in_16(replicator_6_out_22), .in_17(replicator_6_out_23),
    .in_18(replicator_6_out_24), .in_19(replicator_6_out_25), .in_20(replicator_6_out_26),
    .in_21(replicator_6_out_27), .in_22(replicator_6_out_28), .in_23(replicator_6_out_29),
    .in_24(replicator_6_out_30), .in_25(replicator_6_out_31), .in_26(replicator_6_out_32),
    .in_27(replicator_6_out_33), .in_28(replicator_6_out_34), .in_29(replicator_6_out_35),
    .in_30(replicator_6_out_36), .in_31(replicator_6_out_37), .in_32(replicator_6_out_38));  // open: out_43, out_44, out_45, out_46, out_47, out_48, out_49, out_50, out_51, out_52, out_53, out_54, out_55, out_56, out_57, out_58, out_59, out_60, out_61, out_62, out_63, out_64
  // Probe on adapter_6_out_34
  // Probe on adapter_6_out_35
  // Probe on adapter_6_out_36
  // Probe on adapter_6_out_37
  // Probe on adapter_6_out_38
  // Probe on adapter_6_out_39
  // Probe on adapter_6_out_40
  // Probe on adapter_6_out_41
  // Probe on adapter_6_out_42

  // Notes on the sheet:
  //   Replicate several segments of RAM into probes to inspect the values in decimal
  //   POINTERS
  //   STACK
  //   LOCAL
  //   ARG
  //   THIS
  //   THAT
endmodule

module Address_Translator (
  input  [15:0] Address,
  input  [15:0] Offset,
  input  [15:0] Limit,
  output [15:0] Translated_Address,
  output Active___1_means_address_in_range
);

  wire comparator_1_eq, comparator_1_gt, comparator_2_lt, or_1_out;
  wire [15:0] adder_1_out;

  Subtractor #(.width(16)) subtractor_1 (.a(Address), .b(Offset), .out(Translated_Address));  // open: bin, bout
  Comparator #(.width(16)) comparator_1 (
    .a(Address), .b(Offset), .gt(comparator_1_gt), .eq(comparator_1_eq));  // open: lt
  Comparator #(.width(16)) comparator_2 (.a(Address), .b(adder_1_out), .lt(comparator_2_lt));  // open: gt, eq
  Adder #(.width(16)) adder_1 (.a(Offset), .b(Limit), .out(adder_1_out));  // open: cin, cout
  or or_1 (or_1_out, comparator_1_gt, comparator_1_eq);
  and and_1 (Active___1_means_address_in_range, or_1_out, comparator_2_lt);

  // Notes on the sheet:
  //   Translate a global address to a local address, useful for memory mapping. Address range is [offset, offset + limit)
endmodule

module Adapter (
  input  [15:0] in_1,
  input  [15:0] in_2,
  input  [15:0] in_3,
  input  [15:0] in_4,
  input  [15:0] in_5,
  input  [15:0] in_6,
  input  [15:0] in_7,
  input  [15:0] in_8,
  input  [15:0] in_9,
  input  [15:0] in_10,
  input  [15:0] in_11,
  input  [15:0] in_12,
  input  [15:0] in_13,
  input  [15:0] in_14,
  input  [15:0] in_15,
  input  [15:0] in_16,
  input  [15:0] in_17,
  input  [15:0] in_18,
  input  [15:0] in_19,
  input  [15:0] in_20,
  input  [15:0] in_21,
  input  [15:0] in_22,
  input  [15:0] in_23,
  input  [15:0] in_24,
  input  [15:0] in_25,
  input  [15:0] in_26,
  input  [15:0] in_27,
  input  [15:0] in_28,
  input  [15:0] in_29,
  input  [15:0] in_30,
  input  [15:0] in_31,
  input  [15:0] in_32,
  output [15:0] out_33,
  output [15:0] out_34,
  output [15:0] out_35,
  output [15:0] out_36,
  output [15:0] out_37,
  output [15:0] out_38,
  output [15:0] out_39,
  output [15:0] out_40,
  output [15:0] out_41,
  output [15:0] out_42,
  output [15:0] out_43,
  output [15:0] out_44,
  output [15:0] out_45,
  output [15:0] out_46,
  output [15:0] out_47,
  output [15:0] out_48,
  output [15:0] out_49,
  output [15:0] out_50,
  output [15:0] out_51,
  output [15:0] out_52,
  output [15:0] out_53,
  output [15:0] out_54,
  output [15:0] out_55,
  output [15:0] out_56,
  output [15:0] out_57,
  output [15:0] out_58,
  output [15:0] out_59,
  output [15:0] out_60,
  output [15:0] out_61,
  output [15:0] out_62,
  output [15:0] out_63,
  output [15:0] out_64
);


  assign out_33 = in_1;
  assign out_34 = in_2;
  assign out_35 = in_3;
  assign out_36 = in_4;
  assign out_37 = in_5;
  assign out_38 = in_6;
  assign out_39 = in_7;
  assign out_40 = in_8;
  assign out_41 = in_9;
  assign out_42 = in_10;
  assign out_43 = in_11;
  assign out_44 = in_12;
  assign out_45 = in_13;
  assign out_46 = in_14;
  assign out_47 = in_15;
  assign out_48 = in_16;
  assign out_49 = in_17;
  assign out_50 = in_18;
  assign out_51 = in_19;
  assign out_52 = in_20;
  assign out_53 = in_21;
  assign out_54 = in_22;
  assign out_55 = in_23;
  assign out_56 = in_24;
  assign out_57 = in_25;
  assign out_58 = in_26;
  assign out_59 = in_27;
  assign out_60 = in_28;
  assign out_61 = in_29;
  assign out_62 = in_30;
  assign out_63 = in_31;
  assign out_64 = in_32;

  // Notes on the sheet:
  //   Spread out the pins (see subcircuit appearance), add spacing between the vertical pins to make it easier to integrate with other (big) components
endmodule

module Display_Control (
  input  [15:0] Screen_Width,
  input  [15:0] Address,
  input  [15:0] Data,
  input  Write,
  input  CLK,
  input  RESET,
  output [15:0] out_7,
  output [15:0] out_8,
  output [15:0] out_9,
  output [15:0] out_10,
  output [15:0] out_11,
  output [15:0] out_12,
  output [15:0] out_13,
  output [15:0] out_14,
  output [15:0] out_15,
  output [15:0] out_16,
  output [15:0] out_17,
  output [15:0] out_18,
  output [15:0] out_19,
  output [15:0] out_20,
  output [15:0] out_21,
  output [15:0] out_22,
  output [15:0] out_23,
  output [15:0] out_24,
  output [15:0] out_25,
  output [15:0] out_26,
  output [15:0] out_27,
  output [15:0] out_28,
  output [15:0] out_29,
  output [15:0] out_30,
  output [15:0] out_31,
  output [15:0] out_32,
  output [15:0] out_33,
  output [15:0] out_34,
  output [15:0] out_35,
  output [15:0] out_36,
  output [15:0] out_37,
  output [15:0] out_38,
  output [15:0] out_39,
  output [15:0] out_40,
  output [15:0] out_41,
  output [15:0] out_42,
  output [15:0] out_43,
  output [15:0] out_44,
  output [15:0] out_45,
  output [15:0] out_46,
  output [15:0] out_47,
  output [15:0] out_48,
  output [15:0] out_49,
  output [15:0] out_50,
  output [15:0] out_51,
  output [15:0] out_52,
  output [15:0] out_53,
  output [15:0] out_54,
  output [15:0] out_55,
  output [15:0] out_56,
  output [15:0] out_57,
  output [15:0] out_58,
  output [15:0] out_59,
  output [15:0] out_60,
  output [15:0] out_61,
  output [15:0] out_62,
  output [15:0] out_63,
  output [15:0] out_64,
  output [15:0] out_65,
  output [15:0] out_66,
  output [15:0] out_67,
  output [15:0] out_68,
  output [15:0] out_69,
  output [15:0] out_70,
  output [15:0] out_71,
  output [15:0] out_72,
  output [15:0] out_73,
  output [15:0] out_74,
  output [15:0] out_75,
  output [15:0] out_76,
  output [15:0] out_77,
  output [15:0] out_78,
  output [15:0] out_79,
  output [15:0] out_80,
  output [15:0] out_81,
  output [15:0] out_82,
  output [15:0] out_83,
  output [15:0] out_84,
  output [15:0] out_85,
  output [15:0] out_86,
  output [15:0] out_87,
  output [15:0] out_88,
  output [15:0] out_89,
  output [15:0] out_90,
  output [15:0] out_91,
  output [15:0] out_92,
  output [15:0] out_93,
  output [15:0] out_94,
  output [15:0] out_95,
  output [15:0] out_96,
  output [15:0] out_97,
  output [15:0] out_98,
  output [15:0] out_99,
  output [15:0] out_100,
  output [15:0] out_101,
  output [15:0] out_102,
  output [15:0] out_103,
  output [15:0] out_104,
  output [15:0] out_105,
  output [15:0] out_106,
  output [15:0] out_107,
  output [15:0] out_108,
  output [15:0] out_109,
  output [15:0] out_110,
  output [15:0] out_111,
  output [15:0] out_112,
  output [15:0] out_113,
  output [15:0] out_114,
  output [15:0] out_115,
  output [15:0] out_116,
  output [15:0] out_117,
  output [15:0] out_118,
  output [15:0] out_119,
  output [15:0] out_120,
  output [15:0] out_121,
  output [15:0] out_122,
  output [15:0] out_123,
  output [15:0] out_124,
  output [15:0] out_125,
  output [15:0] out_126,
  output [15:0] out_127,
  output [15:0] out_128,
  output [15:0] out_129,
  output [15:0] out_130,
  output [15:0] out_131,
  output [15:0] out_132,
  output [15:0] out_133,
  output [15:0] out_134,
  output [15:0] out_135,
  output [15:0] out_136,
  output [15:0] out_137,
  output [15:0] out_138,
  output [15:0] out_139,
  output [15:0] out_140,
  output [15:0] out_141,
  output [15:0] out_142,
  output [15:0] out_143,
  output [15:0] out_144,
  output [15:0] out_145,
  output [15:0] out_146,
  output [15:0] out_147,
  output [15:0] out_148,
  output [15:0] out_149,
  output [15:0] out_150,
  output [15:0] out_151,
  output [15:0] out_152,
  output [15:0] out_153,
  output [15:0] out_154,
  output [15:0] out_155,
  output [15:0] out_156,
  output [15:0] out_157,
  output [15:0] out_158,
  output [15:0] out_159,
  output [15:0] out_160,
  output [15:0] out_161,
  output [15:0] out_162,
  output [15:0] out_163,
  output [15:0] out_164,
  output [15:0] out_165,
  output [15:0] out_166,
  output [15:0] out_167,
  output [15:0] out_168,
  output [15:0] out_169,
  output [15:0] out_170,
  output [15:0] out_171,
  output [15:0] out_172,
  output [15:0] out_173,
  output [15:0] out_174,
  output [15:0] out_175,
  output [15:0] out_176,
  output [15:0] out_177,
  output [15:0] out_178,
  output [15:0] out_179,
  output [15:0] out_180,
  output [15:0] out_181,
  output [15:0] out_182,
  output [15:0] out_183,
  output [15:0] out_184,
  output [15:0] out_185,
  output [15:0] out_186,
  output [15:0] out_187,
  output [15:0] out_188,
  output [15:0] out_189,
  output [15:0] out_190,
  output [15:0] out_191,
  output [15:0] out_192,
  output [15:0] out_193,
  output [15:0] out_194,
  output [15:0] out_195,
  output [15:0] out_196,
  output [15:0] out_197,
  output [15:0] out_198,
  output [15:0] out_199,
  output [15:0] out_200,
  output [15:0] out_201,
  output [15:0] out_202,
  output [15:0] out_203,
  output [15:0] out_204,
  output [15:0] out_205,
  output [15:0] out_206,
  output [15:0] out_207,
  output [15:0] out_208,
  output [15:0] out_209,
  output [15:0] out_210,
  output [15:0] out_211,
  output [15:0] out_212,
  output [15:0] out_213,
  output [15:0] out_214,
  output [15:0] out_215,
  output [15:0] out_216,
  output [15:0] out_217,
  output [15:0] out_218,
  output [15:0] out_219,
  output [15:0] out_220,
  output [15:0] out_221,
  output [15:0] out_222,
  output [15:0] out_223,
  output [15:0] out_224,
  output [15:0] out_225,
  output [15:0] out_226,
  output [15:0] out_227,
  output [15:0] out_228,
  output [15:0] out_229,
  output [15:0] out_230,
  output [15:0] out_231,
  output [15:0] out_232,
  output [15:0] out_233,
  output [15:0] out_234,
  output [15:0] out_235,
  output [15:0] out_236,
  output [15:0] out_237,
  output [15:0] out_238,
  output [15:0] out_239,
  output [15:0] out_240,
  output [15:0] out_241,
  output [15:0] out_242,
  output [15:0] out_243,
  output [15:0] out_244,
  output [15:0] out_245,
  output [15:0] out_246,
  output [15:0] out_247,
  output [15:0] out_248,
  output [15:0] out_249,
  output [15:0] out_250,
  output [15:0] out_251,
  output [15:0] out_252,
  output [15:0] out_253,
  output [15:0] out_254,
  output [15:0] out_255,
  output [15:0] out_256,
  output [15:0] out_257,
  output [15:0] out_258,
  output [15:0] out_259,
  output [15:0] out_260,
  output [15:0] out_261,
  output [15:0] out_262,
  output [15:0] out_263,
  output [15:0] out_264,
  output [15:0] out_265,
  output [15:0] out_266,
  output [15:0] out_267,
  output [15:0] out_268,
  output [15:0] out_269,
  output [15:0] out_270,
  output [15:0] out_271,
  output [15:0] out_272,
  output [15:0] out_273,
  output [15:0] out_274,
  output [15:0] out_275,
  output [15:0] out_276,
  output [15:0] out_277,
  output [15:0] out_278,
  output [15:0] out_279,
  output [15:0] out_280,
  output [15:0] out_281,
  output [15:0] out_282,
  output [15:0] out_283,
  output [15:0] out_284,
  output [15:0] out_285,
  output [15:0] out_286,
  output [15:0] out_287,
  output [15:0] out_288,
  output [15:0] out_289,
  output [15:0] out_290,
  output [15:0] out_291,
  output [15:0] out_292,
  output [15:0] out_293,
  output [15:0] out_294,
  output [15:0] out_295,
  output [15:0] out_296,
  output [15:0] out_297,
  output [15:0] out_298,
  output [15:0] out_299,
  output [15:0] out_300,
  output [15:0] out_301,
  output [15:0] out_302,
  output [15:0] out_303,
  output [15:0] out_304,
  output [15:0] out_305,
  output [15:0] out_306,
  output [15:0] out_307,
  output [15:0] out_308,
  output [15:0] out_309,
  output [15:0] out_310,
  output [15:0] out_311,
  output [15:0] out_312,
  output [15:0] out_313,
  output [15:0] out_314,
  output [15:0] out_315,
  output [15:0] out_316,
  output [15:0] out_317,
  output [15:0] out_318,
  output [15:0] out_319,
  output [15:0] out_320,
  output [15:0] out_321,
  output [15:0] out_322,
  output [15:0] out_323,
  output [15:0] out_324,
  output [15:0] out_325,
  output [15:0] out_326,
  output [15:0] out_327,
  output [15:0] out_328,
  output [15:0] out_329,
  output [15:0] out_330,
  output [15:0] out_331,
  output [15:0] out_332,
  output [15:0] out_333,
  output [15:0] out_334,
  output [15:0] out_335,
  output [15:0] out_336,
  output [15:0] out_337,
  output [15:0] out_338,
  output [15:0] out_339,
  output [15:0] out_340,
  output [15:0] out_341,
  output [15:0] out_342,
  output [15:0] out_343,
  output [15:0] out_344,
  output [15:0] out_345,
  output [15:0] out_346,
  output [15:0] out_347,
  output [15:0] out_348,
  output [15:0] out_349,
  output [15:0] out_350,
  output [15:0] out_351,
  output [15:0] out_352,
  output [15:0] out_353,
  output [15:0] out_354,
  output [15:0] out_355,
  output [15:0] out_356,
  output [15:0] out_357,
  output [15:0] out_358,
  output [15:0] out_359,
  output [15:0] out_360,
  output [15:0] out_361,
  output [15:0] out_362,
  output [15:0] out_363,
  output [15:0] out_364,
  output [15:0] out_365,
  output [15:0] out_366,
  output [15:0] out_367,
  output [15:0] out_368,
  output [15:0] out_369,
  output [15:0] out_370,
  output [15:0] out_371,
  output [15:0] out_372,
  output [15:0] out_373,
  output [15:0] out_374,
  output [15:0] out_375,
  output [15:0] out_376,
  output [15:0] out_377,
  output [15:0] out_378,
  output [15:0] out_379,
  output [15:0] out_380,
  output [15:0] out_381,
  output [15:0] out_382,
  output [15:0] out_383,
  output [15:0] out_384,
  output [15:0] out_385,
  output [15:0] out_386,
  output [15:0] out_387,
  output [15:0] out_388,
  output [15:0] out_389,
  output [15:0] out_390,
  output [15:0] out_391,
  output [15:0] out_392,
  output [15:0] out_393,
  output [15:0] out_394,
  output [15:0] out_395,
  output [15:0] out_396,
  output [15:0] out_397,
  output [15:0] out_398,
  output [15:0] out_399,
  output [15:0] out_400,
  output [15:0] out_401,
  output [15:0] out_402,
  output [15:0] out_403,
  output [15:0] out_404,
  output [15:0] out_405,
  output [15:0] out_406,
  output [15:0] out_407,
  output [15:0] out_408,
  output [15:0] out_409,
  output [15:0] out_410,
  output [15:0] out_411,
  output [15:0] out_412,
  output [15:0] out_413,
  output [15:0] out_414,
  output [15:0] out_415,
  output [15:0] out_416,
  output [15:0] out_417,
  output [15:0] out_418,
  output [15:0] out_419,
  output [15:0] out_420,
  output [15:0] out_421,
  output [15:0] out_422,
  output [15:0] out_423,
  output [15:0] out_424,
  output [15:0] out_425,
  output [15:0] out_426,
  output [15:0] out_427,
  output [15:0] out_428,
  output [15:0] out_429,
  output [15:0] out_430,
  output [15:0] out_431,
  output [15:0] out_432,
  output [15:0] out_433,
  output [15:0] out_434,
  output [15:0] out_435,
  output [15:0] out_436,
  output [15:0] out_437,
  output [15:0] out_438,
  output [15:0] out_439,
  output [15:0] out_440,
  output [15:0] out_441,
  output [15:0] out_442,
  output [15:0] out_443,
  output [15:0] out_444,
  output [15:0] out_445,
  output [15:0] out_446,
  output [15:0] out_447,
  output [15:0] out_448,
  output [15:0] out_449,
  output [15:0] out_450,
  output [15:0] out_451,
  output [15:0] out_452,
  output [15:0] out_453,
  output [15:0] out_454,
  output [15:0] out_455,
  output [15:0] out_456,
  output [15:0] out_457,
  output [15:0] out_458,
  output [15:0] out_459,
  output [15:0] out_460,
  output [15:0] out_461,
  output [15:0] out_462,
  output [15:0] out_463,
  output [15:0] out_464,
  output [15:0] out_465,
  output [15:0] out_466,
  output [15:0] out_467,
  output [15:0] out_468,
  output [15:0] out_469,
  output [15:0] out_470,
  output [15:0] out_471,
  output [15:0] out_472,
  output [15:0] out_473,
  output [15:0] out_474,
  output [15:0] out_475,
  output [15:0] out_476,
  output [15:0] out_477,
  output [15:0] out_478,
  output [15:0] out_479,
  output [15:0] out_480,
  output [15:0] out_481,
  output [15:0] out_482,
  output [15:0] out_483,
  output [15:0] out_484,
  output [15:0] out_485,
  output [15:0] out_486,
  output [15:0] out_487,
  output [15:0] out_488,
  output [15:0] out_489,
  output [15:0] out_490,
  output [15:0] out_491,
  output [15:0] out_492,
  output [15:0] out_493,
  output [15:0] out_494,
  output [15:0] out_495,
  output [15:0] out_496,
  output [15:0] out_497,
  output [15:0] out_498,
  output [15:0] out_499,
  output [15:0] out_500,
  output [15:0] out_501,
  output [15:0] out_502,
  output [15:0] out_503,
  output [15:0] out_504,
  output [15:0] out_505,
  output [15:0] out_506,
  output [15:0] out_507,
  output [15:0] out_508,
  output [15:0] out_509,
  output [15:0] out_510,
  output [15:0] out_511,
  output [15:0] out_512,
  output [15:0] out_513,
  output [15:0] out_514,
  output [15:0] out_515,
  output [15:0] out_516,
  output [15:0] out_517,
  output [15:0] out_518
);

  wire address_translator_1_active___1_means_address_in_range, and_1_out;
  wire [3:0] pane_decoder_1_pane_address, pane_decoder_1_pane_address_3;
  wire [15:0] address_translator_1_translated_address, Pane_Local_Address;
  wire [27:4] pane_decoder_1_pane_address_2;

  and and_1 (and_1_out, Write, CLK);
  Address_Translator address_translator_1 (
    .Address(Address), .Offset(16'h4000), .Limit(16'h200),
    .Translated_Address(address_translator_1_translated_address),
    .Active___1_means_address_in_range(address_translator_1_active___1_means_address_in_range));
  Pane_Decoder pane_decoder_1 (
    .Enable(address_translator_1_active___1_means_address_in_range),
    .Address(address_translator_1_translated_address), .Pane_Local_Address(Pane_Local_Address),
    .Pane_Address({pane_decoder_1_pane_address, pane_decoder_1_pane_address_2, pane_decoder_1_pane_address_3}),
    .Screen_Width(Screen_Width));
  Pane_Register pane_register_1 (
    .CLK(and_1_out), .Data(Data), .Reset(RESET), .Enable(pane_decoder_1_pane_address[0]),
    .Address(Pane_Local_Address), .out_6(out_7), .out_7(out_15), .out_8(out_23), .out_9(out_31),
    .out_10(out_39), .out_11(out_47), .out_12(out_55), .out_13(out_63), .out_14(out_71), .out_15(out_79),
    .out_16(out_87), .out_17(out_95), .out_18(out_103), .out_19(out_111), .out_20(out_119), .out_21(out_127));
  Pane_Register pane_register_2 (
    .CLK(and_1_out), .Data(Data), .Reset(RESET), .Enable(pane_decoder_1_pane_address[1]),
    .Address(Pane_Local_Address), .out_6(out_135), .out_7(out_143), .out_8(out_151), .out_9(out_159),
    .out_10(out_167), .out_11(out_175), .out_12(out_183), .out_13(out_191), .out_14(out_199),
    .out_15(out_207), .out_16(out_215), .out_17(out_223), .out_18(out_231), .out_19(out_239),
    .out_20(out_247), .out_21(out_255));
  Pane_Register pane_register_3 (
    .CLK(and_1_out), .Data(Data), .Reset(RESET), .Enable(pane_decoder_1_pane_address[2]),
    .Address(Pane_Local_Address), .out_6(out_263), .out_7(out_271), .out_8(out_279), .out_9(out_287),
    .out_10(out_295), .out_11(out_303), .out_12(out_311), .out_13(out_319), .out_14(out_327),
    .out_15(out_335), .out_16(out_343), .out_17(out_351), .out_18(out_359), .out_19(out_367),
    .out_20(out_375), .out_21(out_383));
  Pane_Register pane_register_4 (
    .CLK(and_1_out), .Data(Data), .Reset(RESET), .Enable(pane_decoder_1_pane_address[3]),
    .Address(Pane_Local_Address), .out_6(out_391), .out_7(out_399), .out_8(out_407), .out_9(out_415),
    .out_10(out_423), .out_11(out_431), .out_12(out_439), .out_13(out_447), .out_14(out_455),
    .out_15(out_463), .out_16(out_471), .out_17(out_479), .out_18(out_487), .out_19(out_495),
    .out_20(out_503), .out_21(out_511));
  Pane_Register pane_register_5 (
    .CLK(and_1_out), .Data(Data), .Reset(RESET), .Enable(pane_decoder_1_pane_address_2[24]),
    .Address(Pane_Local_Address), .out_6(out_8), .out_7(out_16), .out_8(out_24), .out_9(out_32),
    .out_10(out_40), .out_11(out_48), .out_12(out_56), .out_13(out_64), .out_14(out_72), .out_15(out_80),
    .out_16(out_88), .out_17(out_96), .out_18(out_104), .out_19(out_112), .out_20(out_120), .out_21(out_128));
  Pane_Register pane_register_6 (
    .CLK(and_1_out), .Data(Data), .Reset(RESET), .Enable(pane_decoder_1_pane_address_2[25]),
    .Address(Pane_Local_Address), .out_6(out_136), .out_7(out_144), .out_8(out_152), .out_9(out_160),
    .out_10(out_168), .out_11(out_176), .out_12(out_184), .out_13(out_192), .out_14(out_200),
    .out_15(out_208), .out_16(out_216), .out_17(out_224), .out_18(out_232), .out_19(out_240),
    .out_20(out_248), .out_21(out_256));
  Pane_Register pane_register_7 (
    .CLK(and_1_out), .Data(Data), .Reset(RESET), .Enable(pane_decoder_1_pane_address_2[26]),
    .Address(Pane_Local_Address), .out_6(out_264), .out_7(out_272), .out_8(out_280), .out_9(out_288),
    .out_10(out_296), .out_11(out_304), .out_12(out_312), .out_13(out_320), .out_14(out_328),
    .out_15(out_336), .out_16(out_344), .out_17(out_352), .out_18(out_360), .out_19(out_368),
    .out_20(out_376), .out_21(out_384));
  Pane_Register pane_register_8 (
    .CLK(and_1_out), .Data(Data), .Reset(RESET), .Enable(pane_decoder_1_pane_address_2[27]),
    .Address(Pane_Local_Address), .out_6(out_392), .out_7(out_400), .out_8(out_408), .out_9(out_416),
    .out_10(out_424), .out_11(out_432), .out_12(out_440), .out_13(out_448), .out_14(out_456),
    .out_15(out_464), .out_16(out_472), .out_17(out_480), .out_18(out_488), .out_19(out_496),
    .out_20(out_504), .out_21(out_512));
  Pane_Register pane_register_9 (
    .CLK(and_1_out), .Data(Data), .Reset(RESET), .Enable(pane_decoder_1_pane_address_2[20]),
    .Address(Pane_Local_Address), .out_6(out_9), .out_7(out_17), .out_8(out_25), .out_9(out_33),
    .out_10(out_41), .out_11(out_49), .out_12(out_57), .out_13(out_65), .out_14(out_73), .out_15(out_81),
    .out_16(out_89), .out_17(out_97), .out_18(out_105), .out_19(out_113), .out_20(out_121), .out_21(out_129));
  Pane_Register pane_register_10 (
    .CLK(and_1_out), .Data(Data), .Reset(RESET), .Enable(pane_decoder_1_pane_address_2[21]),
    .Address(Pane_Local_Address), .out_6(out_137), .out_7(out_145), .out_8(out_153), .out_9(out_161),
    .out_10(out_169), .out_11(out_177), .out_12(out_185), .out_13(out_193), .out_14(out_201),
    .out_15(out_209), .out_16(out_217), .out_17(out_225), .out_18(out_233), .out_19(out_241),
    .out_20(out_249), .out_21(out_257));
  Pane_Register pane_register_11 (
    .CLK(and_1_out), .Data(Data), .Reset(RESET), .Enable(pane_decoder_1_pane_address_2[22]),
    .Address(Pane_Local_Address), .out_6(out_265), .out_7(out_273), .out_8(out_281), .out_9(out_289),
    .out_10(out_297), .out_11(out_305), .out_12(out_313), .out_13(out_321), .out_14(out_329),
    .out_15(out_337), .out_16(out_345), .out_17(out_353), .out_18(out_361), .out_19(out_369),
    .out_20(out_377), .out_21(out_385));
  Pane_Register pane_register_12 (
    .CLK(and_1_out), .Data(Data), .Reset(RESET), .Enable(pane_decoder_1_pane_address_2[23]),
    .Address(Pane_Local_Address), .out_6(out_393), .out_7(out_401), .out_8(out_409), .out_9(out_417),
    .out_10(out_425), .out_11(out_433), .out_12(out_441), .out_13(out_449), .out_14(out_457),
    .out_15(out_465), .out_16(out_473), .out_17(out_481), .out_18(out_489), .out_19(out_497),
    .out_20(out_505), .out_21(out_513));
  Pane_Register pane_register_13 (
    .CLK(and_1_out), .Data(Data), .Reset(RESET), .Enable(pane_decoder_1_pane_address_2[16]),
    .Address(Pane_Local_Address), .out_6(out_10), .out_7(out_18), .out_8(out_26), .out_9(out_34),
    .out_10(out_42), .out_11(out_50), .out_12(out_58), .out_13(out_66), .out_14(out_74), .out_15(out_82),
    .out_16(out_90), .out_17(out_98), .out_18(out_106), .out_19(out_114), .out_20(out_122), .out_21(out_130));
  Pane_Register pane_register_14 (
    .CLK(and_1_out), .Data(Data), .Reset(RESET), .Enable(pane_decoder_1_pane_address_2[17]),
    .Address(Pane_Local_Address), .out_6(out_138), .out_7(out_146), .out_8(out_154), .out_9(out_162),
    .out_10(out_170), .out_11(out_178), .out_12(out_186), .out_13(out_194), .out_14(out_202),
    .out_15(out_210), .out_16(out_218), .out_17(out_226), .out_18(out_234), .out_19(out_242),
    .out_20(out_250), .out_21(out_258));
  Pane_Register pane_register_15 (
    .CLK(and_1_out), .Data(Data), .Reset(RESET), .Enable(pane_decoder_1_pane_address_2[18]),
    .Address(Pane_Local_Address), .out_6(out_266), .out_7(out_274), .out_8(out_282), .out_9(out_290),
    .out_10(out_298), .out_11(out_306), .out_12(out_314), .out_13(out_322), .out_14(out_330),
    .out_15(out_338), .out_16(out_346), .out_17(out_354), .out_18(out_362), .out_19(out_370),
    .out_20(out_378), .out_21(out_386));
  Pane_Register pane_register_16 (
    .CLK(and_1_out), .Data(Data), .Reset(RESET), .Enable(pane_decoder_1_pane_address_2[19]),
    .Address(Pane_Local_Address), .out_6(out_394), .out_7(out_402), .out_8(out_410), .out_9(out_418),
    .out_10(out_426), .out_11(out_434), .out_12(out_442), .out_13(out_450), .out_14(out_458),
    .out_15(out_466), .out_16(out_474), .out_17(out_482), .out_18(out_490), .out_19(out_498),
    .out_20(out_506), .out_21(out_514));
  Pane_Register pane_register_17 (
    .CLK(and_1_out), .Data(Data), .Reset(RESET), .Enable(pane_decoder_1_pane_address_2[12]),
    .Address(Pane_Local_Address), .out_6(out_11), .out_7(out_19), .out_8(out_27), .out_9(out_35),
    .out_10(out_43), .out_11(out_51), .out_12(out_59), .out_13(out_67), .out_14(out_75), .out_15(out_83),
    .out_16(out_91), .out_17(out_99), .out_18(out_107), .out_19(out_115), .out_20(out_123), .out_21(out_131));
  Pane_Register pane_register_18 (
    .CLK(and_1_out), .Data(Data), .Reset(RESET), .Enable(pane_decoder_1_pane_address_2[13]),
    .Address(Pane_Local_Address), .out_6(out_139), .out_7(out_147), .out_8(out_155), .out_9(out_163),
    .out_10(out_171), .out_11(out_179), .out_12(out_187), .out_13(out_195), .out_14(out_203),
    .out_15(out_211), .out_16(out_219), .out_17(out_227), .out_18(out_235), .out_19(out_243),
    .out_20(out_251), .out_21(out_259));
  Pane_Register pane_register_19 (
    .CLK(and_1_out), .Data(Data), .Reset(RESET), .Enable(pane_decoder_1_pane_address_2[14]),
    .Address(Pane_Local_Address), .out_6(out_267), .out_7(out_275), .out_8(out_283), .out_9(out_291),
    .out_10(out_299), .out_11(out_307), .out_12(out_315), .out_13(out_323), .out_14(out_331),
    .out_15(out_339), .out_16(out_347), .out_17(out_355), .out_18(out_363), .out_19(out_371),
    .out_20(out_379), .out_21(out_387));
  Pane_Register pane_register_20 (
    .CLK(and_1_out), .Data(Data), .Reset(RESET), .Enable(pane_decoder_1_pane_address_2[15]),
    .Address(Pane_Local_Address), .out_6(out_395), .out_7(out_403), .out_8(out_411), .out_9(out_419),
    .out_10(out_427), .out_11(out_435), .out_12(out_443), .out_13(out_451), .out_14(out_459),
    .out_15(out_467), .out_16(out_475), .out_17(out_483), .out_18(out_491), .out_19(out_499),
    .out_20(out_507), .out_21(out_515));
  Pane_Register pane_register_21 (
    .CLK(and_1_out), .Data(Data), .Reset(RESET), .Enable(pane_decoder_1_pane_address_2[8]),
    .Address(Pane_Local_Address), .out_6(out_12), .out_7(out_20), .out_8(out_28), .out_9(out_36),
    .out_10(out_44), .out_11(out_52), .out_12(out_60), .out_13(out_68), .out_14(out_76), .out_15(out_84),
    .out_16(out_92), .out_17(out_100), .out_18(out_108), .out_19(out_116), .out_20(out_124), .out_21(out_132));
  Pane_Register pane_register_22 (
    .CLK(and_1_out), .Data(Data), .Reset(RESET), .Enable(pane_decoder_1_pane_address_2[9]),
    .Address(Pane_Local_Address), .out_6(out_140), .out_7(out_148), .out_8(out_156), .out_9(out_164),
    .out_10(out_172), .out_11(out_180), .out_12(out_188), .out_13(out_196), .out_14(out_204),
    .out_15(out_212), .out_16(out_220), .out_17(out_228), .out_18(out_236), .out_19(out_244),
    .out_20(out_252), .out_21(out_260));
  Pane_Register pane_register_23 (
    .CLK(and_1_out), .Data(Data), .Reset(RESET), .Enable(pane_decoder_1_pane_address_2[10]),
    .Address(Pane_Local_Address), .out_6(out_268), .out_7(out_276), .out_8(out_284), .out_9(out_292),
    .out_10(out_300), .out_11(out_308), .out_12(out_316), .out_13(out_324), .out_14(out_332),
    .out_15(out_340), .out_16(out_348), .out_17(out_356), .out_18(out_364), .out_19(out_372),
    .out_20(out_380), .out_21(out_388));
  Pane_Register pane_register_24 (
    .CLK(and_1_out), .Data(Data), .Reset(RESET), .Enable(pane_decoder_1_pane_address_2[11]),
    .Address(Pane_Local_Address), .out_6(out_396), .out_7(out_404), .out_8(out_412), .out_9(out_420),
    .out_10(out_428), .out_11(out_436), .out_12(out_444), .out_13(out_452), .out_14(out_460),
    .out_15(out_468), .out_16(out_476), .out_17(out_484), .out_18(out_492), .out_19(out_500),
    .out_20(out_508), .out_21(out_516));
  Pane_Register pane_register_25 (
    .CLK(and_1_out), .Data(Data), .Reset(RESET), .Enable(pane_decoder_1_pane_address_2[4]),
    .Address(Pane_Local_Address), .out_6(out_13), .out_7(out_21), .out_8(out_29), .out_9(out_37),
    .out_10(out_45), .out_11(out_53), .out_12(out_61), .out_13(out_69), .out_14(out_77), .out_15(out_85),
    .out_16(out_93), .out_17(out_101), .out_18(out_109), .out_19(out_117), .out_20(out_125), .out_21(out_133));
  Pane_Register pane_register_26 (
    .CLK(and_1_out), .Data(Data), .Reset(RESET), .Enable(pane_decoder_1_pane_address_2[5]),
    .Address(Pane_Local_Address), .out_6(out_141), .out_7(out_149), .out_8(out_157), .out_9(out_165),
    .out_10(out_173), .out_11(out_181), .out_12(out_189), .out_13(out_197), .out_14(out_205),
    .out_15(out_213), .out_16(out_221), .out_17(out_229), .out_18(out_237), .out_19(out_245),
    .out_20(out_253), .out_21(out_261));
  Pane_Register pane_register_27 (
    .CLK(and_1_out), .Data(Data), .Reset(RESET), .Enable(pane_decoder_1_pane_address_2[6]),
    .Address(Pane_Local_Address), .out_6(out_269), .out_7(out_277), .out_8(out_285), .out_9(out_293),
    .out_10(out_301), .out_11(out_309), .out_12(out_317), .out_13(out_325), .out_14(out_333),
    .out_15(out_341), .out_16(out_349), .out_17(out_357), .out_18(out_365), .out_19(out_373),
    .out_20(out_381), .out_21(out_389));
  Pane_Register pane_register_28 (
    .CLK(and_1_out), .Data(Data), .Reset(RESET), .Enable(pane_decoder_1_pane_address_2[7]),
    .Address(Pane_Local_Address), .out_6(out_397), .out_7(out_405), .out_8(out_413), .out_9(out_421),
    .out_10(out_429), .out_11(out_437), .out_12(out_445), .out_13(out_453), .out_14(out_461),
    .out_15(out_469), .out_16(out_477), .out_17(out_485), .out_18(out_493), .out_19(out_501),
    .out_20(out_509), .out_21(out_517));
  Pane_Register pane_register_29 (
    .CLK(and_1_out), .Data(Data), .Reset(RESET), .Enable(pane_decoder_1_pane_address_3[0]),
    .Address(Pane_Local_Address), .out_6(out_14), .out_7(out_22), .out_8(out_30), .out_9(out_38),
    .out_10(out_46), .out_11(out_54), .out_12(out_62), .out_13(out_70), .out_14(out_78), .out_15(out_86),
    .out_16(out_94), .out_17(out_102), .out_18(out_110), .out_19(out_118), .out_20(out_126), .out_21(out_134));
  Pane_Register pane_register_30 (
    .CLK(and_1_out), .Data(Data), .Reset(RESET), .Enable(pane_decoder_1_pane_address_3[1]),
    .Address(Pane_Local_Address), .out_6(out_142), .out_7(out_150), .out_8(out_158), .out_9(out_166),
    .out_10(out_174), .out_11(out_182), .out_12(out_190), .out_13(out_198), .out_14(out_206),
    .out_15(out_214), .out_16(out_222), .out_17(out_230), .out_18(out_238), .out_19(out_246),
    .out_20(out_254), .out_21(out_262));
  Pane_Register pane_register_31 (
    .CLK(and_1_out), .Data(Data), .Reset(RESET), .Enable(pane_decoder_1_pane_address_3[2]),
    .Address(Pane_Local_Address), .out_6(out_270), .out_7(out_278), .out_8(out_286), .out_9(out_294),
    .out_10(out_302), .out_11(out_310), .out_12(out_318), .out_13(out_326), .out_14(out_334),
    .out_15(out_342), .out_16(out_350), .out_17(out_358), .out_18(out_366), .out_19(out_374),
    .out_20(out_382), .out_21(out_390));
  Pane_Register pane_register_32 (
    .CLK(and_1_out), .Data(Data), .Reset(RESET), .Enable(pane_decoder_1_pane_address_3[3]),
    .Address(Pane_Local_Address), .out_6(out_398), .out_7(out_406), .out_8(out_414), .out_9(out_422),
    .out_10(out_430), .out_11(out_438), .out_12(out_446), .out_13(out_454), .out_14(out_462),
    .out_15(out_470), .out_16(out_478), .out_17(out_486), .out_18(out_494), .out_19(out_502),
    .out_20(out_510), .out_21(out_518));

  // Notes on the sheet:
  //   Screen Offset
  //   Replicate a segment of RAM (Address + Data + Write + Offset) into a bunch of LED matrix
  //   Each LED matrix is 16x16, the display is a matrix of 8x4 LED matrix
  //   The subcircuit layout is designed to fit nicely into 16x16 LED matrix layout using rows input
  //   Screen Size
  //   Each output pin is 16 bits
  //   There are 512 output pins
endmodule
